// Logisim project fourbits_lookahead.circ as structural Verilog: 2 circuits, main circuit fourbits_carrylookahead
module fourbits_carrylookahead (
  input  Cin,
  input  [3:0] X,
  input  [3:0] Y,
  output S4,
  output S3,
  output S2,
  output S1,
  output Cout
);

  wire and_1_out, and_2_out, and_3_out, and_4_out, and_5_out, and_6_out, and_7_out, and_8_out, and_9_out,
       and_10_out, C1_out, C2_out, C3_out;
  wire [3:0] G_out, P_out;

  and and_1 (and_1_out, P_out[3], G_out[2]);
  or C4 (Cout, G_out[3], and_1_out, and_2_out, and_3_out, and_4_out);
  and and_2 (and_2_out, P_out[3], P_out[2], G_out[1]);
  and and_3 (and_3_out, P_out[3], P_out[2], P_out[1], G_out[0]);
  and and_4 (and_4_out, P_out[3], P_out[2], P_out[1], P_out[0], Cin);
  and and_5 (and_5_out, P_out[2], G_out[1]);
  assign G_out = X & Y;  // AND_Gate G, 4 bits wide
  xor u_S4 (S4, P_out[3], C3_out);
  or C3 (C3_out, G_out[2], and_5_out, and_6_out, and_7_out);
  and and_6 (and_6_out, P_out[2], P_out[1], G_out[0]);
  and and_7 (and_7_out, P_out[2], P_out[1], P_out[0], Cin);
  xor u_S3 (S3, P_out[2], C2_out);
  or C2 (C2_out, G_out[1], and_8_out, and_9_out);
  and and_8 (and_8_out, P_out[1], G_out[0]);
  assign P_out = X ^ Y;  // XOR_Gate P, 4 bits wide
  xor u_S2 (S2, P_out[1], C1_out);
  or C1 (C1_out, G_out[0], and_10_out);
  and and_9 (and_9_out, P_out[1], P_out[0], Cin);
  and and_10 (and_10_out, P_out[0], Cin);
  xor u_S1 (S1, P_out[0], Cin);
endmodule

module test (
  input  [3:0] in_1,
  input  [3:0] in_2
);

  fourbits_carrylookahead fourbits_carrylookahead_1 (.X(in_1), .Y(in_2));  // open: Cin, Cout, S4, S3, S2, S1
endmodule
