// Logisim project CS1409_U201414808_王林_MIPS.circ as structural Verilog: 15 circuits, main circuit main
module main (
  input  in_1
);

  wire and_3_out, and_4_out, BEQ, BNQ, CLK, clock_1_out, comparator_1_eq, EQUAL, i_type_1_ir_type, J_COUNT1,
       J_COUNT2, JAL, JL, Memory1, Memory2, not_1_out, not_2_out, or_1_out, or_2_out, or_3_out,
       r_slra_1_r_slra, register_2_q, SYS_B, SYSCALL, WE, xor_1_out;
  wire [3:0] register_3_q_2, register_3_q_3, register_3_q_4, register_3_q_5, translate_1_alu_op4;
  wire [4:0] multiplexer_1_out, multiplexer_2_out, rom_1_data;
  wire [11:0] counter_1_q, counter_2_q, counter_3_q, counter_4_q;
  wire [25:0] shifter_1_out;
  wire [31:0] a0, adder_1_out, adder_2_out, adder_3_out, adder_4_out, alu_1_result, and_1_out,
       bit_extender_1_out, bit_extender_2_out, bit_extender_3_out, JR_REG, main_1_ra_value, main_1_reg2_2,
       main_1_s0_value, main_1_s1_value, main_1_s2_value, multiplexer_3_out, multiplexer_4_out,
       multiplexer_5_out, multiplexer_6_out, multiplexer_7_out, multiplexer_8_out, multiplexer_9_out,
       multiplexer_10_out, multiplexer_11_out, PC, ram_1_data, register_3_q, rom_1_data_2, shifter_2_out, v0;

  assign CLK = not_1_out ? clock_1_out : 1'bz;  // Controlled_Buffer controlled_buffer_1
  Register #(.width(32)) register_1 (.D(multiplexer_10_out), .Q(PC), .clk(CLK), .clr(in_1));  // open: en
  not not_1 (not_1_out, register_2_q);
  Register #(.width(1)) register_2 (.D(SYS_B), .Q(register_2_q), .clk(clock_1_out));  // open: en, clr
  Adder #(.width(32)) adder_1 (.a(32'h4), .b(PC), .out(adder_1_out));  // open: cin, cout
  ROM #(.addrWidth(10), .dataWidth(32)) rom_1 (
    .addr(PC[11:2]), .data({rom_1_data_2[31:21], rom_1_data, rom_1_data_2[15:0]}));  // open: sel
  Register #(.width(32)) register_3 (
    .D(a0), .en(SYSCALL),
    .Q({register_3_q[31:24], register_3_q_5, register_3_q_4, register_3_q[15:12], register_3_q_3, register_3_q_2, register_3_q[3:0]}),
    .clk(CLK));  // open: clr
  assign and_1_out = 32'hf0000000 & adder_1_out;  // AND_Gate and_1, 32 bits wide
  Hex_Digit_Display hex_digit_display_1 (.value(register_3_q[31:28]));  // open: dp
  Shifter #(.width(26)) shifter_1 (
    .in({rom_1_data_2[25:21], rom_1_data, rom_1_data_2[15:0]}), .\dist (5'b00010), .out(shifter_1_out));
  Comparator #(.width(32)) comparator_1 (.a(v0), .b(32'ha), .eq(comparator_1_eq));  // open: gt, lt
  Hex_Digit_Display hex_digit_display_2 (.value(register_3_q[27:24]));  // open: dp
  assign bit_extender_1_out = {{6{1'b0}}, shifter_1_out};  // Bit_Extender bit_extender_1
  assign bit_extender_2_out = {{27{1'b0}}, rom_1_data_2[10:6]};  // Bit_Extender bit_extender_2
  assign bit_extender_3_out = {{16{rom_1_data_2[15]}}, rom_1_data_2[15:0]};  // Bit_Extender bit_extender_3
  I_TYPE i_type_1 (.op1(rom_1_data_2[31:26]), .IR_type(i_type_1_ir_type));
  LW lw_1 (.op1(rom_1_data_2[31:26]), .LW(Memory2));
  SW sw_1 (.op1(rom_1_data_2[31:26]), .SW(Memory1));
  BEQ beq_1 (.op1(rom_1_data_2[31:26]), .BEQ(BEQ));
  BNE bne_1 (.op1(rom_1_data_2[31:26]), .BEQ(BNQ));
  JL jl_1 (.op(rom_1_data_2[31:26]), .JL(JL));
  JR jr_1 (.op(rom_1_data_2[31:26]), .func(rom_1_data_2[5:0]), .JR(J_COUNT2));
  JAL jal_1 (.op(rom_1_data_2[31:26]), .JAL(JAL));
  Syscall_b syscall_b_1 (
    .op1(rom_1_data_2[31]), .op2(rom_1_data_2[30]), .op3(rom_1_data_2[29]), .op4(rom_1_data_2[28]),
    .op5(rom_1_data_2[27]), .op6(rom_1_data_2[26]), .func1(rom_1_data_2[5]), .func2(rom_1_data_2[4]),
    .func3(rom_1_data_2[3]), .func4(rom_1_data_2[2]), .func5(rom_1_data_2[1]), .func6(rom_1_data_2[0]),
    .syscall(SYSCALL));
  Hex_Digit_Display hex_digit_display_3 (.value(register_3_q_5));  // open: dp
  // Probe on bit_extender_2_out
  R_SLRA r_slra_1 (.op(rom_1_data_2[31:26]), .func(rom_1_data_2[5:0]), .r_slra(r_slra_1_r_slra));
  WE we_1 (.sw(Memory1), .beq(BEQ), .bne(BNQ), .jl(JL), .jr(J_COUNT2), .we(WE));
  buf and_2 (SYS_B, comparator_1_eq);  // AND_Gate
  Hex_Digit_Display hex_digit_display_4 (.value(register_3_q_4));  // open: dp
  Adder #(.width(32)) adder_2 (.a(and_1_out), .b(bit_extender_1_out), .out(adder_2_out));  // open: cin, cout
  // Probe on multiplexer_2_out
  Multiplexer #(.width(5), .enable("false")) multiplexer_1 (
    .in0(rom_1_data_2[15:11]), .in1(rom_1_data), .out(multiplexer_1_out), .sel(i_type_1_ir_type));
  Clock clock_1 (.out(clock_1_out));
  Hex_Digit_Display hex_digit_display_5 (.value(register_3_q_3));  // open: dp
  Hex_Digit_Display hex_digit_display_6 (.value(register_3_q[15:12]));  // open: dp
  // Probe on rom_1_data
  Hex_Digit_Display hex_digit_display_7 (.value(register_3_q_2));  // open: dp
  // Probe on rom_1_data_2[25:21]
  Multiplexer #(.width(5), .enable("false")) multiplexer_2 (
    .in0(multiplexer_1_out), .in1({5{1'b1}}), .out(multiplexer_2_out), .sel(JAL));
  Hex_Digit_Display hex_digit_display_8 (.value(register_3_q[3:0]));  // open: dp
  // Probe on main_1_s1_value
  // Probe on main_1_s0_value
  // Probe on multiplexer_11_out
  translate translate_1 (
    .op1(rom_1_data_2[31]), .op2(rom_1_data_2[30]), .op3(rom_1_data_2[29]), .op4(rom_1_data_2[28]),
    .op5(rom_1_data_2[27]), .op6(rom_1_data_2[26]), .func1(rom_1_data_2[5]), .func2(rom_1_data_2[4]),
    .func3(rom_1_data_2[3]), .func4(rom_1_data_2[2]), .func5(rom_1_data_2[1]), .func6(rom_1_data_2[0]),
    .alu_op1(translate_1_alu_op4[3]), .alu_op2(translate_1_alu_op4[2]), .alu_op3(translate_1_alu_op4[1]),
    .alu_op4(translate_1_alu_op4[0]));
  // Probe on v0
  \CS1409_U201414808_王林_regfile_main  main_1 (
    .Reg1_num(rom_1_data_2[25:21]), .Reg2(rom_1_data), .Write_Reg_num(multiplexer_2_out),
    .Din(multiplexer_11_out), .Write_Enable(WE), .Clock(CLK), .Reg1(JR_REG), .Reg2_2(main_1_reg2_2),
    .s0_Value(main_1_s0_value), .s1_Value(main_1_s1_value), .s2_Value(main_1_s2_value),
    .ra_Value(main_1_ra_value), .v0(v0), .a0(a0));
  // Probe on main_1_s2_value
  // Probe on main_1_ra_value
  Multiplexer #(.width(32), .enable("false")) multiplexer_3 (
    .in0(JR_REG), .in1(main_1_reg2_2), .out(multiplexer_3_out), .sel(r_slra_1_r_slra));
  // Probe on translate_1_alu_op4
  Counter #(.width(12), .max('hfff)) counter_1 (
    .load(1'b0), .D(12'h1), .Q(counter_1_q), .clk(CLK));  // open: count, carry, clr
  Multiplexer #(.width(32), .enable("false")) multiplexer_4 (
    .in0(main_1_reg2_2), .in1(bit_extender_2_out), .out(multiplexer_4_out), .sel(r_slra_1_r_slra));
  // Probe on counter_1_q
  Shifter #(.width(32)) shifter_2 (.in(bit_extender_3_out), .\dist (5'b00010), .out(shifter_2_out));
  // Probe on multiplexer_3_out
  // Probe on multiplexer_5_out
  Multiplexer #(.width(32), .enable("false")) multiplexer_5 (
    .in0(multiplexer_4_out), .in1(bit_extender_3_out), .out(multiplexer_5_out), .sel(xor_1_out));
  xor xor_1 (xor_1_out, i_type_1_ir_type, BEQ, BNQ);
  or or_1 (or_1_out, BEQ, BNQ);
  Adder #(.width(32)) adder_3 (.a(adder_1_out), .b(shifter_2_out), .out(adder_3_out));  // open: cin, cout
  ALU alu_1 (
    .AluOP(translate_1_alu_op4), .X(multiplexer_3_out), .Equal(EQUAL), .Result(alu_1_result),
    .Y(multiplexer_5_out));  // open: Signed_Overflow, Result_2, UnSigned_Overflow
  Counter #(.width(12), .max('hfff)) counter_2 (
    .load(1'b0), .D(12'h1), .count(or_1_out), .Q(counter_2_q), .clk(CLK));  // open: carry, clr
  // Probe on counter_2_q
  or or_2 (or_2_out, Memory1, Memory2);
  and and_3 (and_3_out, BEQ, EQUAL);
  Counter #(.width(12), .max('hfff)) counter_3 (
    .load(1'b0), .D(12'h1), .count(or_2_out), .Q(counter_3_q), .clk(CLK));  // open: carry, clr
  Multiplexer #(.width(32), .enable("false")) multiplexer_6 (
    .in0(adder_1_out), .in1(adder_3_out), .out(multiplexer_6_out), .sel(and_3_out));
  // Probe on counter_3_q
  Multiplexer #(.width(32), .enable("false")) multiplexer_7 (
    .in0(multiplexer_6_out), .in1(adder_3_out), .out(multiplexer_7_out), .sel(and_4_out));
  and and_4 (and_4_out, not_2_out, BNQ);
  not not_2 (not_2_out, EQUAL);
  RAM #(.addrWidth(10), .dataWidth(32), .bus("separate")) ram_1 (
    .addr(alu_1_result[11:2]), .din(main_1_reg2_2), .data(ram_1_data), .str(Memory1), .clk(CLK), .ld(Memory2));  // open: sel, clr
  or or_3 (or_3_out, J_COUNT1, J_COUNT2);
  Multiplexer #(.width(32), .enable("false")) multiplexer_8 (
    .in0(alu_1_result), .in1(ram_1_data), .out(multiplexer_8_out), .sel(Memory2));
  Counter #(.width(12), .max('hfff)) counter_4 (
    .load(1'b0), .D(12'h1), .Q(counter_4_q), .clk(or_3_out));  // open: count, carry, clr
  // Probe on counter_4_q
  Multiplexer #(.width(32), .enable("false")) multiplexer_9 (
    .in0(multiplexer_7_out), .in1(adder_2_out), .out(multiplexer_9_out), .sel(J_COUNT1));
  or or_4 (J_COUNT1, JL, JAL);
  // Probe on JR_REG
  Adder #(.width(32)) adder_4 (.a(32'h4), .b(PC), .out(adder_4_out));  // open: cin, cout
  Multiplexer #(.width(32), .enable("false")) multiplexer_10 (
    .in0(multiplexer_9_out), .in1(JR_REG), .out(multiplexer_10_out), .sel(J_COUNT2));
  Multiplexer #(.width(32), .enable("false")) multiplexer_11 (
    .in0(multiplexer_8_out), .in1(adder_4_out), .out(multiplexer_11_out), .sel(JAL));

  // Other names for the same wires on the sheet: JR = J_COUNT2; J_count3 = BEQ; J_count4 = BNQ

  // Notes on the sheet:
  //   contents of rom_1 (hex, n*v repeats v):
  //   20110001 8000c05 20110001 20120002 20130003 8000c09 20110001 20120002 20130003 8000c0d 20110001
  //   20120002 20130003 8000c11 20110001 20120002 20130003 c000cb8 20100001 20110001 118fc0 112020
  //   20020022 c 118882 12200001 8000c15 112020 20020022 c 20110001 118880 112020 20020022 c 12200001
  //   8000c1f 20110001 118fc0 112020 20020022 c 1188c3 112020 20020022 c 118903 112020 20020022 c 118903
  //   112020 20020022 c 118903 112020 20020022 c 118903 112020 20020022 c 118903 112020 20020022 c 118903
  //   112020 20020022 c 118903 112020 20020022 c 20100001 109fc0 139fc3 8021 2012000c 24160003 26100001
  //   3210000f 20080008 20090001 139900 2709825 132020 20020022 c 1094022 1500fff9 22100001 2018000f
  //   2188024 108700 20080008 20090001 139902 2709825 132021 20020022 c 1094022 1500fff9 108702 2c9b022
  //   12c00001 8000c50 4020 1084027 84400 3508ffff 82021 20020022 c 2010ffff 20110000 ae300000 22100001
  //   22310004 ae300000 22100001 22310004 ae300000 22100001 22310004 ae300000 22100001 22310004 ae300000
  //   22100001 22310004 ae300000 22100001 22310004 ae300000 22100001 22310004 ae300000 22100001 22310004
  //   ae300000 22100001 22310004 ae300000 22100001 22310004 ae300000 22100001 22310004 ae300000 22100001
  //   22310004 ae300000 22100001 22310004 ae300000 22100001 22310004 ae300000 22100001 22310004 ae300000
  //   22100001 22310004 22100001 8020 2011003c 8e130000 8e340000 274402a 11000002 ae330000 ae140000
  //   2231fffc 1611fff8 102020 20020022 c 22100004 2011003c 1611fff2 2002000a c 20100000 22100001 102020
  //   20020022 c 22100002 102020 20020022 c 22100003 102020 20020022 c 22100004 102020 20020022 c 22100005
  //   102020 20020022 c 22100006 102020 20020022 c 22100007 102020 20020022 c 22100008 102020 20020022
  //   20020022 c 3e00008
endmodule

// ALU_CONTROL
module translate (
  input  op1,
  input  op2,
  input  op3,
  input  op4,
  input  op5,
  input  op6,
  input  func1,
  input  func2,
  input  func3,
  input  func4,
  input  func5,
  input  func6,
  output alu_op1,
  output alu_op2,
  output alu_op3,
  output alu_op4
);

  wire and_1_out, and_2_out, and_3_out, and_4_out, and_5_out, and_6_out, and_7_out, and_8_out, and_9_out,
       and_10_out, and_11_out, and_12_out, and_13_out, and_14_out, and_15_out, and_16_out, and_17_out,
       and_18_out, and_19_out, and_20_out, and_21_out, and_22_out, and_23_out, and_24_out, and_25_out,
       and_26_out, and_27_out, and_28_out, and_29_out, and_30_out, and_31_out, and_32_out, and_33_out,
       and_34_out, and_35_out, and_36_out, and_37_out, and_38_out, and_39_out, and_40_out, and_41_out,
       and_42_out, and_43_out, not_1_out, not_2_out, not_3_out, not_4_out, not_5_out, not_6_out, not_7_out,
       not_8_out, not_9_out, not_10_out, not_11_out, not_12_out, not_13_out, not_14_out, not_15_out,
       not_16_out, not_17_out, not_18_out, not_19_out, not_20_out, not_21_out, not_22_out, not_23_out,
       not_24_out, not_25_out, not_26_out, not_27_out, not_28_out, not_29_out, not_30_out, not_31_out,
       not_32_out, not_33_out, not_34_out, not_35_out, not_36_out, not_37_out, not_38_out, not_39_out,
       not_40_out, not_41_out, not_42_out, not_43_out, not_44_out, not_45_out, not_46_out, not_47_out,
       not_48_out, not_49_out, not_50_out, not_51_out, not_52_out, not_53_out, not_54_out, not_55_out,
       not_56_out, not_57_out, not_58_out, not_59_out, not_60_out, not_61_out, not_62_out, not_63_out,
       not_64_out, not_65_out, not_66_out, not_67_out, not_68_out, not_69_out, not_70_out, not_71_out,
       not_72_out, not_73_out, not_74_out, not_75_out, not_76_out, not_77_out, not_78_out, not_79_out,
       not_80_out, not_81_out, not_82_out, not_83_out, not_84_out, not_85_out, not_86_out, not_87_out,
       not_88_out, not_89_out, not_90_out, not_91_out, not_92_out, not_93_out, not_94_out, not_95_out,
       not_96_out, not_97_out, not_98_out, not_99_out, not_100_out, not_101_out, not_102_out, not_103_out,
       not_104_out, not_105_out, not_106_out, not_107_out, not_108_out, not_109_out, not_110_out,
       not_111_out, not_112_out, not_113_out, not_114_out, not_115_out, not_116_out, not_117_out,
       not_118_out, not_119_out, not_120_out, not_121_out, not_122_out, not_123_out, not_124_out,
       not_125_out, not_126_out, not_127_out, not_128_out, not_129_out, not_130_out, not_131_out,
       not_132_out, not_133_out, not_134_out, not_135_out, not_136_out, not_137_out, not_138_out,
       not_139_out, not_140_out, not_141_out, not_142_out, not_143_out, not_144_out, or_1_out, or_2_out,
       or_3_out, or_4_out, or_5_out, or_6_out;

  not not_1 (not_1_out, func3);
  not not_2 (not_2_out, func5);
  not not_3 (not_3_out, func3);
  not not_4 (not_4_out, func6);
  not not_5 (not_5_out, func3);
  not not_6 (not_6_out, func4);
  not not_7 (not_7_out, func6);
  not not_8 (not_8_out, func4);
  not not_9 (not_9_out, func3);
  not not_10 (not_10_out, func4);
  not not_11 (not_11_out, func5);
  not not_12 (not_12_out, func6);
  not not_13 (not_13_out, func3);
  not not_14 (not_14_out, func4);
  not not_15 (not_15_out, func5);
  not not_16 (not_16_out, func3);
  not not_17 (not_17_out, func4);
  not not_18 (not_18_out, func6);
  not not_19 (not_19_out, func3);
  not not_20 (not_20_out, func4);
  not not_21 (not_21_out, func3);
  not not_22 (not_22_out, func5);
  not not_23 (not_23_out, func6);
  not not_24 (not_24_out, func4);
  not not_25 (not_25_out, func3);
  not not_26 (not_26_out, func4);
  not not_27 (not_27_out, func6);
  not not_28 (not_28_out, func3);
  not not_29 (not_29_out, func4);
  not not_30 (not_30_out, func3);
  not not_31 (not_31_out, func3);
  not not_32 (not_32_out, func5);
  not not_33 (not_33_out, func6);
  not not_34 (not_34_out, func4);
  not not_35 (not_35_out, func6);
  not not_36 (not_36_out, func3);
  not not_37 (not_37_out, func4);
  not not_38 (not_38_out, func6);
  not not_39 (not_39_out, func3);
  not not_40 (not_40_out, func6);
  not not_41 (not_41_out, func3);
  not not_42 (not_42_out, func4);
  not not_43 (not_43_out, func5);
  not not_44 (not_44_out, func6);
  not not_45 (not_45_out, func3);
  not not_46 (not_46_out, func4);
  not not_47 (not_47_out, func5);
  not not_48 (not_48_out, func3);
  not not_49 (not_49_out, func5);
  not not_50 (not_50_out, func6);
  not not_51 (not_51_out, func3);
  not not_52 (not_52_out, func6);
  not not_53 (not_53_out, func4);
  not not_54 (not_54_out, func6);
  not not_55 (not_55_out, func3);
  not not_56 (not_56_out, func4);
  not not_57 (not_57_out, func3);
  and and_1 (and_1_out, not_1_out, func4, not_2_out, func6);
  and and_2 (and_2_out, not_3_out, func4, func5, not_4_out);
  and and_3 (and_3_out, not_5_out, func4, func5, func6);
  and and_4 (and_4_out, func3, not_6_out, func5, not_7_out);
  and and_5 (and_5_out, func3, not_8_out, func5, func6);
  and and_6 (and_6_out, not_9_out, not_10_out, not_11_out, not_12_out);
  and and_7 (and_7_out, not_13_out, not_14_out, not_15_out, func6);
  and and_8 (and_8_out, not_16_out, not_17_out, func5, not_18_out);
  and and_9 (and_9_out, not_19_out, not_20_out, func5, func6);
  and and_10 (and_10_out, not_21_out, func4, not_22_out, not_23_out);
  and and_11 (and_11_out, func3, not_24_out, func5, func6);
  and and_12 (and_12_out, not_25_out, not_26_out, func5, not_27_out);
  and and_13 (and_13_out, not_28_out, not_29_out, func5, func6);
  and and_14 (and_14_out, not_30_out, func4, func5, func6);
  and and_15 (and_15_out, not_31_out, func4, not_32_out, not_33_out);
  and and_16 (and_16_out, func3, not_34_out, func5, not_35_out);
  and and_17 (and_17_out, not_36_out, not_37_out, func5, not_38_out);
  and and_18 (and_18_out, not_39_out, func4, func5, not_40_out);
  and and_19 (and_19_out, not_41_out, not_42_out, not_43_out, not_44_out);
  and and_20 (and_20_out, not_45_out, not_46_out, not_47_out, func6);
  and and_21 (and_21_out, not_48_out, func4, not_49_out, not_50_out);
  and and_22 (and_22_out, not_51_out, func4, func5, not_52_out);
  and and_23 (and_23_out, func3, not_53_out, func5, not_54_out);
  and and_24 (and_24_out, not_55_out, not_56_out, func5, func6);
  and and_25 (and_25_out, not_57_out, func4, func5, func6);
  not not_58 (not_58_out, op1);
  not not_59 (not_59_out, op2);
  not not_60 (not_60_out, op3);
  not not_61 (not_61_out, op4);
  not not_62 (not_62_out, op5);
  not not_63 (not_63_out, op6);
  not not_64 (not_64_out, func2);
  or or_1 (or_1_out, and_1_out, and_2_out, and_3_out, and_4_out, and_5_out);
  not not_65 (not_65_out, op1);
  not not_66 (not_66_out, op2);
  not not_67 (not_67_out, op5);
  not not_68 (not_68_out, op1);
  not not_69 (not_69_out, op2);
  not not_70 (not_70_out, op6);
  not not_71 (not_71_out, op1);
  not not_72 (not_72_out, op2);
  not not_73 (not_73_out, op3);
  not not_74 (not_74_out, op4);
  not not_75 (not_75_out, op5);
  not not_76 (not_76_out, op6);
  not not_77 (not_77_out, func2);
  or or_2 (or_2_out, and_6_out, and_7_out, and_8_out, and_9_out, and_10_out, and_11_out);
  not not_78 (not_78_out, op1);
  not not_79 (not_79_out, op2);
  not not_80 (not_80_out, op4);
  not not_81 (not_81_out, op5);
  not not_82 (not_82_out, op6);
  not not_83 (not_83_out, op1);
  not not_84 (not_84_out, op2);
  not not_85 (not_85_out, op4);
  not not_86 (not_86_out, op5);
  not not_87 (not_87_out, op1);
  not not_88 (not_88_out, op2);
  not not_89 (not_89_out, op5);
  not not_90 (not_90_out, op6);
  not not_91 (not_91_out, op2);
  not not_92 (not_92_out, op4);
  not not_93 (not_93_out, op1);
  not not_94 (not_94_out, op2);
  not not_95 (not_95_out, op3);
  not not_96 (not_96_out, op4);
  not not_97 (not_97_out, op5);
  not not_98 (not_98_out, op6);
  not not_99 (not_99_out, func2);
  or or_3 (or_3_out, and_12_out, and_13_out, and_14_out, and_15_out, and_16_out);
  not not_100 (not_100_out, op1);
  not not_101 (not_101_out, op2);
  not not_102 (not_102_out, op3);
  not not_103 (not_103_out, op4);
  not not_104 (not_104_out, op5);
  not not_105 (not_105_out, op6);
  not not_106 (not_106_out, func1);
  not not_107 (not_107_out, func2);
  or or_4 (or_4_out, and_17_out, and_18_out);
  not not_108 (not_108_out, op1);
  not not_109 (not_109_out, op2);
  not not_110 (not_110_out, op5);
  not not_111 (not_111_out, op6);
  not not_112 (not_112_out, op1);
  not not_113 (not_113_out, op2);
  not not_114 (not_114_out, op3);
  not not_115 (not_115_out, op4);
  not not_116 (not_116_out, op5);
  not not_117 (not_117_out, op6);
  not not_118 (not_118_out, func2);
  or or_5 (or_5_out, and_19_out, and_20_out, and_21_out, and_22_out, and_23_out);
  not not_119 (not_119_out, op1);
  not not_120 (not_120_out, op2);
  not not_121 (not_121_out, op3);
  not not_122 (not_122_out, op4);
  not not_123 (not_123_out, op5);
  not not_124 (not_124_out, op6);
  not not_125 (not_125_out, func1);
  not not_126 (not_126_out, func2);
  or or_6 (or_6_out, and_24_out, and_25_out);
  not not_127 (not_127_out, op1);
  not not_128 (not_128_out, op2);
  not not_129 (not_129_out, op4);
  not not_130 (not_130_out, op5);
  not not_131 (not_131_out, op6);
  not not_132 (not_132_out, op1);
  not not_133 (not_133_out, op2);
  not not_134 (not_134_out, op4);
  not not_135 (not_135_out, op5);
  not not_136 (not_136_out, op1);
  not not_137 (not_137_out, op2);
  not not_138 (not_138_out, op5);
  not not_139 (not_139_out, op6);
  not not_140 (not_140_out, op1);
  not not_141 (not_141_out, op2);
  not not_142 (not_142_out, op6);
  not not_143 (not_143_out, op2);
  not not_144 (not_144_out, op4);
  and and_26 (and_26_out, not_58_out, not_59_out, not_60_out, not_61_out, not_62_out, not_63_out, func1, not_64_out, or_1_out);
  and and_27 (and_27_out, not_65_out, not_66_out, op3, op4, not_67_out, op6);
  and and_28 (and_28_out, not_68_out, not_69_out, op3, op4, op5, not_70_out);
  and and_29 (and_29_out, not_71_out, not_72_out, not_73_out, not_74_out, not_75_out, not_76_out, func1, not_77_out, or_2_out);
  and and_30 (and_30_out, not_78_out, not_79_out, op3, not_80_out, not_81_out, not_82_out);
  and and_31 (and_31_out, not_83_out, not_84_out, op3, not_85_out, not_86_out, op6);
  and and_32 (and_32_out, not_87_out, not_88_out, op3, op4, not_89_out, not_90_out);
  and and_33 (and_33_out, op1, not_91_out, not_92_out, op5, op6);
  and and_34 (and_34_out, not_93_out, not_94_out, not_95_out, not_96_out, not_97_out, not_98_out, func1, not_99_out, or_3_out);
  and and_35 (and_35_out, not_100_out, not_101_out, not_102_out, not_103_out, not_104_out, not_105_out, not_106_out, not_107_out, or_4_out);
  and and_36 (and_36_out, not_108_out, not_109_out, op3, op4, not_110_out, not_111_out);
  and and_37 (and_37_out, not_112_out, not_113_out, not_114_out, not_115_out, not_116_out, not_117_out, func1, not_118_out, or_5_out);
  and and_38 (and_38_out, not_119_out, not_120_out, not_121_out, not_122_out, not_123_out, not_124_out, not_125_out, not_126_out, or_6_out);
  and and_39 (and_39_out, not_127_out, not_128_out, op3, not_129_out, not_130_out, not_131_out);
  and and_40 (and_40_out, not_132_out, not_133_out, op3, not_134_out, not_135_out, op6);
  and and_41 (and_41_out, not_136_out, not_137_out, op3, op4, not_138_out, not_139_out);
  and and_42 (and_42_out, not_140_out, not_141_out, op3, op4, op5, not_142_out);
  and and_43 (and_43_out, op1, not_143_out, not_144_out, op5, op6);
  or or_7 (alu_op1, and_26_out, and_27_out, and_28_out);
  or or_8 (alu_op2, and_29_out, and_30_out, and_31_out, and_32_out, and_33_out);
  or or_9 (alu_op3, and_34_out, and_35_out, and_36_out);
  or or_10 (alu_op4, and_37_out, and_38_out, and_39_out, and_40_out, and_41_out, and_42_out, and_43_out);
endmodule

module r_slra (
  input  [4:0] op1,
  output r1
);

  wire not_1_out, not_2_out, not_3_out, not_4_out, not_5_out;

  not not_1 (not_1_out, op1[0]);
  not not_2 (not_2_out, op1[1]);
  not not_3 (not_3_out, op1[2]);
  not not_4 (not_4_out, op1[3]);
  not not_5 (not_5_out, op1[4]);
  and and_1 (r1, not_1_out, not_2_out, not_3_out, not_4_out, not_5_out);
endmodule

module R_TYPE (
  input  [5:0] op1,
  output IR_type
);

  wire not_1_out, not_2_out, not_3_out, not_4_out, not_5_out, not_6_out;

  not not_1 (not_1_out, op1[0]);
  not not_2 (not_2_out, op1[1]);
  not not_3 (not_3_out, op1[2]);
  not not_4 (not_4_out, op1[3]);
  not not_5 (not_5_out, op1[4]);
  not not_6 (not_6_out, op1[5]);
  and and_1 (IR_type, not_1_out, not_2_out, not_3_out, not_4_out, not_5_out, not_6_out);
endmodule

// R/ITYPE
module I_TYPE (
  input  [5:0] op1,
  output IR_type
);

  or or_1 (IR_type, op1[5], op1[4], op1[3], op1[2], op1[1], op1[0]);
endmodule

module LW (
  input  [5:0] op1,
  output LW
);

  wire not_1_out, not_2_out, not_3_out;

  not not_1 (not_1_out, op1[4]);
  not not_2 (not_2_out, op1[3]);
  not not_3 (not_3_out, op1[2]);
  and and_1 (LW, op1[5], not_1_out, not_2_out, not_3_out, op1[1], op1[0]);
endmodule

module SW (
  input  [5:0] op1,
  output SW
);

  wire not_1_out, not_2_out;

  not not_1 (not_1_out, op1[4]);
  not not_2 (not_2_out, op1[2]);
  and and_1 (SW, op1[5], not_1_out, op1[3], not_2_out, op1[1], op1[0]);
endmodule

module BEQ (
  input  [5:0] op1,
  output BEQ
);

  wire not_1_out, not_2_out, not_3_out, not_4_out, not_5_out;

  not not_1 (not_1_out, op1[5]);
  not not_2 (not_2_out, op1[4]);
  not not_3 (not_3_out, op1[3]);
  not not_4 (not_4_out, op1[1]);
  not not_5 (not_5_out, op1[0]);
  and and_1 (BEQ, not_1_out, not_2_out, not_3_out, op1[2], not_4_out, not_5_out);
endmodule

module BNE (
  input  [5:0] op1,
  output BEQ
);

  wire not_1_out, not_2_out, not_3_out, not_4_out;

  not not_1 (not_1_out, op1[5]);
  not not_2 (not_2_out, op1[4]);
  not not_3 (not_3_out, op1[3]);
  not not_4 (not_4_out, op1[1]);
  and and_1 (BEQ, not_1_out, not_2_out, not_3_out, op1[2], not_4_out, op1[0]);
endmodule

module R_SLRA (
  input  [5:0] op,
  input  [5:0] func,
  output r_slra
);

  wire and_1_out, and_2_out, and_3_out, not_1_out, not_2_out, not_3_out, not_4_out, not_5_out, not_6_out,
       not_7_out, not_8_out, not_9_out, not_10_out, not_11_out, not_12_out, not_13_out, or_1_out;

  not not_1 (not_1_out, func[1]);
  not not_2 (not_2_out, func[0]);
  not not_3 (not_3_out, func[0]);
  and and_1 (and_1_out, not_1_out, not_2_out);
  and and_2 (and_2_out, func[1], not_3_out);
  and and_3 (and_3_out, func[1], func[0]);
  not not_4 (not_4_out, op[5]);
  not not_5 (not_5_out, op[4]);
  not not_6 (not_6_out, op[3]);
  not not_7 (not_7_out, op[2]);
  not not_8 (not_8_out, op[1]);
  not not_9 (not_9_out, op[0]);
  not not_10 (not_10_out, func[5]);
  not not_11 (not_11_out, func[4]);
  not not_12 (not_12_out, func[3]);
  not not_13 (not_13_out, func[2]);
  or or_1 (or_1_out, and_1_out, and_2_out, and_3_out);
  and and_4 (r_slra, not_4_out, not_5_out, not_6_out, not_7_out, not_8_out, not_9_out, not_10_out, not_11_out, not_12_out, not_13_out, or_1_out);
endmodule

module JL (
  input  [5:0] op,
  output JL
);

  wire not_1_out, not_2_out, not_3_out, not_4_out, not_5_out;

  not not_1 (not_1_out, op[5]);
  not not_2 (not_2_out, op[4]);
  not not_3 (not_3_out, op[3]);
  not not_4 (not_4_out, op[2]);
  not not_5 (not_5_out, op[0]);
  and and_1 (JL, not_1_out, not_2_out, not_3_out, not_4_out, op[1], not_5_out);
endmodule

module WE (
  input  sw,
  input  beq,
  input  bne,
  input  jl,
  input  jr,
  output we
);

  nor nor_1 (we, sw, beq, bne, jl, jr);
endmodule

// SYSCALL_BREAK
module Syscall_b (
  input  op1,
  input  op2,
  input  op3,
  input  op4,
  input  op5,
  input  op6,
  input  func1,
  input  func2,
  input  func3,
  input  func4,
  input  func5,
  input  func6,
  output syscall
);

  wire not_1_out, not_2_out, not_3_out, not_4_out, not_5_out, not_6_out, not_7_out, not_8_out, not_9_out,
       not_10_out;

  not not_1 (not_1_out, op1);
  not not_2 (not_2_out, op2);
  not not_3 (not_3_out, op3);
  not not_4 (not_4_out, op4);
  not not_5 (not_5_out, op5);
  not not_6 (not_6_out, op6);
  not not_7 (not_7_out, func1);
  not not_8 (not_8_out, func2);
  not not_9 (not_9_out, func5);
  not not_10 (not_10_out, func6);
  and and_1 (syscall, not_1_out, not_2_out, not_3_out, not_4_out, not_5_out, not_6_out, not_7_out, not_8_out, func3, func4, not_9_out, not_10_out);
endmodule

module JAL (
  input  [5:0] op,
  output JAL
);

  wire not_1_out, not_2_out, not_3_out, not_4_out;

  not not_1 (not_1_out, op[5]);
  not not_2 (not_2_out, op[4]);
  not not_3 (not_3_out, op[3]);
  not not_4 (not_4_out, op[2]);
  and and_1 (JAL, not_1_out, not_2_out, not_3_out, not_4_out, op[1], op[0]);
endmodule

module JR (
  input  [5:0] op,
  input  [5:0] func,
  output JR
);

  wire not_1_out, not_2_out, not_3_out, not_4_out, not_5_out, not_6_out, not_7_out, not_8_out, not_9_out,
       not_10_out, not_11_out;

  not not_1 (not_1_out, op[5]);
  not not_2 (not_2_out, op[4]);
  not not_3 (not_3_out, op[3]);
  not not_4 (not_4_out, op[2]);
  not not_5 (not_5_out, op[1]);
  not not_6 (not_6_out, op[0]);
  not not_7 (not_7_out, func[5]);
  not not_8 (not_8_out, func[4]);
  not not_9 (not_9_out, func[2]);
  not not_10 (not_10_out, func[1]);
  not not_11 (not_11_out, func[0]);
  and and_1 (JR, not_1_out, not_2_out, not_3_out, not_4_out, not_5_out, not_6_out, not_7_out, not_8_out, func[3], not_9_out, not_10_out, not_11_out);
endmodule
