// Logisim project CS1409_U201414808_王林_alu.circ as structural Verilog
module ALU (
  input  [31:0] X,
  input  [31:0] Y,
  input  [3:0] AluOP,
  output Signed_Overflow,
  output UnSigned_Overflow,
  output Equal,
  output [31:0] Result,
  output [31:0] Result_2
);

  // Probe on X
  // Probe on X
  // Probe on Y
  // Probe on Y
  my_alu my_alu_1 (
    .in_1(X), .in_2(Y), .UOF(UnSigned_Overflow), .out_5(Signed_Overflow), .out_6(Result_2), .out_7(Result),
    .out_8(Equal), .in_3(AluOP));
  // Probe on AluOP
  // Probe on Result
  // Probe on Result
  // Probe on Result_2

  // Other names for the same wires on the sheet: OF = Signed_Overflow; Result2[31:0] = Result_2; S[3:0] = AluOP;
  //   UOF = UnSigned_Overflow

  // Notes on the sheet:
  //   不要改变此引脚区域内容，也不要改变ALU封装形式
  //   输入引脚
  //   请在下方利用上方输入输出引脚的隧道信号构建ALU电路，ctrl+d复制选择部件
  //   华中科技大学计算机学院 计算机组成原理，鸣谢加州大学伯克利CS61C课程
  //   输出引脚
  //   探测区域
endmodule

module \演示电路  (
  input  [31:0] X,
  input  [31:0] Y,
  input  [3:0] ALUOP,
  output Signed_Overflow,
  output Unsigned_overflow,
  output [31:0] Result,
  output [31:0] Result_2,
  output Equal
);

  // Probe on X
  // Probe on X
  ALU alu_1 (
    .AluOP(ALUOP), .X(X), .Equal(Equal), .Result(Result), .Signed_Overflow(Signed_Overflow), .Y(Y),
    .Result_2(Result_2), .UnSigned_Overflow(Unsigned_overflow));
  // Probe on ALUOP
  // Probe on Y
  // Probe on Y
  // Probe on Result
  // Probe on Result
  // Probe on Result_2

  // Notes on the sheet:
  //   ALu电路无需调整位置即可连接在该电路中，并且不能出现蓝色线缆和三态输出
endmodule

module \等差数列  (
  input  [31:0] \数列初始值 ,
  input  [31:0] \等差值 ,
  input  \时钟 ,
  output [31:0] Result
);

  // Probe on \数列初始值 
  // Probe on \数列初始值 
  // Probe on \等差值 
  // Probe on \等差值 
  // Probe on Result
  // Probe on Result

  // Other names for the same wires on the sheet: 数列初值[31:0] = \数列初始值 ; 累加和[31:0] = Result

  // Notes on the sheet:
  //   不要改变此引脚区域内容，也不要改变ALU封装形式
  //   请在下方利用上方输入输出引脚的隧道信号构建等差数列求和电路，ctrl+d复制选择部件
  //   华中科技大学计算机学院 计算机组成原理，鸣谢加州大学伯克利CS61C课程
  //   输出引脚
  //   探测区域
endmodule

// CLA74181
module fourbits_ahead (
  input  C0,
  input  [3:0] X,
  input  [3:0] Y,
  output C4,
  output OF,
  output S4,
  output S3,
  output S2,
  output S1,
  output P4_star,
  output G4_star
);

  wire and_1_out, and_2_out, and_3_out, and_5_out, and_6_out, and_7_out, and_8_out, and_9_out, and_10_out,
       and_11_out, C1_out, C2_out, C3_out;
  wire [3:0] G_out, P_out;

  or u_C4 (C4, G4_star, and_5_out);
  or or_1 (G4_star, G_out[3], and_1_out, and_2_out, and_3_out);
  and and_1 (and_1_out, P_out[3], G_out[2]);
  and and_2 (and_2_out, P_out[3], P_out[2], G_out[1]);
  and and_3 (and_3_out, P_out[3], P_out[2], P_out[1], G_out[0]);
  assign G_out = X & Y;  // AND_Gate G, 4 bits wide
  xor xor_1 (OF, C4, C3_out);
  and and_4 (P4_star, P_out[3], P_out[2], P_out[1], P_out[0]);
  and and_5 (and_5_out, P4_star, C0);
  and and_6 (and_6_out, P_out[2], G_out[1]);
  xor xor_2 (S4, P_out[3], C3_out);
  or C3 (C3_out, G_out[2], and_6_out, and_7_out, and_8_out);
  and and_7 (and_7_out, P_out[2], P_out[1], G_out[0]);
  and and_8 (and_8_out, P_out[2], P_out[1], P_out[0], C0);
  xor xor_3 (S3, P_out[2], C2_out);
  or C2 (C2_out, G_out[1], and_9_out, and_10_out);
  and and_9 (and_9_out, P_out[1], G_out[0]);
  and and_10 (and_10_out, P_out[1], P_out[0], C0);
  assign P_out = X ^ Y;  // XOR_Gate P, 4 bits wide
  xor xor_4 (S2, P_out[1], C1_out);
  or C1 (C1_out, G_out[0], and_11_out);
  and and_11 (and_11_out, P_out[0], C0);
  xor xor_5 (S1, P_out[0], C0);
endmodule

// CAL74182
module CLA74182 (
  input  C0,
  input  [3:0] G,
  input  [3:0] P,
  output C3,
  output C2,
  output C1
);

  wire and_1_out, and_2_out, and_3_out, and_4_out, and_5_out, and_6_out, and_7_out, and_8_out, and_9_out,
       and_10_out, and_11_out, or_1_out, or_2_out;

  or or_1 (or_1_out, or_2_out, and_5_out);
  or or_2 (or_2_out, G[3], and_1_out, and_3_out, and_2_out);
  and and_1 (and_1_out, P[3], G[2]);
  and and_2 (and_2_out, P[3], P[2], P[1], G[0]);
  and and_3 (and_3_out, P[3], P[2], G[1]);
  and and_4 (and_4_out, P[3], P[2], P[1], P[0]);
  and and_5 (and_5_out, and_4_out, C0);
  and and_6 (and_6_out, P[2], G[1]);
  or or_3 (C3, G[2], and_6_out, and_7_out, and_8_out);
  and and_7 (and_7_out, P[2], P[1], G[0]);
  and and_8 (and_8_out, P[2], P[1], P[0], C0);
  or or_4 (C2, G[1], and_9_out, and_10_out);
  and and_9 (and_9_out, P[1], G[0]);
  and and_10 (and_10_out, P[1], P[0], C0);
  or or_5 (C1, G[0], and_11_out);
  and and_11 (and_11_out, P[0], C0);
endmodule

// ADD_32bits
module _32bits_ahead (
  input  [31:0] X,
  input  [31:0] Y,
  output [31:0] S,
  output out_4,
  output OF
);

  wire cla74182_1_c1, cla74182_1_c2, cla74182_1_c3, cla74182_2_c1, cla74182_2_c2, cla74182_2_c3,
       fourbits_ahead_5_c4;
  wire [3:0] fourbits_ahead_4_g4_star, fourbits_ahead_4_p4_star, fourbits_ahead_8_g4_star,
       fourbits_ahead_8_p4_star;

  fourbits_ahead fourbits_ahead_1 (
    .P4_star(fourbits_ahead_4_p4_star[3]), .G4_star(fourbits_ahead_4_g4_star[3]), .C0(cla74182_1_c3),
    .C4(out_4), .OF(OF), .S4(S[31]), .S3(S[30]), .S2(S[29]), .S1(S[28]), .X(X[31:28]), .Y(Y[31:28]));
  CLA74182 cla74182_1 (
    .C0(fourbits_ahead_5_c4), .C3(cla74182_1_c3), .C2(cla74182_1_c2), .C1(cla74182_1_c1),
    .G(fourbits_ahead_4_g4_star), .P(fourbits_ahead_4_p4_star));
  fourbits_ahead fourbits_ahead_2 (
    .P4_star(fourbits_ahead_4_p4_star[2]), .G4_star(fourbits_ahead_4_g4_star[2]), .C0(cla74182_1_c2),
    .S4(S[27]), .S3(S[26]), .S2(S[25]), .S1(S[24]), .X(X[27:24]), .Y(Y[27:24]));  // open: C4, OF
  fourbits_ahead fourbits_ahead_3 (
    .P4_star(fourbits_ahead_4_p4_star[1]), .G4_star(fourbits_ahead_4_g4_star[1]), .C0(cla74182_1_c1),
    .S4(S[23]), .S3(S[22]), .S2(S[21]), .S1(S[20]), .X(X[23:20]), .Y(Y[23:20]));  // open: C4, OF
  fourbits_ahead fourbits_ahead_4 (
    .P4_star(fourbits_ahead_4_p4_star[0]), .G4_star(fourbits_ahead_4_g4_star[0]), .C0(fourbits_ahead_5_c4),
    .S4(S[19]), .S3(S[18]), .S2(S[17]), .S1(S[16]), .X(X[19:16]), .Y(Y[19:16]));  // open: C4, OF
  fourbits_ahead fourbits_ahead_5 (
    .P4_star(fourbits_ahead_8_p4_star[3]), .G4_star(fourbits_ahead_8_g4_star[3]), .C0(cla74182_2_c3),
    .C4(fourbits_ahead_5_c4), .S4(S[15]), .S3(S[14]), .S2(S[13]), .S1(S[12]), .X(Y[15:12]), .Y(X[15:12]));  // open: OF
  CLA74182 cla74182_2 (
    .C0(1'b0), .C3(cla74182_2_c3), .C2(cla74182_2_c2), .C1(cla74182_2_c1), .G(fourbits_ahead_8_g4_star),
    .P(fourbits_ahead_8_p4_star));
  fourbits_ahead fourbits_ahead_6 (
    .P4_star(fourbits_ahead_8_p4_star[2]), .G4_star(fourbits_ahead_8_g4_star[2]), .C0(cla74182_2_c2),
    .S4(S[11]), .S3(S[10]), .S2(S[9]), .S1(S[8]), .X(Y[11:8]), .Y(X[11:8]));  // open: C4, OF
  fourbits_ahead fourbits_ahead_7 (
    .P4_star(fourbits_ahead_8_p4_star[1]), .G4_star(fourbits_ahead_8_g4_star[1]), .C0(cla74182_2_c1),
    .S4(S[7]), .S3(S[6]), .S2(S[5]), .S1(S[4]), .X(Y[7:4]), .Y(X[7:4]));  // open: C4, OF
  fourbits_ahead fourbits_ahead_8 (
    .P4_star(fourbits_ahead_8_p4_star[0]), .G4_star(fourbits_ahead_8_g4_star[0]), .C0(1'b0), .S4(S[3]),
    .S3(S[2]), .S2(S[1]), .S1(S[0]), .X(Y[3:0]), .Y(X[3:0]));  // open: C4, OF
endmodule

// SUB_32bits
module _32bits_sub (
  input  [31:0] X,
  input  [31:0] in_2,
  output UOF,
  output OF,
  output [31:0] S
);

  wire n32bits_ahead_2_out_4;
  wire [31:0] bit_extender_1_out, n32bits_ahead_1_s, xor_1_out;

  assign bit_extender_1_out = {{31{1'b1}}, 1'b1};  // Bit_Extender bit_extender_1
  assign xor_1_out = in_2 ^ bit_extender_1_out;  // XOR_Gate xor_1, 32 bits wide
  _32bits_ahead u_32bits_ahead_1 (.S(n32bits_ahead_1_s), .X(xor_1_out), .Y(32'h1));  // open: out_4, OF
  xor xor_2 (UOF, 1'b1, n32bits_ahead_2_out_4);
  _32bits_ahead u_32bits_ahead_2 (.out_4(n32bits_ahead_2_out_4), .OF(OF), .S(S), .X(X), .Y(n32bits_ahead_1_s));
endmodule

module my_alu (
  input  [31:0] in_1,
  input  [31:0] in_2,
  input  [3:0] in_3,
  output UOF,
  output out_5,
  output [31:0] out_6,
  output [31:0] out_7,
  output out_8
);

  wire comparator_1_lt, comparator_2_lt, n32bits_ahead_1_of, n32bits_ahead_1_out_4, n32bits_sub_1_of,
       n32bits_sub_1_uof;
  wire [4:0] bitselector_1_out;
  wire [31:0] and_1_out, bit_extender_1_out, bit_extender_2_out, divider_1_out, divider_1_rem,
       multiplier_1_cout, multiplier_1_out, n32bits_ahead_1_s, n32bits_sub_1_s, or_1_out, shifter_1_out,
       shifter_2_out, shifter_3_out, xor_1_out, xor_2_out;

  BitSelector #(.width(32), .group(5)) bitselector_1 (.in(in_2), .out(bitselector_1_out), .sel(3'b000));
  Shifter #(.width(32)) shifter_1 (.in(in_1), .\dist (bitselector_1_out), .out(shifter_1_out));
  Shifter #(.width(32), .shift("ar")) shifter_2 (.in(in_1), .\dist (bitselector_1_out), .out(shifter_2_out));
  Shifter #(.width(32), .shift("lr")) shifter_3 (.in(in_1), .\dist (bitselector_1_out), .out(shifter_3_out));
  Multiplier #(.width(32)) multiplier_1 (
    .a(in_1), .b(in_2), .out(multiplier_1_out), .cin({32{1'b0}}), .cout(multiplier_1_cout));
  Divider #(.width(32)) divider_1 (.a(in_1), .b(in_2), .out(divider_1_out), .upper({32{1'b0}}), .rem(divider_1_rem));
  Comparator #(.width(32)) comparator_1 (.a(in_1), .b(in_2), .lt(comparator_1_lt));  // open: gt, eq
  Comparator #(.width(32), .mode("unsigned")) comparator_2 (.a(in_1), .b(in_2), .lt(comparator_2_lt));  // open: gt, eq
  assign and_1_out = in_1 & in_2;  // AND_Gate and_1, 32 bits wide
  assign or_1_out = in_1 | in_2;  // OR_Gate or_1, 32 bits wide
  assign xor_1_out = in_1 ^ in_2;  // XOR_Gate xor_1, 32 bits wide
  assign bit_extender_1_out = {{31{1'b0}}, comparator_1_lt};  // Bit_Extender bit_extender_1
  assign bit_extender_2_out = {{31{1'b0}}, comparator_2_lt};  // Bit_Extender bit_extender_2
  assign xor_2_out = or_1_out ^ {32{1'b1}};  // XOR_Gate xor_2, 32 bits wide
  _32bits_ahead u_32bits_ahead_1 (
    .out_4(n32bits_ahead_1_out_4), .OF(n32bits_ahead_1_of), .S(n32bits_ahead_1_s), .X(in_1), .Y(in_2));
  _32bits_sub u_32bits_sub_1 (
    .X(in_1), .in_2(in_2), .UOF(n32bits_sub_1_uof), .OF(n32bits_sub_1_of), .S(n32bits_sub_1_s));
  Multiplexer #(.select(4), .enable("false")) multiplexer_1 (
    .in0(1'b0), .in1(1'b0), .in2(1'b0), .in3(1'b0), .in4(1'b0), .in5(n32bits_ahead_1_of),
    .in6(n32bits_sub_1_of), .in7(1'b0), .in8(1'b0), .in9(1'b0), .in10(1'b0), .in11(1'b0), .in12(1'b0),
    .in13(1'b0), .in14(1'b0), .in15(1'b0), .out(out_5), .sel(in_3));
  Comparator #(.width(32), .mode("unsigned")) comparator_3 (
    .a(n32bits_sub_1_s), .b({32{1'b0}}), .eq(out_8));  // open: gt, lt
  Multiplexer #(.select(4), .enable("false")) multiplexer_2 (
    .in0(1'b0), .in1(1'b0), .in2(1'b0), .in3(1'b0), .in4(1'b0), .in5(n32bits_ahead_1_out_4),
    .in6(n32bits_sub_1_uof), .in7(1'b0), .in8(1'b0), .in9(1'b0), .in10(1'b0), .in11(1'b0), .in12(1'b0),
    .in13(1'b0), .in14(1'b0), .in15(1'b0), .out(UOF), .sel(in_3));
  Multiplexer #(.select(4), .width(32), .enable("false")) multiplexer_3 (
    .in0(shifter_1_out), .in1(shifter_2_out), .in2(shifter_3_out), .in3(multiplier_1_out),
    .in4(divider_1_out), .in5(n32bits_ahead_1_s), .in6(n32bits_sub_1_s), .in7(and_1_out), .in8(or_1_out),
    .in9(xor_1_out), .in10(xor_2_out), .in11(bit_extender_1_out), .in12(bit_extender_2_out),
    .in13({32{1'b0}}), .in14({32{1'b0}}), .in15({32{1'b0}}), .out(out_7), .sel(in_3));
  Multiplexer #(.select(4), .width(32), .enable("false")) multiplexer_4 (
    .in0({32{1'b0}}), .in1({32{1'b0}}), .in2({32{1'b0}}), .in3(multiplier_1_cout), .in4(divider_1_rem),
    .in5({32{1'b0}}), .in6({32{1'b0}}), .in7({32{1'b0}}), .in8({32{1'b0}}), .in9({32{1'b0}}),
    .in10({32{1'b0}}), .in11({32{1'b0}}), .in12({32{1'b0}}), .in13({32{1'b0}}), .in14({32{1'b0}}),
    .in15({32{1'b0}}), .out(out_6), .sel(in_3));
endmodule
