// Logisim project CS1409_U201414808_王林_自动累加器.circ as structural Verilog: 2 circuits, main circuit Counter_auto
module Counter_auto (
  input  in_1,
  input  in_2,
  input  in_3
);

  wire and_1_out, clock_1_out, comparator_1_lt, comparator_2_gt, comparator_3_eq, comparator_3_lt,
       comparator_4_eq, comparator_4_gt, comparator_5_lt, comparator_6_gt, comparator_7_gt, comparator_8_lt,
       controlled_buffer_8_out, controlled_inverter_1_out;
  wire [4:0] controlled_buffer_9_out, counter_3_q, counter_4_q;
  wire [5:0] counter_1_q, counter_2_q;
  wire [31:0] alu_1_result, controlled_buffer_1_out, controlled_buffer_2_out, controlled_buffer_3_out,
       controlled_buffer_7_out, R_out, register_1_q, X, Y;

  Counter #(.width(6), .max('h3f), .ongoal("stay")) counter_1 (
    .D({6{1'b0}}), .Q(counter_1_q), .clk(and_1_out), .clr(in_2));  // open: load, count, carry
  // Probe on X
  // Probe on Y
  Comparator #(.width(6), .mode("unsigned")) comparator_1 (
    .a(counter_1_q), .b({6{1'b1}}), .lt(comparator_1_lt));  // open: gt, eq
  Comparator #(.width(6), .mode("unsigned")) comparator_2 (
    .a(counter_1_q), .b(6'b011111), .gt(comparator_2_gt));  // open: eq, lt
  and and_1 (and_1_out, comparator_1_lt, clock_1_out);
  Clock clock_1 (.out(clock_1_out));
  assign controlled_buffer_1_out = comparator_2_gt ? R_out : 32'bz;  // Controlled_Buffer controlled_buffer_1
  assign controlled_inverter_1_out = in_3 ? ~comparator_2_gt : 1'bz;  // Controlled_Inverter controlled_inverter_1
  // Probe on R_out
  RAM #(.addrWidth(6), .dataWidth(32)) ram_1 (
    .addr(counter_1_q), .data(controlled_buffer_1_out), .clk(and_1_out), .ld(controlled_inverter_1_out));  // open: sel, clr
  Counter #(.width(6), .max('h3f)) counter_2 (
    .D({6{1'b0}}), .Q(counter_2_q), .clk(and_1_out), .clr(in_2));  // open: load, count, carry
  Hex_Digit_Display hex_digit_display_1 (.value(R_out[31:28]));  // open: dp
  Hex_Digit_Display hex_digit_display_2 (.value(R_out[27:24]));  // open: dp
  assign controlled_buffer_2_out = comparator_3_lt ? controlled_buffer_1_out : 32'bz;  // Controlled_Buffer controlled_buffer_2
  Comparator #(.width(6), .mode("unsigned")) comparator_3 (
    .a({6{1'b0}}), .b(counter_2_q), .eq(comparator_3_eq), .lt(comparator_3_lt));  // open: gt
  Comparator #(.width(6), .mode("unsigned")) comparator_4 (
    .a(counter_2_q), .b(6'b000001), .gt(comparator_4_gt), .eq(comparator_4_eq));  // open: lt
  Comparator #(.width(6), .mode("unsigned")) comparator_5 (
    .a(counter_2_q), .b(6'b100000), .lt(comparator_5_lt));  // open: gt, eq
  Comparator #(.width(6), .mode("unsigned")) comparator_6 (
    .a(counter_2_q), .b({6{1'b0}}), .gt(comparator_6_gt));  // open: eq, lt
  Comparator #(.width(6), .mode("unsigned")) comparator_7 (
    .a(counter_2_q), .b(6'b011111), .gt(comparator_7_gt));  // open: eq, lt
  Comparator #(.width(6), .mode("unsigned")) comparator_8 (
    .a(counter_2_q), .b(6'b100000), .lt(comparator_8_lt));  // open: gt, eq
  Hex_Digit_Display hex_digit_display_3 (.value(R_out[23:20]));  // open: dp
  assign controlled_buffer_3_out = comparator_3_eq ? controlled_buffer_1_out : 32'bz;  // Controlled_Buffer controlled_buffer_3
  Hex_Digit_Display hex_digit_display_4 (.value(R_out[19:16]));  // open: dp
  Register #(.width(32)) register_1 (.D(controlled_buffer_3_out), .Q(register_1_q), .clk(and_1_out));  // open: en, clr
  Hex_Digit_Display hex_digit_display_5 (.value(R_out[15:12]));  // open: dp
  Hex_Digit_Display hex_digit_display_6 (.value(R_out[11:8]));  // open: dp
  assign X = comparator_5_lt ? controlled_buffer_2_out : 32'bz;  // Controlled_Buffer controlled_buffer_4
  assign Y = comparator_4_eq ? register_1_q : 32'bz;  // Controlled_Buffer controlled_buffer_5
  Hex_Digit_Display hex_digit_display_7 (.value(R_out[7:4]));  // open: dp
  assign Y = comparator_4_gt ? R_out : 32'bz;  // Controlled_Buffer controlled_buffer_6
  Hex_Digit_Display hex_digit_display_8 (.value(R_out[3:0]));  // open: dp
  ALU alu_1 (
    .AluOP(4'b0101), .X(X), .Result(alu_1_result), .Y(Y));  // open: Equal, Signed_Overflow, Result_2, UnSigned_Overflow
  assign controlled_buffer_7_out = comparator_5_lt ? alu_1_result : 32'bz;  // Controlled_Buffer controlled_buffer_7
  // Probe on alu_1_result
  Counter #(.width(5), .max('h1f)) counter_3 (
    .D(5'b00001), .Q(counter_3_q), .clk(and_1_out), .clr(in_1));  // open: load, count, carry
  Counter #(.width(5), .max('h1f)) counter_4 (
    .D({5{1'b0}}), .Q(counter_4_q), .clk(controlled_buffer_8_out), .clr(in_1));  // open: load, count, carry
  assign controlled_buffer_8_out = comparator_6_gt ? and_1_out : 1'bz;  // Controlled_Buffer controlled_buffer_8
  MIPS_regs mips_regs_1 (
    .WE(comparator_5_lt), .R1(controlled_buffer_9_out), .Din(controlled_buffer_7_out), .Clk(and_1_out),
    .W_num(counter_3_q), .R1_out(R_out));  // open: R2_out, s0, s1, s2, ra, R2, v0, a0
  assign controlled_buffer_9_out = comparator_8_lt ? counter_4_q : 5'bz;  // Controlled_Buffer controlled_buffer_9
  assign controlled_buffer_9_out = comparator_7_gt ? counter_3_q : 5'bz;  // Controlled_Buffer controlled_buffer_10
  // Probe on R_out
endmodule

module test (
);

  RAM #(.addrWidth(6)) ram_1 ();  // open: addr, data, sel, clk, ld, clr
endmodule
