// Logisim project 中断_MIPS.circ as structural Verilog: 25 circuits, main circuit main
module main (
  input  in_1
);

  wire _1_out, _2_out, _3_out, and_3_out, and_4_out, and_5_out, and_6_out, BEQ, BLEZ, blezr, BNQ, CLK,
       clock_1_out, comparator_1_eq, EQUAL, ERET, EXP, hasexp, i_type_1_ir_type, J_COUNT1, J_COUNT2, JAL, JL,
       LBU, LUI, Memory1, Memory2, MFC0, MTC0, not_1_out, or_1_out, or_2_out, or_3_out, or_5_out,
       r_slra_1_r_slra, register_2_q, SYS_B, SYSCALL, WE, xor_1_out, zero_extend_1_zero_ext;
  wire [3:0] translate_1_alu_op4;
  wire [4:0] multiplexer_5_out, multiplexer_7_out, rd, rt;
  wire [7:0] _1, _2, _3, _4, multiplexer_17_out;
  wire [9:0] demultiplexer_1_out0, demultiplexer_1_out1;
  wire [11:0] counter_1_q, counter_2_q, counter_3_q, counter_4_q;
  wire [25:0] shifter_1_out;
  wire [31:0] a0, adder_1_out, adder_2_out, adder_3_out, adder_4_out, adder_5_out, and_1_out,
       bit_extender_1_out, bit_extender_2_out, bit_extender_3_out, bit_extender_4_out, bit_extender_5_out,
       CP0OUT, EPC, immediate, JR_REG, main_1_ra_value, main_1_reg2_2, main_1_s0_value, main_1_s1_value,
       main_1_s2_value, multiplexer_1_out, multiplexer_2_out, multiplexer_4_out, multiplexer_8_out,
       multiplexer_9_out, multiplexer_10_out, multiplexer_11_out, multiplexer_12_out, multiplexer_13_out,
       multiplexer_14_out, multiplexer_15_out, multiplexer_16_out, multiplexer_18_out, multiplexer_19_out,
       multiplexer_20_out, multiplexer_21_out, multiplexer_22_out, PC, register_3_q, rom_1_data, rom_2_data,
       shifter_2_out, shifter_3_out, shifter_4_out, v0;
  wire [31:1] alu_1_result;

  Multiplexer #(.width(32), .enable("false")) multiplexer_1 (
    .in0(multiplexer_19_out), .in1(EPC), .out(multiplexer_1_out), .sel(ERET));
  // Probe on multiplexer_2_out
  Multiplexer #(.width(32), .enable("false")) multiplexer_2 (
    .in0(multiplexer_1_out), .in1(32'h80000000), .out(multiplexer_2_out), .sel(hasexp));
  Register #(.width(32)) register_1 (.D(multiplexer_2_out), .Q(PC), .clk(CLK), .clr(in_1));  // open: en
  Demultiplexer #(.width(10), .enable("false")) demultiplexer_1 (
    .out0(demultiplexer_1_out0), .out1(demultiplexer_1_out1), .in(PC[11:2]), .sel(PC[31]));
  // Probe on PC
  Multiplexer #(.enable("false")) multiplexer_3 (.in0(clock_1_out), .in1(1'b1), .out(CLK), .sel(register_2_q));
  Clock clock_1 (.out(clock_1_out));
  Register #(.width(1), .trigger("falling")) register_2 (.D(1'b1), .Q(register_2_q), .clk(SYS_B));  // open: en, clr
  Adder #(.width(32)) adder_1 (.a(32'h4), .b(PC), .out(adder_1_out));  // open: cin, cout
  ROM #(.addrWidth(10), .dataWidth(32)) rom_1 (.addr(demultiplexer_1_out0), .data(rom_1_data));  // open: sel
  Multiplexer #(.width(32), .enable("false")) multiplexer_4 (
    .in0(rom_1_data), .in1(rom_2_data), .out({multiplexer_4_out[31:21], rt, rd, multiplexer_4_out[10:0]}),
    .sel(PC[31]));
  ROM #(.addrWidth(10), .dataWidth(32)) rom_2 (.addr(demultiplexer_1_out1), .data(rom_2_data));  // open: sel
  LUI lui_1 (.op1(multiplexer_4_out[31:26]), .LUI(LUI));
  LBU lbu_1 (.op1(multiplexer_4_out[31:26]), .LUI(LBU));
  BLEZ blez_1 (.op1(multiplexer_4_out[31:26]), .BLEZ(BLEZ));
  INTRUPT intrupt_1 (.op1(multiplexer_4_out[31:26]), .INTRRUPT(EXP));
  mfc0 mfc0_1 (.op1(multiplexer_4_out[31:26]), .mfc0in(multiplexer_4_out[25:21]), .MFC0(MFC0));
  mtc0 mtc0_1 (.op1(multiplexer_4_out[31:26]), .mfc0in(multiplexer_4_out[25:21]), .MFC0(MTC0));
  eret eret_1 (.op1(multiplexer_4_out[31:26]), .eretin(multiplexer_4_out[5:0]), .ERET(ERET));
  assign and_1_out = 32'hf0000000 & adder_1_out;  // AND_Gate and_1, 32 bits wide
  Shifter #(.width(26)) shifter_1 (
    .in({multiplexer_4_out[25:21], rt, rd, multiplexer_4_out[10:0]}), .\dist (5'b00010), .out(shifter_1_out));
  assign bit_extender_1_out = {{6{1'b0}}, shifter_1_out};  // Bit_Extender bit_extender_1
  assign bit_extender_2_out = {{27{1'b0}}, multiplexer_4_out[10:6]};  // Bit_Extender bit_extender_2
  R_SLRA r_slra_1 (.op(multiplexer_4_out[31:26]), .func(multiplexer_4_out[5:0]), .r_slra(r_slra_1_r_slra));
  zero_extend zero_extend_1 (.op1(multiplexer_4_out[31:26]), .zero_ext(zero_extend_1_zero_ext));
  I_TYPE i_type_1 (.op1(multiplexer_4_out[31:26]), .IR_type(i_type_1_ir_type));
  LW lw_1 (.op1(multiplexer_4_out[31:26]), .LW(Memory2));
  SW sw_1 (.op1(multiplexer_4_out[31:26]), .SW(Memory1));
  BEQ beq_1 (.op1(multiplexer_4_out[31:26]), .BEQ(BEQ));
  BNE bne_1 (.op1(multiplexer_4_out[31:26]), .BEQ(BNQ));
  JL jl_1 (.op(multiplexer_4_out[31:26]), .JL(JL));
  JR jr_1 (.op(multiplexer_4_out[31:26]), .func(multiplexer_4_out[5:0]), .JR(J_COUNT2));
  JAL jal_1 (.op(multiplexer_4_out[31:26]), .JAL(JAL));
  Syscall_b syscall_b_1 (
    .op1(multiplexer_4_out[31]), .op2(multiplexer_4_out[30]), .op3(multiplexer_4_out[29]),
    .op4(multiplexer_4_out[28]), .op5(multiplexer_4_out[27]), .op6(multiplexer_4_out[26]),
    .func1(multiplexer_4_out[5]), .func2(multiplexer_4_out[4]), .func3(multiplexer_4_out[3]),
    .func4(multiplexer_4_out[2]), .func5(multiplexer_4_out[1]), .func6(multiplexer_4_out[0]),
    .syscall(SYSCALL));
  Comparator #(.width(32)) comparator_1 (.a(v0), .b(32'ha), .eq(comparator_1_eq));  // open: gt, lt
  // Probe on bit_extender_2_out
  assign bit_extender_3_out = {{16{rd[4]}}, {rd, multiplexer_4_out[10:0]}};  // Bit_Extender bit_extender_3
  assign bit_extender_4_out = {{16{1'b0}}, {rd, multiplexer_4_out[10:0]}};  // Bit_Extender bit_extender_4
  WE we_1 (.sw(Memory1), .beq(BEQ), .bne(BNQ), .jl(JL), .jr(J_COUNT2), .blez(BLEZ), .we(WE));
  buf and_2 (SYS_B, comparator_1_eq);  // AND_Gate
  Adder #(.width(32)) adder_2 (.a(and_1_out), .b(bit_extender_1_out), .out(adder_2_out));  // open: cin, cout
  // Probe on multiplexer_7_out
  Multiplexer #(.width(5), .enable("false")) multiplexer_5 (
    .in0(rd), .in1(rt), .out(multiplexer_5_out), .sel(i_type_1_ir_type));
  Multiplexer #(.width(32), .enable("false")) multiplexer_6 (
    .in0(bit_extender_3_out), .in1(bit_extender_4_out), .out(immediate), .sel(zero_extend_1_zero_ext));
  // Probe on rt
  // Probe on multiplexer_4_out[25:21]
  Multiplexer #(.width(5), .enable("false")) multiplexer_7 (
    .in0(multiplexer_5_out), .in1({5{1'b1}}), .out(multiplexer_7_out), .sel(JAL));
  Button u__2 (.out(_2_out));
  Button u__3 (.out(_3_out));
  // Probe on main_1_s1_value
  // Probe on main_1_s0_value
  // Probe on multiplexer_22_out
  translate translate_1 (
    .op1(multiplexer_4_out[31]), .op2(multiplexer_4_out[30]), .op3(multiplexer_4_out[29]),
    .op4(multiplexer_4_out[28]), .op5(multiplexer_4_out[27]), .op6(multiplexer_4_out[26]),
    .func1(multiplexer_4_out[5]), .func2(multiplexer_4_out[4]), .func3(multiplexer_4_out[3]),
    .func4(multiplexer_4_out[2]), .func5(multiplexer_4_out[1]), .func6(multiplexer_4_out[0]),
    .alu_op1(translate_1_alu_op4[3]), .alu_op2(translate_1_alu_op4[2]), .alu_op3(translate_1_alu_op4[1]),
    .alu_op4(translate_1_alu_op4[0]));
  Button u__1 (.out(_1_out));
  // Probe on v0
  \CS1409_U201414808_王林_regfile_main  main_1 (
    .Reg1_num(multiplexer_4_out[25:21]), .Reg2(rt), .Write_Reg_num(multiplexer_7_out),
    .Din(multiplexer_22_out), .Write_Enable(and_3_out), .Clock(CLK), .Reg1(JR_REG), .Reg2_2(main_1_reg2_2),
    .s0_Value(main_1_s0_value), .s1_Value(main_1_s1_value), .s2_Value(main_1_s2_value),
    .ra_Value(main_1_ra_value), .v0(v0), .a0(a0));
  and and_3 (and_3_out, WE, ~MTC0);  // AND_Gate
  // Probe on main_1_s2_value
  // Probe on main_1_ra_value
  Multiplexer #(.width(32), .enable("false")) multiplexer_8 (
    .in0(JR_REG), .in1(main_1_reg2_2), .out(multiplexer_8_out), .sel(r_slra_1_r_slra));
  // Probe on main_1_reg2_2
  // Probe on translate_1_alu_op4
  // Probe on PC
  CP0 cp0_1 (
    .c1(rd), .c2(rd), .PCin(PC), .cp0we(MTC0), .out(CP0OUT), ._1(_1_out), ._2(_2_out), ._3(_3_out),
    .IR(hasexp), .DTin(main_1_reg2_2), .EPCout(EPC), .in_8(CLK));
  // Probe on rd
  // Probe on rd
  Counter #(.width(12), .max('hfff)) counter_1 (
    .load(1'b0), .D(12'h1), .Q(counter_1_q), .clk(CLK));  // open: count, carry, clr
  Multiplexer #(.width(32), .enable("false")) multiplexer_9 (
    .in0(main_1_reg2_2), .in1(bit_extender_2_out), .out(multiplexer_9_out), .sel(r_slra_1_r_slra));
  // Probe on EPC
  // Probe on counter_1_q
  Shifter #(.width(32)) shifter_2 (.in(immediate), .\dist (5'b00010), .out(shifter_2_out));
  // Probe on multiplexer_8_out
  // Probe on multiplexer_10_out
  Multiplexer #(.width(32), .enable("false")) multiplexer_10 (
    .in0(multiplexer_9_out), .in1(immediate), .out(multiplexer_10_out), .sel(xor_1_out));
  xor xor_1 (xor_1_out, i_type_1_ir_type, BEQ, BNQ);
  or or_1 (or_1_out, BEQ, BNQ);
  Adder #(.width(32)) adder_3 (.a(adder_1_out), .b(shifter_2_out), .out(adder_3_out));  // open: cin, cout
  Multiplexer #(.width(32), .enable("false")) multiplexer_11 (
    .in0(multiplexer_10_out), .in1({32{1'b0}}), .out(multiplexer_11_out), .sel(BLEZ));
  // Probe on CP0OUT
  ALU alu_1 (
    .AluOP(translate_1_alu_op4), .X(multiplexer_8_out), .Equal(EQUAL), .Result({alu_1_result, blezr}),
    .Y(multiplexer_11_out));  // open: Signed_Overflow, Result_2, UnSigned_Overflow
  Counter #(.width(12), .max('hfff)) counter_2 (
    .load(1'b0), .D(12'h1), .count(or_1_out), .Q(counter_2_q), .clk(CLK));  // open: carry, clr
  // Probe on counter_2_q
  or or_2 (or_2_out, Memory1, Memory2);
  and and_4 (and_4_out, BEQ, EQUAL);
  Counter #(.width(12), .max('hfff)) counter_3 (
    .load(1'b0), .D(12'h1), .count(or_2_out), .Q(counter_3_q), .clk(CLK));  // open: carry, clr
  Multiplexer #(.width(32), .enable("false")) multiplexer_12 (
    .in0(adder_1_out), .in1(adder_3_out), .out(multiplexer_12_out), .sel(and_4_out));
  // Probe on counter_3_q
  Multiplexer #(.width(32), .enable("false")) multiplexer_13 (
    .in0(multiplexer_12_out), .in1(adder_3_out), .out(multiplexer_13_out), .sel(and_5_out));
  and and_5 (and_5_out, not_1_out, BNQ);
  not not_1 (not_1_out, EQUAL);
  RAM #(.addrWidth(10), .dataWidth(32), .bus("separate")) ram_1 (
    .addr(alu_1_result[11:2]), .din(main_1_reg2_2), .data({_4, _3, _2, _1}), .str(Memory1), .clk(CLK),
    .ld(Memory2));  // open: sel, clr
  or or_3 (or_3_out, J_COUNT1, J_COUNT2);
  Multiplexer #(.width(32), .enable("false")) multiplexer_14 (
    .in0({alu_1_result, blezr}), .in1({_4, _3, _2, _1}), .out(multiplexer_14_out), .sel(Memory2));
  Register #(.width(32)) register_3 (.D(a0), .en(SYSCALL), .Q(register_3_q), .clk(CLK));  // open: clr
  Counter #(.width(12), .max('hfff)) counter_4 (
    .load(1'b0), .D(12'h1), .Q(counter_4_q), .clk(or_3_out));  // open: count, carry, clr
  // Probe on counter_4_q
  Multiplexer #(.width(32), .enable("false")) multiplexer_15 (
    .in0(multiplexer_13_out), .in1(adder_2_out), .out(multiplexer_15_out), .sel(J_COUNT1));
  or or_4 (J_COUNT1, JL, JAL);
  Hex_Digit_Display hex_digit_display_1 (.value(register_3_q[31:28]));  // open: dp
  // Probe on JR_REG
  Adder #(.width(32)) adder_4 (.a(32'h4), .b(PC), .out(adder_4_out));  // open: cin, cout
  Hex_Digit_Display hex_digit_display_2 (.value(register_3_q[23:20]));  // open: dp
  Hex_Digit_Display hex_digit_display_3 (.value(register_3_q[27:24]));  // open: dp
  Multiplexer #(.width(32), .enable("false")) multiplexer_16 (
    .in0(multiplexer_15_out), .in1(JR_REG), .out(multiplexer_16_out), .sel(J_COUNT2));
  Multiplexer #(.select(2), .width(8), .enable("false")) multiplexer_17 (
    .in0(_1), .in1(_2), .in2(_3), .in3(_4), .out(multiplexer_17_out), .sel({alu_1_result[1], blezr}));
  Multiplexer #(.width(32), .enable("false")) multiplexer_18 (
    .in0(multiplexer_14_out), .in1(adder_4_out), .out(multiplexer_18_out), .sel(JAL));
  Hex_Digit_Display hex_digit_display_4 (.value(register_3_q[19:16]));  // open: dp
  // Probe on shifter_3_out
  Shifter #(.width(32)) shifter_3 (.in(immediate), .\dist (5'b00010), .out(shifter_3_out));
  assign bit_extender_5_out = {{24{1'b0}}, multiplexer_17_out};  // Bit_Extender bit_extender_5
  // Probe on {alu_1_result[1], blezr}
  Hex_Digit_Display hex_digit_display_5 (.value(register_3_q[15:12]));  // open: dp
  // Probe on CP0OUT
  Adder #(.width(32)) adder_5 (.a(multiplexer_16_out), .b(shifter_3_out), .out(adder_5_out));  // open: cin, cout
  // Probe on adder_5_out
  // Probe on bit_extender_5_out
  Shifter #(.width(32)) shifter_4 (.in(immediate), .\dist (5'b10000), .out(shifter_4_out));
  Hex_Digit_Display hex_digit_display_6 (.value(register_3_q[11:8]));  // open: dp
  Multiplexer #(.width(32), .enable("false")) multiplexer_19 (
    .in0(multiplexer_16_out), .in1(adder_5_out), .out(multiplexer_19_out), .sel(and_6_out));
  and and_6 (and_6_out, BLEZ, or_5_out);
  or or_5 (or_5_out, blezr, EQUAL);
  Multiplexer #(.width(32), .enable("false")) multiplexer_20 (
    .in0(multiplexer_18_out), .in1(shifter_4_out), .out(multiplexer_20_out), .sel(LUI));
  Hex_Digit_Display hex_digit_display_7 (.value(register_3_q[7:4]));  // open: dp
  Multiplexer #(.width(32), .enable("false")) multiplexer_21 (
    .in0(multiplexer_20_out), .in1(bit_extender_5_out), .out(multiplexer_21_out), .sel(LBU));
  Multiplexer #(.width(32), .enable("false")) multiplexer_22 (
    .in0(multiplexer_21_out), .in1(CP0OUT), .out(multiplexer_22_out), .sel(MFC0));
  Hex_Digit_Display hex_digit_display_8 (.value(register_3_q[3:0]));  // open: dp

  // Other names for the same wires on the sheet: JR = J_COUNT2; J_count3 = BEQ; J_count4 = BNQ

  // Notes on the sheet:
  //   contents of rom_1 (hex, n*v repeats v):
  //   20110001 8000c05 20110001 20120002 20130003 8000c09 20110001 20120002 20130003 8000c0d 20110001
  //   20120002 20130003 8000c11 20110001 20120002 20130003 c000cb8 20100001 20110001 118fc0 112020
  //   20020022 c 118882 12200001 8000c15 112020 20020022 c 20110001 118880 112020 20020022 c 12200001
  //   8000c1f 20110001 118fc0 112020 20020022 c 1188c3 112020 20020022 c 118903 112020 20020022 c 118903
  //   112020 20020022 c 118903 112020 20020022 c 118903 112020 20020022 c 118903 112020 20020022 c 118903
  //   112020 20020022 c 118903 112020 20020022 c 20100001 109fc0 139fc3 8021 2012000c 24160003 26100001
  //   3210000f 20080008 20090001 139900 2709825 132020 20020022 c 1094022 1500fff9 22100001 2018000f
  //   2188024 108700 20080008 20090001 139902 2709825 132021 20020022 c 1094022 1500fff9 108702 2c9b022
  //   12c00001 8000c50 4020 1084027 84400 3508ffff 82021 20020022 c 2010ffff 20110000 ae300000 22100001
  //   22310004 ae300000 22100001 22310004 ae300000 22100001 22310004 ae300000 22100001 22310004 ae300000
  //   22100001 22310004 ae300000 22100001 22310004 ae300000 22100001 22310004 ae300000 22100001 22310004
  //   ae300000 22100001 22310004 ae300000 22100001 22310004 ae300000 22100001 22310004 ae300000 22100001
  //   22310004 ae300000 22100001 22310004 ae300000 22100001 22310004 ae300000 22100001 22310004 ae300000
  //   22100001 22310004 22100001 8020 2011003c 8e130000 8e340000 274402a 11000002 ae330000 ae140000
  //   2231fffc 1611fff8 102020 20020022 c 22100004 2011003c 1611fff2 2002000a c 20100000 22100001 102020
  //   20020022 c 22100002 102020 20020022 c 22100003 102020 20020022 c 22100004 102020 20020022 c 22100005
  //   102020 20020022 c 22100006 102020 20020022 c 22100007 102020 20020022 c 22100008 102020 20020022
  //   20020022 c 3e00008
  //   contents of rom_2 (hex, n*v repeats v):
  //   401a6000 375a0001 409a6000 23bd0080 afb00000 23bd0004 40106000 108043 108040 afb00000 23bd0004
  //   afb10000 23bd0004 afa20000 23bd0004 afa40000 23bd0004 afba0000 23bd0004 40107000 afb00000 23bd0004
  //   40116800 20100001 12300004 20100002 12300006 20100003 12300008 20110003 40916000 20110001 12300008
  //   20110007 40916000 20110002 12300004 2011000f 40916000 20110003 12300000 401a6000 1ad043 1ad040
  //   409a6000 40116800 20100001 12300006 20100002 12300011 20100003 1230001c 20100000 12000026 20110000
  //   20020022 22040000 c 108100 1630fffc 20100001 108700 22040000 c 108103 1630fffc 12300019 20110000
  //   20020022 22040000 c 108100 1630fffc 20100002 108700 22040000 c 108103 1630fffc 1230000c 20110000
  //   20020022 22040000 c 108100 1630fffc 20100003 108700 22040000 c 108103 1630fffc 20040000 c 401a6000
  //   375a0001 409a6000 23bdfffc 8fb00000 40907000 23bdfffc 8fba0000 23bdfffc 8fa40000 23bdfffc 8fa20000
  //   23bdfffc 8fb10000 23bdfffc 8fb00000 36100001 40906000 23bdfffc 8fb00000 23bdff80 401a6000 1ad043
  //   1ad040 409a6000 42000018
endmodule

// ALU_CONTROL
module translate (
  input  op1,
  input  op2,
  input  op3,
  input  op4,
  input  op5,
  input  op6,
  input  func1,
  input  func2,
  input  func3,
  input  func4,
  input  func5,
  input  func6,
  output alu_op1,
  output alu_op2,
  output alu_op3,
  output alu_op4
);

  wire and_1_out, and_2_out, and_3_out, and_4_out, and_5_out, and_6_out, and_7_out, and_8_out, and_9_out,
       and_10_out, and_11_out, and_12_out, and_13_out, and_14_out, and_15_out, and_16_out, and_17_out,
       and_18_out, and_19_out, and_20_out, and_21_out, and_22_out, and_23_out, and_24_out, and_25_out,
       and_26_out, and_27_out, and_28_out, and_29_out, and_30_out, and_31_out, and_32_out, and_33_out,
       and_34_out, and_35_out, and_36_out, and_37_out, and_38_out, and_39_out, and_40_out, and_41_out,
       and_42_out, and_43_out, and_44_out, and_45_out, and_46_out, and_47_out, and_48_out, and_49_out,
       and_50_out, and_51_out, and_52_out, and_53_out, not_1_out, not_2_out, not_3_out, not_4_out, not_5_out,
       not_6_out, not_7_out, not_8_out, not_9_out, not_10_out, not_11_out, not_12_out, not_13_out,
       not_14_out, not_15_out, not_16_out, not_17_out, not_18_out, not_19_out, not_20_out, not_21_out,
       not_22_out, not_23_out, not_24_out, not_25_out, not_26_out, not_27_out, not_28_out, not_29_out,
       not_30_out, not_31_out, not_32_out, not_33_out, not_34_out, not_35_out, not_36_out, not_37_out,
       not_38_out, not_39_out, not_40_out, not_41_out, not_42_out, not_43_out, not_44_out, not_45_out,
       not_46_out, not_47_out, not_48_out, not_49_out, not_50_out, not_51_out, not_52_out, not_53_out,
       not_54_out, not_55_out, not_56_out, not_57_out, not_58_out, not_59_out, not_60_out, not_61_out,
       not_62_out, not_63_out, not_64_out, not_65_out, not_66_out, not_67_out, not_68_out, not_69_out,
       not_70_out, not_71_out, not_72_out, not_73_out, not_74_out, not_75_out, not_76_out, not_77_out,
       not_78_out, not_79_out, not_80_out, not_81_out, not_82_out, not_83_out, not_84_out, not_85_out,
       not_86_out, not_87_out, not_88_out, not_89_out, not_90_out, not_91_out, not_92_out, not_93_out,
       not_94_out, not_95_out, not_96_out, not_97_out, not_98_out, not_99_out, not_100_out, not_101_out,
       not_102_out, not_103_out, not_104_out, not_105_out, not_106_out, not_107_out, not_108_out,
       not_109_out, not_110_out, not_111_out, not_112_out, not_113_out, not_114_out, not_115_out,
       not_116_out, not_117_out, not_118_out, not_119_out, not_120_out, not_121_out, not_122_out,
       not_123_out, not_124_out, not_125_out, not_126_out, not_127_out, not_128_out, not_129_out,
       not_130_out, not_131_out, not_132_out, not_133_out, not_134_out, not_135_out, not_136_out,
       not_137_out, not_138_out, not_139_out, not_140_out, not_141_out, not_142_out, not_143_out,
       not_144_out, not_145_out, not_146_out, not_147_out, not_148_out, not_149_out, not_150_out,
       not_151_out, not_152_out, not_153_out, not_154_out, not_155_out, not_156_out, not_157_out,
       not_158_out, not_159_out, not_160_out, not_161_out, not_162_out, not_163_out, not_164_out,
       not_165_out, not_166_out, not_167_out, not_168_out, not_169_out, not_170_out, not_171_out,
       not_172_out, not_173_out, not_174_out, not_175_out, not_176_out, not_177_out, not_178_out,
       not_179_out, not_180_out, not_181_out, not_182_out, or_1_out, or_2_out, or_3_out, or_4_out, or_5_out,
       or_6_out;

  not not_1 (not_1_out, func3);
  not not_2 (not_2_out, func5);
  not not_3 (not_3_out, func3);
  not not_4 (not_4_out, func6);
  not not_5 (not_5_out, func3);
  not not_6 (not_6_out, func4);
  not not_7 (not_7_out, func6);
  not not_8 (not_8_out, func4);
  not not_9 (not_9_out, func3);
  not not_10 (not_10_out, func4);
  not not_11 (not_11_out, func5);
  not not_12 (not_12_out, func6);
  not not_13 (not_13_out, func3);
  not not_14 (not_14_out, func4);
  not not_15 (not_15_out, func5);
  not not_16 (not_16_out, func3);
  not not_17 (not_17_out, func4);
  not not_18 (not_18_out, func6);
  not not_19 (not_19_out, func3);
  not not_20 (not_20_out, func4);
  not not_21 (not_21_out, func3);
  not not_22 (not_22_out, func5);
  not not_23 (not_23_out, func6);
  not not_24 (not_24_out, func4);
  not not_25 (not_25_out, func3);
  not not_26 (not_26_out, func4);
  not not_27 (not_27_out, func6);
  not not_28 (not_28_out, func3);
  not not_29 (not_29_out, func4);
  not not_30 (not_30_out, func3);
  not not_31 (not_31_out, func3);
  not not_32 (not_32_out, func5);
  not not_33 (not_33_out, func6);
  not not_34 (not_34_out, func4);
  not not_35 (not_35_out, func6);
  not not_36 (not_36_out, func3);
  not not_37 (not_37_out, func4);
  not not_38 (not_38_out, func6);
  not not_39 (not_39_out, func3);
  not not_40 (not_40_out, func6);
  not not_41 (not_41_out, func3);
  not not_42 (not_42_out, func4);
  not not_43 (not_43_out, func5);
  not not_44 (not_44_out, func6);
  not not_45 (not_45_out, func3);
  not not_46 (not_46_out, func4);
  not not_47 (not_47_out, func5);
  not not_48 (not_48_out, func3);
  not not_49 (not_49_out, func5);
  not not_50 (not_50_out, func6);
  not not_51 (not_51_out, func3);
  not not_52 (not_52_out, func6);
  not not_53 (not_53_out, func4);
  not not_54 (not_54_out, func6);
  not not_55 (not_55_out, func3);
  not not_56 (not_56_out, func4);
  not not_57 (not_57_out, func3);
  and and_1 (and_1_out, not_1_out, func4, not_2_out, func6);
  and and_2 (and_2_out, not_3_out, func4, func5, not_4_out);
  and and_3 (and_3_out, not_5_out, func4, func5, func6);
  and and_4 (and_4_out, func3, not_6_out, func5, not_7_out);
  and and_5 (and_5_out, func3, not_8_out, func5, func6);
  and and_6 (and_6_out, not_9_out, not_10_out, not_11_out, not_12_out);
  and and_7 (and_7_out, not_13_out, not_14_out, not_15_out, func6);
  and and_8 (and_8_out, not_16_out, not_17_out, func5, not_18_out);
  and and_9 (and_9_out, not_19_out, not_20_out, func5, func6);
  and and_10 (and_10_out, not_21_out, func4, not_22_out, not_23_out);
  and and_11 (and_11_out, func3, not_24_out, func5, func6);
  and and_12 (and_12_out, not_25_out, not_26_out, func5, not_27_out);
  and and_13 (and_13_out, not_28_out, not_29_out, func5, func6);
  and and_14 (and_14_out, not_30_out, func4, func5, func6);
  and and_15 (and_15_out, not_31_out, func4, not_32_out, not_33_out);
  and and_16 (and_16_out, func3, not_34_out, func5, not_35_out);
  and and_17 (and_17_out, not_36_out, not_37_out, func5, not_38_out);
  and and_18 (and_18_out, not_39_out, func4, func5, not_40_out);
  and and_19 (and_19_out, not_41_out, not_42_out, not_43_out, not_44_out);
  and and_20 (and_20_out, not_45_out, not_46_out, not_47_out, func6);
  and and_21 (and_21_out, not_48_out, func4, not_49_out, not_50_out);
  and and_22 (and_22_out, not_51_out, func4, func5, not_52_out);
  and and_23 (and_23_out, func3, not_53_out, func5, not_54_out);
  and and_24 (and_24_out, not_55_out, not_56_out, func5, func6);
  and and_25 (and_25_out, not_57_out, func4, func5, func6);
  not not_58 (not_58_out, op1);
  not not_59 (not_59_out, op2);
  not not_60 (not_60_out, op3);
  not not_61 (not_61_out, op4);
  not not_62 (not_62_out, op5);
  not not_63 (not_63_out, op6);
  not not_64 (not_64_out, func2);
  or or_1 (or_1_out, and_1_out, and_2_out, and_3_out, and_4_out, and_5_out);
  not not_65 (not_65_out, op1);
  not not_66 (not_66_out, op2);
  not not_67 (not_67_out, op5);
  not not_68 (not_68_out, op1);
  not not_69 (not_69_out, op2);
  not not_70 (not_70_out, op6);
  not not_71 (not_71_out, op1);
  not not_72 (not_72_out, op2);
  not not_73 (not_73_out, op4);
  not not_74 (not_74_out, op6);
  not not_75 (not_75_out, op1);
  not not_76 (not_76_out, op2);
  not not_77 (not_77_out, op4);
  not not_78 (not_78_out, op1);
  not not_79 (not_79_out, op2);
  not not_80 (not_80_out, op3);
  not not_81 (not_81_out, op6);
  not not_82 (not_82_out, op1);
  not not_83 (not_83_out, op2);
  not not_84 (not_84_out, op3);
  not not_85 (not_85_out, op4);
  not not_86 (not_86_out, op5);
  not not_87 (not_87_out, op6);
  not not_88 (not_88_out, func2);
  or or_2 (or_2_out, and_6_out, and_7_out, and_8_out, and_9_out, and_10_out, and_11_out);
  not not_89 (not_89_out, op1);
  not not_90 (not_90_out, op2);
  not not_91 (not_91_out, op4);
  not not_92 (not_92_out, op5);
  not not_93 (not_93_out, op6);
  not not_94 (not_94_out, op1);
  not not_95 (not_95_out, op2);
  not not_96 (not_96_out, op4);
  not not_97 (not_97_out, op5);
  not not_98 (not_98_out, op1);
  not not_99 (not_99_out, op2);
  not not_100 (not_100_out, op5);
  not not_101 (not_101_out, op6);
  not not_102 (not_102_out, op2);
  not not_103 (not_103_out, op4);
  not not_104 (not_104_out, op1);
  not not_105 (not_105_out, op2);
  not not_106 (not_106_out, op4);
  not not_107 (not_107_out, op2);
  not not_108 (not_108_out, op3);
  not not_109 (not_109_out, op5);
  not not_110 (not_110_out, op6);
  not not_111 (not_111_out, op1);
  not not_112 (not_112_out, op2);
  not not_113 (not_113_out, op3);
  not not_114 (not_114_out, op4);
  not not_115 (not_115_out, op5);
  not not_116 (not_116_out, op6);
  not not_117 (not_117_out, func2);
  or or_3 (or_3_out, and_12_out, and_13_out, and_14_out, and_15_out, and_16_out);
  not not_118 (not_118_out, op1);
  not not_119 (not_119_out, op2);
  not not_120 (not_120_out, op3);
  not not_121 (not_121_out, op4);
  not not_122 (not_122_out, op5);
  not not_123 (not_123_out, op6);
  not not_124 (not_124_out, func1);
  not not_125 (not_125_out, func2);
  or or_4 (or_4_out, and_17_out, and_18_out);
  not not_126 (not_126_out, op1);
  not not_127 (not_127_out, op2);
  not not_128 (not_128_out, op5);
  not not_129 (not_129_out, op6);
  not not_130 (not_130_out, op1);
  not not_131 (not_131_out, op2);
  not not_132 (not_132_out, op4);
  not not_133 (not_133_out, op6);
  not not_134 (not_134_out, op1);
  not not_135 (not_135_out, op2);
  not not_136 (not_136_out, op3);
  not not_137 (not_137_out, op6);
  not not_138 (not_138_out, op1);
  not not_139 (not_139_out, op2);
  not not_140 (not_140_out, op3);
  not not_141 (not_141_out, op4);
  not not_142 (not_142_out, op5);
  not not_143 (not_143_out, op6);
  not not_144 (not_144_out, func2);
  or or_5 (or_5_out, and_19_out, and_20_out, and_21_out, and_22_out, and_23_out);
  not not_145 (not_145_out, op1);
  not not_146 (not_146_out, op2);
  not not_147 (not_147_out, op3);
  not not_148 (not_148_out, op4);
  not not_149 (not_149_out, op5);
  not not_150 (not_150_out, op6);
  not not_151 (not_151_out, func1);
  not not_152 (not_152_out, func2);
  or or_6 (or_6_out, and_24_out, and_25_out);
  not not_153 (not_153_out, op1);
  not not_154 (not_154_out, op2);
  not not_155 (not_155_out, op4);
  not not_156 (not_156_out, op5);
  not not_157 (not_157_out, op6);
  not not_158 (not_158_out, op1);
  not not_159 (not_159_out, op2);
  not not_160 (not_160_out, op4);
  not not_161 (not_161_out, op5);
  not not_162 (not_162_out, op1);
  not not_163 (not_163_out, op2);
  not not_164 (not_164_out, op5);
  not not_165 (not_165_out, op6);
  not not_166 (not_166_out, op1);
  not not_167 (not_167_out, op2);
  not not_168 (not_168_out, op6);
  not not_169 (not_169_out, op2);
  not not_170 (not_170_out, op4);
  not not_171 (not_171_out, op1);
  not not_172 (not_172_out, op2);
  not not_173 (not_173_out, op4);
  not not_174 (not_174_out, op6);
  not not_175 (not_175_out, op2);
  not not_176 (not_176_out, op3);
  not not_177 (not_177_out, op5);
  not not_178 (not_178_out, op6);
  not not_179 (not_179_out, op1);
  not not_180 (not_180_out, op2);
  not not_181 (not_181_out, op3);
  not not_182 (not_182_out, op6);
  and and_26 (and_26_out, not_58_out, not_59_out, not_60_out, not_61_out, not_62_out, not_63_out, func1, not_64_out, or_1_out);
  and and_27 (and_27_out, not_65_out, not_66_out, op3, op4, not_67_out, op6);
  and and_28 (and_28_out, not_68_out, not_69_out, op3, op4, op5, not_70_out);
  and and_29 (and_29_out, not_71_out, not_72_out, op3, not_73_out, op5, not_74_out);
  and and_30 (and_30_out, not_75_out, not_76_out, op3, not_77_out, op5, op6);
  and and_31 (and_31_out, not_78_out, not_79_out, not_80_out, op4, op5, not_81_out);
  and and_32 (and_32_out, not_82_out, not_83_out, not_84_out, not_85_out, not_86_out, not_87_out, func1, not_88_out, or_2_out);
  and and_33 (and_33_out, not_89_out, not_90_out, op3, not_91_out, not_92_out, not_93_out);
  and and_34 (and_34_out, not_94_out, not_95_out, op3, not_96_out, not_97_out, op6);
  and and_35 (and_35_out, not_98_out, not_99_out, op3, op4, not_100_out, not_101_out);
  and and_36 (and_36_out, op1, not_102_out, not_103_out, op5, op6);
  and and_37 (and_37_out, not_104_out, not_105_out, op3, not_106_out, op5, op6);
  and and_38 (and_38_out, op1, not_107_out, not_108_out, op4, not_109_out, not_110_out);
  and and_39 (and_39_out, not_111_out, not_112_out, not_113_out, not_114_out, not_115_out, not_116_out, func1, not_117_out, or_3_out);
  and and_40 (and_40_out, not_118_out, not_119_out, not_120_out, not_121_out, not_122_out, not_123_out, not_124_out, not_125_out, or_4_out);
  and and_41 (and_41_out, not_126_out, not_127_out, op3, op4, not_128_out, not_129_out);
  and and_42 (and_42_out, not_130_out, not_131_out, op3, not_132_out, op5, not_133_out);
  and and_43 (and_43_out, not_134_out, not_135_out, not_136_out, op4, op5, not_137_out);
  and and_44 (and_44_out, not_138_out, not_139_out, not_140_out, not_141_out, not_142_out, not_143_out, func1, not_144_out, or_5_out);
  and and_45 (and_45_out, not_145_out, not_146_out, not_147_out, not_148_out, not_149_out, not_150_out, not_151_out, not_152_out, or_6_out);
  and and_46 (and_46_out, not_153_out, not_154_out, op3, not_155_out, not_156_out, not_157_out);
  and and_47 (and_47_out, not_158_out, not_159_out, op3, not_160_out, not_161_out, op6);
  and and_48 (and_48_out, not_162_out, not_163_out, op3, op4, not_164_out, not_165_out);
  and and_49 (and_49_out, not_166_out, not_167_out, op3, op4, op5, not_168_out);
  and and_50 (and_50_out, op1, not_169_out, not_170_out, op5, op6);
  and and_51 (and_51_out, not_171_out, not_172_out, op3, not_173_out, op5, not_174_out);
  and and_52 (and_52_out, op1, not_175_out, not_176_out, op4, not_177_out, not_178_out);
  and and_53 (and_53_out, not_179_out, not_180_out, not_181_out, op4, op5, not_182_out);
  or or_7 (alu_op1, and_26_out, and_27_out, and_28_out, and_29_out, and_30_out, and_31_out);
  or or_8 (alu_op2, and_32_out, and_33_out, and_34_out, and_35_out, and_36_out, and_37_out, and_38_out);
  or or_9 (alu_op3, and_39_out, and_40_out, and_41_out, and_42_out, and_43_out);
  or or_10 (alu_op4, and_44_out, and_45_out, and_46_out, and_47_out, and_48_out, and_49_out, and_50_out, and_51_out, and_52_out, and_53_out);
endmodule

module r_slra (
  input  [4:0] op1,
  output r1
);

  wire not_1_out, not_2_out, not_3_out, not_4_out, not_5_out;

  not not_1 (not_1_out, op1[0]);
  not not_2 (not_2_out, op1[1]);
  not not_3 (not_3_out, op1[2]);
  not not_4 (not_4_out, op1[3]);
  not not_5 (not_5_out, op1[4]);
  and and_1 (r1, not_1_out, not_2_out, not_3_out, not_4_out, not_5_out);
endmodule

module R_TYPE (
  input  [5:0] op1,
  output IR_type
);

  wire not_1_out, not_2_out, not_3_out, not_4_out, not_5_out, not_6_out;

  not not_1 (not_1_out, op1[0]);
  not not_2 (not_2_out, op1[1]);
  not not_3 (not_3_out, op1[2]);
  not not_4 (not_4_out, op1[3]);
  not not_5 (not_5_out, op1[4]);
  not not_6 (not_6_out, op1[5]);
  and and_1 (IR_type, not_1_out, not_2_out, not_3_out, not_4_out, not_5_out, not_6_out);
endmodule

// R/ITYPE
module I_TYPE (
  input  [5:0] op1,
  output IR_type
);

  or or_1 (IR_type, op1[5], op1[4], op1[3], op1[2], op1[1], op1[0]);
endmodule

module LW (
  input  [5:0] op1,
  output LW
);

  wire and_1_out, and_2_out, not_1_out, not_2_out, not_3_out, not_4_out, not_5_out, not_6_out, not_7_out;

  not not_1 (not_1_out, op1[4]);
  not not_2 (not_2_out, op1[3]);
  not not_3 (not_3_out, op1[2]);
  not not_4 (not_4_out, op1[4]);
  not not_5 (not_5_out, op1[3]);
  not not_6 (not_6_out, op1[1]);
  not not_7 (not_7_out, op1[0]);
  and and_1 (and_1_out, op1[5], not_1_out, not_2_out, not_3_out, op1[1], op1[0]);
  and and_2 (and_2_out, op1[5], not_4_out, not_5_out, op1[2], not_6_out, not_7_out);
  or or_1 (LW, and_1_out, and_2_out);
endmodule

module SW (
  input  [5:0] op1,
  output SW
);

  wire not_1_out, not_2_out;

  not not_1 (not_1_out, op1[4]);
  not not_2 (not_2_out, op1[2]);
  and and_1 (SW, op1[5], not_1_out, op1[3], not_2_out, op1[1], op1[0]);
endmodule

module BEQ (
  input  [5:0] op1,
  output BEQ
);

  wire not_1_out, not_2_out, not_3_out, not_4_out, not_5_out;

  not not_1 (not_1_out, op1[5]);
  not not_2 (not_2_out, op1[4]);
  not not_3 (not_3_out, op1[3]);
  not not_4 (not_4_out, op1[1]);
  not not_5 (not_5_out, op1[0]);
  and and_1 (BEQ, not_1_out, not_2_out, not_3_out, op1[2], not_4_out, not_5_out);
endmodule

module BNE (
  input  [5:0] op1,
  output BEQ
);

  wire not_1_out, not_2_out, not_3_out, not_4_out;

  not not_1 (not_1_out, op1[5]);
  not not_2 (not_2_out, op1[4]);
  not not_3 (not_3_out, op1[3]);
  not not_4 (not_4_out, op1[1]);
  and and_1 (BEQ, not_1_out, not_2_out, not_3_out, op1[2], not_4_out, op1[0]);
endmodule

module R_SLRA (
  input  [5:0] op,
  input  [5:0] func,
  output r_slra
);

  wire and_1_out, and_2_out, and_3_out, not_1_out, not_2_out, not_3_out, not_4_out, not_5_out, not_6_out,
       not_7_out, not_8_out, not_9_out, not_10_out, not_11_out, not_12_out, not_13_out, or_1_out;

  not not_1 (not_1_out, func[1]);
  not not_2 (not_2_out, func[0]);
  not not_3 (not_3_out, func[0]);
  and and_1 (and_1_out, not_1_out, not_2_out);
  and and_2 (and_2_out, func[1], not_3_out);
  and and_3 (and_3_out, func[1], func[0]);
  not not_4 (not_4_out, op[5]);
  not not_5 (not_5_out, op[4]);
  not not_6 (not_6_out, op[3]);
  not not_7 (not_7_out, op[2]);
  not not_8 (not_8_out, op[1]);
  not not_9 (not_9_out, op[0]);
  not not_10 (not_10_out, func[5]);
  not not_11 (not_11_out, func[4]);
  not not_12 (not_12_out, func[3]);
  not not_13 (not_13_out, func[2]);
  or or_1 (or_1_out, and_1_out, and_2_out, and_3_out);
  and and_4 (r_slra, not_4_out, not_5_out, not_6_out, not_7_out, not_8_out, not_9_out, not_10_out, not_11_out, not_12_out, not_13_out, or_1_out);
endmodule

module JL (
  input  [5:0] op,
  output JL
);

  wire not_1_out, not_2_out, not_3_out, not_4_out, not_5_out;

  not not_1 (not_1_out, op[5]);
  not not_2 (not_2_out, op[4]);
  not not_3 (not_3_out, op[3]);
  not not_4 (not_4_out, op[2]);
  not not_5 (not_5_out, op[0]);
  and and_1 (JL, not_1_out, not_2_out, not_3_out, not_4_out, op[1], not_5_out);
endmodule

module WE (
  input  sw,
  input  beq,
  input  bne,
  input  jl,
  input  jr,
  input  blez,
  output we
);

  nor nor_1 (we, sw, beq, bne, jl, jr, blez);
endmodule

// SYSCALL_BREAK
module Syscall_b (
  input  op1,
  input  op2,
  input  op3,
  input  op4,
  input  op5,
  input  op6,
  input  func1,
  input  func2,
  input  func3,
  input  func4,
  input  func5,
  input  func6,
  output syscall
);

  wire not_1_out, not_2_out, not_3_out, not_4_out, not_5_out, not_6_out, not_7_out, not_8_out, not_9_out,
       not_10_out;

  not not_1 (not_1_out, op1);
  not not_2 (not_2_out, op2);
  not not_3 (not_3_out, op3);
  not not_4 (not_4_out, op4);
  not not_5 (not_5_out, op5);
  not not_6 (not_6_out, op6);
  not not_7 (not_7_out, func1);
  not not_8 (not_8_out, func2);
  not not_9 (not_9_out, func5);
  not not_10 (not_10_out, func6);
  and and_1 (syscall, not_1_out, not_2_out, not_3_out, not_4_out, not_5_out, not_6_out, not_7_out, not_8_out, func3, func4, not_9_out, not_10_out);
endmodule

module JAL (
  input  [5:0] op,
  output JAL
);

  wire not_1_out, not_2_out, not_3_out, not_4_out;

  not not_1 (not_1_out, op[5]);
  not not_2 (not_2_out, op[4]);
  not not_3 (not_3_out, op[3]);
  not not_4 (not_4_out, op[2]);
  and and_1 (JAL, not_1_out, not_2_out, not_3_out, not_4_out, op[1], op[0]);
endmodule

module JR (
  input  [5:0] op,
  input  [5:0] func,
  output JR
);

  wire not_1_out, not_2_out, not_3_out, not_4_out, not_5_out, not_6_out, not_7_out, not_8_out, not_9_out,
       not_10_out, not_11_out;

  not not_1 (not_1_out, op[5]);
  not not_2 (not_2_out, op[4]);
  not not_3 (not_3_out, op[3]);
  not not_4 (not_4_out, op[2]);
  not not_5 (not_5_out, op[1]);
  not not_6 (not_6_out, op[0]);
  not not_7 (not_7_out, func[5]);
  not not_8 (not_8_out, func[4]);
  not not_9 (not_9_out, func[2]);
  not not_10 (not_10_out, func[1]);
  not not_11 (not_11_out, func[0]);
  and and_1 (JR, not_1_out, not_2_out, not_3_out, not_4_out, not_5_out, not_6_out, not_7_out, not_8_out, func[3], not_9_out, not_10_out, not_11_out);
endmodule

// zeroext
module zero_extend (
  input  [5:0] op1,
  output zero_ext
);

  wire and_1_out, and_2_out, and_3_out, and_4_out, and_5_out, not_1_out, not_2_out, not_3_out, not_4_out,
       not_5_out, not_6_out, not_7_out, not_8_out, not_9_out, or_1_out;

  not not_1 (not_1_out, op1[2]);
  not not_2 (not_2_out, op1[1]);
  not not_3 (not_3_out, op1[1]);
  not not_4 (not_4_out, op1[0]);
  not not_5 (not_5_out, op1[1]);
  not not_6 (not_6_out, op1[0]);
  not not_7 (not_7_out, op1[2]);
  and and_1 (and_1_out, not_1_out, not_2_out, op1[0]);
  and and_2 (and_2_out, op1[2], not_3_out, not_4_out);
  and and_3 (and_3_out, op1[2], not_5_out, op1[0]);
  and and_4 (and_4_out, op1[2], op1[1], not_6_out);
  and and_5 (and_5_out, not_7_out, op1[1], op1[0]);
  not not_8 (not_8_out, op1[5]);
  not not_9 (not_9_out, op1[4]);
  or or_1 (or_1_out, and_1_out, and_2_out, and_3_out, and_4_out, and_5_out);
  and and_6 (zero_ext, not_8_out, not_9_out, op1[3], or_1_out);
endmodule

module LUI (
  input  [5:0] op1,
  output LUI
);

  wire not_1_out, not_2_out;

  not not_1 (not_1_out, op1[5]);
  not not_2 (not_2_out, op1[4]);
  and and_1 (LUI, not_1_out, not_2_out, op1[3], op1[2], op1[1], op1[0]);
endmodule

module BLEZ (
  input  [5:0] op1,
  output BLEZ
);

  wire not_1_out, not_2_out, not_3_out, not_4_out;

  not not_1 (not_1_out, op1[5]);
  not not_2 (not_2_out, op1[4]);
  not not_3 (not_3_out, op1[3]);
  not not_4 (not_4_out, op1[0]);
  and and_1 (BLEZ, not_1_out, not_2_out, not_3_out, op1[2], op1[1], not_4_out);
endmodule

module LBU (
  input  [5:0] op1,
  output LUI
);

  wire not_1_out, not_2_out, not_3_out, not_4_out;

  not not_1 (not_1_out, op1[4]);
  not not_2 (not_2_out, op1[3]);
  not not_3 (not_3_out, op1[1]);
  not not_4 (not_4_out, op1[0]);
  and and_1 (LUI, op1[5], not_1_out, not_2_out, op1[2], not_3_out, not_4_out);
endmodule

module inresp (
  input  _1,
  input  _2,
  input  IE,
  input  _3,
  input  [2:0] code,
  input  clk,
  output [1:0] out_7,
  output out_8
);

  wire _1_t, _2_t, _3_t, and_1_out, and_2_out, and_3_out, d_ff_1_q, d_ff_3_q, d_ff_5_q, demultiplexer_1_out1,
       demultiplexer_1_out2, demultiplexer_1_out3, multiplexer_1_out, multiplexer_2_out, multiplexer_3_out,
       priority_encoder_1_gs, register_1_q, register_2_q, register_3_q, register_4_q, signal1, signal2,
       signal3;

  D_Flip_Flop d_ff_1 (.clk(_1), .D(1'b1), .Q(d_ff_1_q), .reset(signal1));  // open: Qn, preset, en
  Multiplexer #(.enable("false")) multiplexer_1 (.in0(d_ff_1_q), .in1(1'b0), .out(multiplexer_1_out), .sel(signal1));
  D_Flip_Flop d_ff_2 (.clk(clk), .D(multiplexer_1_out), .Q(_1_t));  // open: Qn, preset, en, reset
  D_Flip_Flop d_ff_3 (.clk(_2), .D(1'b1), .Q(d_ff_3_q), .reset(signal2));  // open: Qn, preset, en
  Multiplexer #(.enable("false")) multiplexer_2 (.in0(d_ff_3_q), .in1(1'b0), .out(multiplexer_2_out), .sel(signal2));
  D_Flip_Flop d_ff_4 (.clk(clk), .D(multiplexer_2_out), .Q(_2_t));  // open: Qn, preset, en, reset
  D_Flip_Flop d_ff_5 (.clk(_3), .D(1'b1), .Q(d_ff_5_q), .reset(signal3));  // open: Qn, preset, en
  Multiplexer #(.enable("false")) multiplexer_3 (.in0(d_ff_5_q), .in1(1'b0), .out(multiplexer_3_out), .sel(signal3));
  D_Flip_Flop d_ff_6 (.clk(clk), .D(multiplexer_3_out), .Q(_3_t));  // open: Qn, preset, en, reset
  Register #(.width(1)) register_1 (.D(code[0]), .Q(register_1_q), .clk(clk));  // open: en, clr
  Register #(.width(1)) register_2 (.D(code[1]), .Q(register_2_q), .clk(clk));  // open: en, clr
  Register #(.width(1)) register_3 (.D(code[2]), .Q(register_3_q), .clk(clk));  // open: en, clr
  and and_1 (and_1_out, _1_t, ~register_1_q);  // AND_Gate
  and and_2 (and_2_out, _2_t, ~register_2_q);  // AND_Gate
  and and_3 (and_3_out, _3_t, ~register_3_q);  // AND_Gate
  Priority_Encoder #(.select(2)) priority_encoder_1 (
    .in0(1'b0), .in1(and_1_out), .in2(and_2_out), .in3(and_3_out), .out(out_7), .gs(priority_encoder_1_gs),
    .en_in(1'b1));  // open: en_out
  Register #(.width(1)) register_4 (.D(IE), .Q(register_4_q), .clk(clk));  // open: en, clr
  and and_4 (out_8, priority_encoder_1_gs, register_4_q);
  Demultiplexer #(.select(2), .enable("false")) demultiplexer_1 (
    .out1(demultiplexer_1_out1), .out2(demultiplexer_1_out2), .out3(demultiplexer_1_out3), .in(out_8),
    .sel(out_7));  // open: out0
  and and_5 (signal1, demultiplexer_1_out1, _1_t);
  and and_6 (signal2, demultiplexer_1_out2, _2_t);
  and and_7 (signal3, demultiplexer_1_out3, _3_t);

  // Other names for the same wires on the sheet: num[1:0] = out_7
endmodule

// INTP
module INTRUPT (
  input  [5:0] op1,
  output INTRRUPT
);

  wire not_1_out, not_2_out, not_3_out, not_4_out, not_5_out;

  not not_1 (not_1_out, op1[5]);
  not not_2 (not_2_out, op1[3]);
  not not_3 (not_3_out, op1[2]);
  not not_4 (not_4_out, op1[1]);
  not not_5 (not_5_out, op1[0]);
  and and_1 (INTRRUPT, not_1_out, op1[4], not_2_out, not_3_out, not_4_out, not_5_out);
endmodule

// MFC0
module mfc0 (
  input  [5:0] op1,
  input  [4:0] mfc0in,
  output MFC0
);

  wire intrupt_1_intrrupt, not_1_out, not_2_out, not_3_out, not_4_out, not_5_out;

  INTRUPT intrupt_1 (.op1(op1), .INTRRUPT(intrupt_1_intrrupt));
  not not_1 (not_1_out, mfc0in[4]);
  not not_2 (not_2_out, mfc0in[3]);
  not not_3 (not_3_out, mfc0in[2]);
  not not_4 (not_4_out, mfc0in[1]);
  not not_5 (not_5_out, mfc0in[0]);
  and and_1 (MFC0, intrupt_1_intrrupt, not_1_out, not_2_out, not_3_out, not_4_out, not_5_out);
endmodule

// MTC0
module mtc0 (
  input  [5:0] op1,
  input  [4:0] mfc0in,
  output MFC0
);

  wire intrupt_1_intrrupt, not_1_out, not_2_out, not_3_out, not_4_out;

  INTRUPT intrupt_1 (.op1(op1), .INTRRUPT(intrupt_1_intrrupt));
  not not_1 (not_1_out, mfc0in[4]);
  not not_2 (not_2_out, mfc0in[3]);
  not not_3 (not_3_out, mfc0in[1]);
  not not_4 (not_4_out, mfc0in[0]);
  and and_1 (MFC0, intrupt_1_intrrupt, not_1_out, not_2_out, mfc0in[2], not_3_out, not_4_out);
endmodule

module CP0 (
  input  [31:0] PCin,
  input  [31:0] DTin,
  input  _3,
  input  _2,
  input  _1,
  input  cp0we,
  input  [4:0] c1,
  input  in_8,
  input  [4:0] c2,
  output [31:0] EPCout,
  output [31:0] out,
  output IR
);

  wire demultiplexer_1_out12, demultiplexer_1_out14, not_1_out, not_2_out, or_1_out;
  wire [1:0] inresp_1_out_7;
  wire [31:0] CAUSE_q, intnum, multiplexer_1_out, SR;

  assign intnum = {{30{1'b0}}, inresp_1_out_7};  // Bit_Extender bit_extender_1
  inresp inresp_1 (
    ._1(_1), .out_7(inresp_1_out_7), ._2(_2), ._3(_3), .code(SR[3:1]), .clk(in_8), .out_8(IR), .IE(not_1_out));
  not not_1 (not_1_out, SR[0]);
  Demultiplexer #(.select(5), .enable("false")) demultiplexer_1 (
    .out12(demultiplexer_1_out12), .out14(demultiplexer_1_out14), .in(cp0we), .sel(c1));  // open: out0, out1, out2, out3, out4, out5, out6, out7, out8, out9, out10, out11, out13, out15, out16, out17, out18, out19, out20, out21, out22, out23, out24, out25, out26, out27, out28, out29, out30, out31
  not not_2 (not_2_out, IR);
  Multiplexer #(.width(32), .enable("false")) multiplexer_1 (
    .in0(PCin), .in1(DTin), .out(multiplexer_1_out), .sel(not_2_out));
  or or_1 (or_1_out, IR, demultiplexer_1_out14);
  Register #(.width(32)) EPC (.D(multiplexer_1_out), .en(or_1_out), .Q(EPCout), .clk(in_8));  // open: clr
  Register #(.width(32)) u_SR (.D(DTin), .en(demultiplexer_1_out12), .Q(SR), .clk(in_8));  // open: clr
  Register #(.width(32)) CAUSE (.D(intnum), .en(1'b1), .Q(CAUSE_q), .clk(in_8));  // open: clr
  Multiplexer #(.select(5), .width(32), .enable("false")) multiplexer_2 (
    .in12(SR), .in13(CAUSE_q), .in14(EPCout), .out(out), .sel(c2));  // open: in0, in1, in2, in3, in4, in5, in6, in7, in8, in9, in10, in11, in15, in16, in17, in18, in19, in20, in21, in22, in23, in24, in25, in26, in27, in28, in29, in30, in31

  // Other names for the same wires on the sheet: CLK = in_8
endmodule

module eret (
  input  [5:0] op1,
  input  [5:0] eretin,
  output ERET
);

  wire intrupt_1_intrrupt, not_1_out, not_2_out, not_3_out, not_4_out;

  INTRUPT intrupt_1 (.op1(op1), .INTRRUPT(intrupt_1_intrrupt));
  not not_1 (not_1_out, eretin[5]);
  not not_2 (not_2_out, eretin[2]);
  not not_3 (not_3_out, eretin[1]);
  not not_4 (not_4_out, eretin[0]);
  and and_1 (ERET, intrupt_1_intrrupt, not_1_out, eretin[4], eretin[3], not_2_out, not_3_out, not_4_out);
endmodule
