// Logisim project 重定向_中断_MIPS.circ as structural Verilog: 32 circuits, main circuit main
module main (
  input  in_1
);

  wire _1_out, _2_out, _3_out, and_3_out, and_5_out, and_6_out, BEQ, BL3, BLEZ, BNQ, BRUANCH,
       bypath_1_forwarda1, bypath_1_forwarda3, bypath_1_forwardb1, bypath_1_forwardb3, CLK, clock_1_out,
       clr1, clr2, comparator_1_eq, d_ff_1_q, d_ff_2_q, EQUAL, ERET1, ERET2, ex_mem_1_jal, ex_mem_1_we,
       hasexp, hazard_unity_1_stop, id_ex_1_i_type_2, id_ex_1_lui_2, id_ex_1_slra_2, id_ex_1_we_2,
       if_id_1_beq, if_id_1_blez, if_id_1_bne, if_id_1_eret, if_id_1_i_type, if_id_1_jal, if_id_1_jl,
       if_id_1_jr, if_id_1_lbu, if_id_1_lui, if_id_1_lw, if_id_1_mfc0, if_id_1_mtc0, if_id_1_slra,
       if_id_1_sw, if_id_1_sys_b, if_id_1_we, J_clr, J_COUNT1, JAL, JL, JR, LBU, LBU1, LUI, LW, LW1,
       mem_wb_1_eret_wb_out, mem_wb_1_jal, Memory2, MFC0, MTC0, not_1_out, or_2_out, or_3_out, or_4_out,
       or_5_out, or_8_out, register_2_q, SW, SW1, SYS_B, SYSCALL, SYSCALL1, SYSCALL2, WE, xor_1_out;
  wire [1:0] bypath_1_forwarda2, bypath_1_forwardb2;
  wire [3:0] ALU_SOURCE, if_id_1_alu_source, register_3_q, register_3_q_2, register_3_q_3, register_3_q_4,
       register_3_q_5, register_3_q_6;
  wire [4:0] ex_mem_1_rsout, id_ex_1_rd_exout, id_ex_1_rs_num, id_ex_1_rt_num, if_id_1_r1_num,
       if_id_1_r2_num, if_id_1_rd, if_id_1_rw_num, RW, RW1, RW2;
  wire [7:0] _1, _2, _3, _4, multiplexer_25_out;
  wire [9:0] demultiplexer_1_out0, demultiplexer_1_out1;
  wire [11:0] counter_2_q, counter_3_q, counter_4_q, counter_5_q, counter_6_q;
  wire [13:0] counter_1_q;
  wire [31:0] a0, adder_1_out, adder_2_out, adder_3_out, adder_4_out, alur1, alur2, and_4_out,
       bit_extender_1_out, cp0_1_out, cp0_data, DIN, EPC, ex_mem_1_alu_r, ex_mem_1_mdin, id_ex_1_r2_num_2,
       id_ex_1_shamt_2, if_id_1_immediate, if_id_1_jump_addr, if_id_1_new_pc2, if_id_1_shamt, IMMEDIATE,
       immediate_t, j_pcaddress, JR_REG, JUMP_ADDR, main_1_reg1, main_1_reg2_2, mem_wb_1_data, mem_wb_1_pc_4,
       multiplexer_1_out, multiplexer_2_out, multiplexer_3_out, multiplexer_5_out, multiplexer_6_out,
       multiplexer_7_out, multiplexer_8_out, multiplexer_9_out, multiplexer_10_out, multiplexer_11_out,
       multiplexer_12_out, multiplexer_13_out, multiplexer_15_out, multiplexer_16_out, multiplexer_17_out,
       multiplexer_18_out, multiplexer_20_out, multiplexer_21_out, multiplexer_22_out, multiplexer_24_out,
       multiplexer_26_out, PC_4, PC_next, register_1_q, rom_1_data, rom_2_data, shifter_1_out, shifter_2_out,
       shifter_3_out, v0;
  wire [31:24] register_3_q_7;

  or or_1 (J_clr, JL, JAL, BRUANCH, JR, BL3);
  Multiplexer #(.width(32), .enable("false")) multiplexer_1 (
    .in0(adder_1_out), .in1(j_pcaddress), .out(multiplexer_1_out), .sel(J_clr));
  Multiplexer #(.width(32), .enable("false")) multiplexer_2 (
    .in0(multiplexer_1_out), .in1(EPC), .out(multiplexer_2_out), .sel(ERET1));
  Multiplexer #(.width(32), .enable("false")) multiplexer_3 (
    .in0(multiplexer_2_out), .in1(32'h80000000), .out(multiplexer_3_out), .sel(hasexp));
  or or_2 (or_2_out, LW1, LBU1);
  Register #(.width(32)) register_1 (
    .D(multiplexer_3_out), .en(hazard_unity_1_stop), .Q(register_1_q), .clk(CLK), .clr(in_1));
  Button u__3 (.out(_3_out));
  Multiplexer #(.enable("false")) multiplexer_4 (.in0(clock_1_out), .in1(1'b1), .out(CLK), .sel(register_2_q));
  Clock clock_1 (.out(clock_1_out));
  Comparator #(.width(32)) comparator_1 (.a(v0), .b(32'ha), .eq(comparator_1_eq));  // open: gt, lt
  HAZARD_UNITY hazard_unity_1 (
    .LWin(or_2_out), .IDEX_RT1(id_ex_1_rt_num), .CLK(CLK), .IFID_RS1(if_id_1_r1_num),
    .IFID_RT1(if_id_1_r2_num), .STOP(hazard_unity_1_stop), .CLEAR(clr2));
  Demultiplexer #(.width(10), .enable("false")) demultiplexer_1 (
    .out0(demultiplexer_1_out0), .out1(demultiplexer_1_out1), .in(register_1_q[11:2]), .sel(register_1_q[31]));
  Multiplexer #(.width(32), .enable("false")) multiplexer_5 (
    .in0(PC_next), .in1(j_pcaddress), .out(multiplexer_5_out), .sel(J_clr));
  Button u__1 (.out(_1_out));
  Button u__2 (.out(_2_out));
  D_Flip_Flop #(.trigger("falling")) d_ff_1 (.clk(CLK), .D(J_clr), .Q(d_ff_1_q));  // open: Qn, preset, en, reset
  Multiplexer #(.width(32), .enable("false")) multiplexer_6 (
    .in0(multiplexer_5_out), .in1(register_1_q), .out(multiplexer_6_out), .sel(ERET2));
  Register #(.width(1), .trigger("falling")) register_2 (.D(1'b1), .Q(register_2_q), .clk(SYS_B));  // open: en, clr
  and and_1 (SYS_B, SYSCALL, comparator_1_eq);
  and and_2 (clr1, ~CLK, d_ff_1_q);  // AND_Gate
  Adder #(.width(32)) adder_1 (.a(32'h4), .b(register_1_q), .out(adder_1_out));  // open: cin, cout
  ROM #(.addrWidth(10), .dataWidth(32)) rom_1 (.addr(demultiplexer_1_out0), .data(rom_1_data));  // open: sel
  ROM #(.addrWidth(10), .dataWidth(32)) rom_2 (.addr(demultiplexer_1_out1), .data(rom_2_data));  // open: sel
  // Probe on cp0_data
  CP0 cp0_1 (
    .c1(id_ex_1_rd_exout), .c2(id_ex_1_rd_exout), .PCin(multiplexer_6_out), .cp0we(MTC0), .out(cp0_1_out),
    .DTin(cp0_data), .EPCout(EPC), .clk(CLK), ._1(_1_out), ._2(_2_out), .out_12(hasexp), ._3(_3_out));
  or or_3 (or_3_out, hasexp, clr1);
  Multiplexer #(.width(32), .enable("false")) multiplexer_7 (
    .in0(rom_1_data), .in1(rom_2_data), .out(multiplexer_7_out), .sel(register_1_q[31]));
  IF_ID if_id_1 (
    .PC_4(adder_1_out), .INSTRUCTION(multiplexer_7_out), .CLK(CLK), .NEW_PC2(if_id_1_new_pc2),
    .JUMP_ADDR(if_id_1_jump_addr), .I_TYPE(if_id_1_i_type), .LW(if_id_1_lw), .SW(if_id_1_sw),
    .BEQ(if_id_1_beq), .BNE(if_id_1_bne), .JL(if_id_1_jl), .JR(if_id_1_jr), .BLEZ(if_id_1_blez),
    .WE(if_id_1_we), .JAL(if_id_1_jal), .LUI(if_id_1_lui), .LBU(if_id_1_lbu), .SYS_B(if_id_1_sys_b),
    .ALU_SOURCE(if_id_1_alu_source), .SLRA(if_id_1_slra), .R1_num(if_id_1_r1_num), .R2_num(if_id_1_r2_num),
    .RW_num(if_id_1_rw_num), .shamt(if_id_1_shamt), .immediate(if_id_1_immediate), .CLEAR(or_3_out),
    .STOP(hazard_unity_1_stop), .MFC0(if_id_1_mfc0), .MTC0(if_id_1_mtc0), .ERET(if_id_1_eret),
    .RD(if_id_1_rd), .PC_ID(register_1_q));  // open: PC_id_out
  Register #(.width(32)) register_3 (
    .D(a0), .en(SYSCALL),
    .Q({register_3_q_7, register_3_q_6, register_3_q_5, register_3_q_4, register_3_q_3, register_3_q_2, register_3_q}),
    .clk(CLK));  // open: clr
  // Probe on j_pcaddress
  Hex_Digit_Display hex_digit_display_1 (.value(register_3_q_7[31:28]));  // open: dp
  Hex_Digit_Display hex_digit_display_2 (.value(register_3_q_7[27:24]));  // open: dp
  \CS1409_U201414808_王林_regfile_main  main_1 (
    .Reg1_num(if_id_1_r1_num), .Reg2(if_id_1_r2_num), .Write_Reg_num(RW), .Din(DIN), .Write_Enable(WE),
    .Clock(CLK), .Reg1(main_1_reg1), .Reg2_2(main_1_reg2_2), .v0(v0), .a0(a0));  // open: s0_Value, s1_Value, s2_Value, ra_Value
  Hex_Digit_Display hex_digit_display_3 (.value(register_3_q_6));  // open: dp
  // Probe on if_id_1_r2_num
  Hex_Digit_Display hex_digit_display_4 (.value(register_3_q_5));  // open: dp
  // Probe on if_id_1_r1_num
  Multiplexer #(.width(32), .enable("false")) multiplexer_8 (
    .in0(main_1_reg1), .in1(DIN), .out(multiplexer_8_out), .sel(bypath_1_forwarda1));
  Hex_Digit_Display hex_digit_display_5 (.value(register_3_q_4));  // open: dp
  // Probe on multiplexer_8_out
  Multiplexer #(.width(32), .enable("false")) multiplexer_9 (
    .in0(main_1_reg2_2), .in1(DIN), .out(multiplexer_9_out), .sel(bypath_1_forwardb1));
  Hex_Digit_Display hex_digit_display_6 (.value(register_3_q_3));  // open: dp
  Hex_Digit_Display hex_digit_display_7 (.value(register_3_q_2));  // open: dp
  Hex_Digit_Display hex_digit_display_8 (.value(register_3_q));  // open: dp
  // Probe on id_ex_1_rt_num
  ID_EX id_ex_1 (
    .RW_num(if_id_1_rw_num), .I_TYPE(if_id_1_i_type), .LW(if_id_1_lw), .SW(if_id_1_sw), .BEQ(if_id_1_beq),
    .BNE(if_id_1_bne), .RW_num_2(RW1), .I_TYPE_2(id_ex_1_i_type_2), .LW_2(LW1), .SW_2(SW1), .BEQ_2(BEQ),
    .BNE_2(BNQ), .JL(if_id_1_jl), .JR(if_id_1_jr), .BLEZ(if_id_1_blez), .WE(if_id_1_we), .JAL(if_id_1_jal),
    .LUI(if_id_1_lui), .JL_2(JL), .JR_2(JR), .BLEZ_2(BLEZ), .WE_2(id_ex_1_we_2), .JAL_2(JAL),
    .LUI_2(id_ex_1_lui_2), .LBU(if_id_1_lbu), .SYS_B(if_id_1_sys_b), .ALU_SOURCE(if_id_1_alu_source),
    .SLRA(if_id_1_slra), .R1_num(multiplexer_8_out), .R2_num(multiplexer_9_out), .LBU_2(LBU1),
    .SYS_B_2(SYSCALL1), .ALU_SOURCE_2(ALU_SOURCE), .SLRA_2(id_ex_1_slra_2), .R1_num_2(JR_REG),
    .R2_num_2(id_ex_1_r2_num_2), .shamt(if_id_1_shamt), .immediate(if_id_1_immediate),
    .JUMP_ADDR(if_id_1_jump_addr), .shamt_2(id_ex_1_shamt_2), .immediate_2(immediate_t),
    .JUMP_ADDR_2(JUMP_ADDR), .PC(if_id_1_new_pc2), .PC_2(PC_next), .CLK(CLK), .RSin(if_id_1_r1_num),
    .RTin(if_id_1_r2_num), .RS_num(id_ex_1_rs_num), .RT_num(id_ex_1_rt_num), .CLEAR(clr2),
    .mfc0_id(if_id_1_mfc0), .mfc0_ex_in(MFC0), .mtc0_exin(if_id_1_mtc0), .rd_exin(if_id_1_rd),
    .eret_exin(if_id_1_eret), .mtc0_exout(MTC0), .eret_ex_out(ERET1), .rd_exout(id_ex_1_rd_exout));
  // Probe on id_ex_1_rt_num
  D_Flip_Flop #(.trigger("falling")) d_ff_2 (.clk(CLK), .D(BRUANCH), .Q(d_ff_2_q));  // open: Qn, preset, en, reset
  // Probe on PC_next
  Counter #(.width(14), .max('h3fff)) counter_1 (
    .load(1'b0), .D(14'h1), .Q(counter_1_q), .clk(CLK));  // open: count, carry, clr
  // Probe on counter_1_q
  // Probe on counter_2_q
  Counter #(.width(12), .max('hfff)) counter_2 (
    .load(1'b0), .D(12'h1), .Q(counter_2_q), .clk(and_3_out));  // open: count, carry, clr
  and and_3 (and_3_out, ~CLK, d_ff_2_q);  // AND_Gate
  assign and_4_out = 32'hf0000000 & PC_next;  // AND_Gate and_4, 32 bits wide
  Multiplexer #(.width(32), .enable("false")) multiplexer_10 (
    .in0(JR_REG), .in1(id_ex_1_r2_num_2), .out(multiplexer_10_out), .sel(id_ex_1_slra_2));
  // Probe on PC_next
  Multiplexer #(.width(32), .enable("false")) multiplexer_11 (
    .in0(id_ex_1_r2_num_2), .in1(id_ex_1_shamt_2), .out(multiplexer_11_out), .sel(id_ex_1_slra_2));
  Adder #(.width(32)) adder_2 (.a(and_4_out), .b(JUMP_ADDR), .out(adder_2_out));  // open: cin, cout
  Shifter #(.width(32)) shifter_1 (.in(immediate_t), .\dist (5'b00010), .out(shifter_1_out));
  Multiplexer #(.select(2), .width(32), .enable("false")) multiplexer_12 (
    .in0(multiplexer_10_out), .in1(DIN), .in2(multiplexer_21_out), .out(multiplexer_12_out),
    .sel(bypath_1_forwarda2));  // open: in3
  Multiplexer #(.select(2), .width(32), .enable("false")) multiplexer_13 (
    .in0(multiplexer_11_out), .in1(DIN), .in2(multiplexer_21_out), .out(multiplexer_13_out),
    .sel(bypath_1_forwardb2));  // open: in3
  or or_4 (or_4_out, SW, LW);
  or or_5 (or_5_out, J_COUNT1, JR);
  // Probe on adder_2_out
  Adder #(.width(32)) adder_3 (.a(PC_next), .b(shifter_1_out), .out(adder_3_out));  // open: cin, cout
  Multiplexer #(.width(32), .enable("false")) multiplexer_14 (
    .in0(multiplexer_13_out), .in1(immediate_t), .out(cp0_data), .sel(xor_1_out));
  xor xor_1 (xor_1_out, id_ex_1_i_type_2, BEQ, BNQ);
  Counter #(.width(12), .max('hfff)) counter_3 (
    .load(1'b0), .D(12'h1), .Q(counter_3_q), .clk(or_4_out));  // open: count, carry, clr
  // Probe on counter_3_q
  // Probe on counter_4_q
  Counter #(.width(12), .max('hfff)) counter_4 (
    .load(1'b0), .D(12'h1), .Q(counter_4_q), .clk(or_5_out));  // open: count, carry, clr
  Multiplexer #(.width(32), .enable("false")) multiplexer_15 (
    .in0(PC_next), .in1(adder_3_out), .out(multiplexer_15_out), .sel(BRUANCH));
  or or_6 (BRUANCH, and_6_out, and_5_out);
  and and_5 (and_5_out, not_1_out, BNQ);
  and and_6 (and_6_out, BEQ, EQUAL);
  not not_1 (not_1_out, EQUAL);
  // Probe on multiplexer_12_out
  Multiplexer #(.width(32), .enable("false")) multiplexer_16 (
    .in0(id_ex_1_r2_num_2), .in1(DIN), .out(multiplexer_16_out), .sel(bypath_1_forwardb3));
  ALU alu_1 (
    .AluOP(ALU_SOURCE), .X(multiplexer_12_out), .Equal(EQUAL), .Result(alur1), .Y(multiplexer_17_out));  // open: Signed_Overflow, Result_2, UnSigned_Overflow
  Multiplexer #(.width(32), .enable("false")) multiplexer_17 (
    .in0(cp0_data), .in1({32{1'b0}}), .out(multiplexer_17_out), .sel(BLEZ));
  // Probe on alur1
  Multiplexer #(.width(32), .enable("false")) multiplexer_18 (
    .in0(multiplexer_15_out), .in1(adder_2_out), .out(multiplexer_18_out), .sel(J_COUNT1));
  or or_7 (J_COUNT1, JL, JAL);
  EX_MEM ex_mem_1 (
    .PC1(PC_next), .ALU_R1(alur2), .MDIN1(multiplexer_16_out), .SYSCALL1(SYSCALL1), .RW1(RW1), .LBU1(LBU1),
    .IMMEDIATE1(immediate_t), .LW1(LW1), .SW1(SW1), .JAL1(JAL), .WE1(id_ex_1_we_2), .LUI1(id_ex_1_lui_2),
    .CLK(CLK), .PC(PC_4), .ALU_R(ex_mem_1_alu_r), .MDIN(ex_mem_1_mdin), .SYSCALL(SYSCALL2), .RW(RW2),
    .LBU(LBU), .LW(LW), .SW(SW), .JAL(ex_mem_1_jal), .IMMEDIATE(IMMEDIATE), .WE(ex_mem_1_we), .LUI(LUI),
    .RSin(id_ex_1_rt_num), .RSout(ex_mem_1_rsout), .eret_mem_in(ERET1), .eret_mem_out(ERET2));
  // Probe on ALU_SOURCE
  Multiplexer #(.width(32), .enable("false")) multiplexer_19 (.in0(alur1), .in1(cp0_1_out), .out(alur2), .sel(MFC0));
  BYPATH bypath_1 (
    .WR1_MEM(RW2), .WR2_WB(RW), .WE1_MEM(ex_mem_1_we), .WE2_WB(WE), .ForwardA2(bypath_1_forwarda2),
    .ForwardB2(bypath_1_forwardb2), .RS_read2(id_ex_1_rs_num), .RT_read2(id_ex_1_rt_num),
    .RS_read1(if_id_1_r1_num), .RT_read(if_id_1_r2_num), .ForwardA1(bypath_1_forwarda1),
    .ForwardB1(bypath_1_forwardb1), .RT_read3(ex_mem_1_rsout), .ForwardA3(bypath_1_forwarda3),
    .ForwardB3(bypath_1_forwardb3), .SLARin(id_ex_1_slra_2));
  Counter #(.width(12), .max('hfff)) counter_5 (
    .load(1'b0), .D(12'h1), .Q(counter_5_q), .clk(clr1));  // open: count, carry, clr
  Counter #(.width(12), .max('hfff)) counter_6 (
    .load(1'b0), .D(12'h1), .Q(counter_6_q), .clk(clr2));  // open: count, carry, clr
  // Probe on counter_6_q
  // Probe on JR_REG
  // Probe on counter_5_q
  Multiplexer #(.width(32), .enable("false")) multiplexer_20 (
    .in0(multiplexer_18_out), .in1(JR_REG), .out(multiplexer_20_out), .sel(JR));
  // Probe on PC_4
  Shifter #(.width(32)) shifter_2 (.in(IMMEDIATE), .\dist (5'b10000), .out(shifter_2_out));
  Shifter #(.width(32)) shifter_3 (.in(immediate_t), .\dist (5'b00010), .out(shifter_3_out));
  Multiplexer #(.width(32), .enable("false")) multiplexer_21 (
    .in0(ex_mem_1_alu_r), .in1(shifter_2_out), .out(multiplexer_21_out), .sel(LUI));
  Multiplexer #(.width(32), .enable("false")) multiplexer_22 (
    .in0(ex_mem_1_mdin), .in1(DIN), .out(multiplexer_22_out), .sel(bypath_1_forwarda3));
  Adder #(.width(32)) adder_4 (.a(multiplexer_20_out), .b(shifter_3_out), .out(adder_4_out));  // open: cin, cout
  // Probe on multiplexer_21_out
  Multiplexer #(.width(32), .enable("false")) multiplexer_23 (
    .in0(multiplexer_20_out), .in1(adder_4_out), .out(j_pcaddress), .sel(BL3));
  and and_7 (BL3, BLEZ, or_8_out);
  or or_8 (or_8_out, alur2[0], EQUAL);
  // Probe on RW2
  // Probe on j_pcaddress
  or or_9 (Memory2, LW, LBU);
  RAM #(.addrWidth(10), .dataWidth(32), .bus("separate")) ram_1 (
    .addr(multiplexer_21_out[11:2]), .din(multiplexer_22_out), .data({_4, _3, _2, _1}), .str(SW), .clk(CLK),
    .ld(Memory2));  // open: sel, clr
  Multiplexer #(.width(32), .enable("false")) multiplexer_24 (
    .in0(multiplexer_21_out), .in1({_4, _3, _2, _1}), .out(multiplexer_24_out), .sel(Memory2));
  Multiplexer #(.select(2), .width(8), .enable("false")) multiplexer_25 (
    .in0(_1), .in1(_2), .in2(_3), .in3(_4), .out(multiplexer_25_out), .sel(multiplexer_21_out[1:0]));
  assign bit_extender_1_out = {{24{1'b0}}, multiplexer_25_out};  // Bit_Extender bit_extender_1
  // Probe on multiplexer_24_out
  Multiplexer #(.width(32), .enable("false")) multiplexer_26 (
    .in0(multiplexer_24_out), .in1(bit_extender_1_out), .out(multiplexer_26_out), .sel(LBU));
  MEM_WB mem_wb_1 (
    .PC_41(PC_4), .DATA1(multiplexer_26_out), .SYSCALL1(SYSCALL2), .RW(RW2), .JAL1(ex_mem_1_jal),
    .WE1(ex_mem_1_we), .CLK(CLK), .PC_4(mem_wb_1_pc_4), .DATA(mem_wb_1_data), .SYSCALL(SYSCALL), .RW_2(RW),
    .JAL(mem_wb_1_jal), .WE(WE), .eret_wb_in(ERET2), .eret_wb_out(mem_wb_1_eret_wb_out));
  Multiplexer #(.width(32), .enable("false")) multiplexer_27 (
    .in0(mem_wb_1_data), .in1(mem_wb_1_pc_4), .out(DIN), .sel(mem_wb_1_jal));

  // Other names for the same wires on the sheet: blezr = alur2[0]

  // Notes on the sheet:
  //   contents of rom_1 (hex, n*v repeats v):
  //   20110001 8000c05 20110001 20120002 20130003 8000c09 20110001 20120002 20130003 8000c0d 20110001
  //   20120002 20130003 8000c11 20110001 20120002 20130003 c000ce0 20100001 20110001 118fc0 112020
  //   20020022 c 118882 12200001 8000c15 112020 20020022 c 20110001 118880 112020 20020022 c 12200001
  //   8000c1f 20110001 118fc0 112020 20020022 c 1188c3 112020 20020022 c 118903 112020 20020022 c 118903
  //   112020 20020022 c 118903 112020 20020022 c 118903 112020 20020022 c 118903 112020 20020022 c 118903
  //   112020 20020022 c 118903 112020 20020022 c 20100001 109fc0 139fc3 8021 2012000c 24160003 26100001
  //   3210000f 20080008 20090001 139900 2709825 132020 20020022 c 1094022 1500fff9 22100001 2018000f
  //   2188024 108700 20080008 20090001 139902 2709825 132021 20020022 c 1094022 1500fff9 108702 2c9b022
  //   12c00001 8000c50 4020 1084027 84400 3508ffff 82021 20020022 c 2010ffff 20110000 ae300000 22100001
  //   22310004 ae300000 22100001 22310004 ae300000 22100001 22310004 ae300000 22100001 22310004 ae300000
  //   22100001 22310004 ae300000 22100001 22310004 ae300000 22100001 22310004 ae300000 22100001 22310004
  //   ae300000 22100001 22310004 ae300000 22100001 22310004 ae300000 22100001 22310004 ae300000 22100001
  //   22310004 ae300000 22100001 22310004 ae300000 22100001 22310004 ae300000 22100001 22310004 ae300000
  //   22100001 22310004 22100001 8020 2011003c 8e130000 8e340000 274402a 11000002 ae330000 ae140000
  //   2231fffc 1611fff8 102020 20020022 c 22100004 2011003c 1611fff2 20100034 92130000 132020 20020022 c
  //   10*0 3c130001 132020 20020022 c 8020 1a000002 2002000a c 11*0 3c01fffe 3421ffff 2619826 132020
  //   20020022 c 2002000a c 20100000 22100001 102020 20020022 c 22100002 102020 20020022 c 22100003 102020
  //   20020022 c 22100004 102020 20020022 c 22100005 102020 20020022 c 22100006 102020 20020022 c 22100007
  //   102020 20020022 c 22100008 102020 20020022 20020022 c 3e00008
  //   contents of rom_2 (hex, n*v repeats v):
  //   401a6000 375a0001 409a6000 23bd0080 afb00000 23bd0004 40106000 108043 108040 afb00000 23bd0004
  //   afb10000 23bd0004 afa20000 23bd0004 afa40000 23bd0004 afba0000 23bd0004 40107000 afb00000 23bd0004
  //   40116800 20100001 12300004 20100002 12300006 20100003 12300008 20110003 40916000 20110001 12300008
  //   20110007 40916000 20110002 12300004 2011000f 40916000 20110003 12300000 401a6000 1ad043 1ad040
  //   409a6000 40116800 20100001 12300006 20100002 12300011 20100003 1230001c 20100000 12000026 20110000
  //   20020022 22040000 c 108100 1630fffc 20100001 108700 22040000 c 108103 1630fffc 12300019 20110000
  //   20020022 22040000 c 108100 1630fffc 20100002 108700 22040000 c 108103 1630fffc 1230000c 20110000
  //   20020022 22040000 c 108100 1630fffc 20100003 108700 22040000 c 108103 1630fffc 20040000 c 401a6000
  //   375a0001 409a6000 23bdfffc 8fb00000 40907000 23bdfffc 8fba0000 23bdfffc 8fa40000 23bdfffc 8fa20000
  //   23bdfffc 8fb10000 23bdfffc 8fb00000 36100001 40906000 23bdfffc 8fb00000 23bdff80 401a6000 1ad043
  //   1ad040 409a6000 42000018
endmodule

// ALU_CONTROL
module ALU_T (
  input  [5:0] op,
  input  [5:0] funct,
  output [3:0] out_3
);

  wire and_1_out, and_2_out, and_3_out, and_4_out, and_5_out, and_6_out, and_7_out, and_8_out, and_9_out,
       and_10_out, and_11_out, and_12_out, and_13_out, and_14_out, and_15_out, and_16_out, and_17_out,
       and_18_out, and_19_out, and_20_out, and_21_out, and_22_out, and_23_out, and_24_out, and_25_out,
       and_26_out, and_27_out, and_28_out, and_29_out, and_30_out, and_31_out, and_32_out, and_33_out,
       and_34_out, and_35_out, and_36_out, and_37_out, and_38_out, and_39_out, and_40_out, and_41_out,
       and_42_out, and_43_out, and_44_out, and_45_out, and_46_out, and_47_out, and_48_out, and_49_out,
       and_50_out, and_51_out, and_52_out, and_53_out, not_1_out, not_2_out, not_3_out, not_4_out, not_5_out,
       not_6_out, not_7_out, not_8_out, not_9_out, not_10_out, not_11_out, not_12_out, not_13_out,
       not_14_out, not_15_out, not_16_out, not_17_out, not_18_out, not_19_out, not_20_out, not_21_out,
       not_22_out, not_23_out, not_24_out, not_25_out, not_26_out, not_27_out, not_28_out, not_29_out,
       not_30_out, not_31_out, not_32_out, not_33_out, not_34_out, not_35_out, not_36_out, not_37_out,
       not_38_out, not_39_out, not_40_out, not_41_out, not_42_out, not_43_out, not_44_out, not_45_out,
       not_46_out, not_47_out, not_48_out, not_49_out, not_50_out, not_51_out, not_52_out, not_53_out,
       not_54_out, not_55_out, not_56_out, not_57_out, not_58_out, not_59_out, not_60_out, not_61_out,
       not_62_out, not_63_out, not_64_out, not_65_out, not_66_out, not_67_out, not_68_out, not_69_out,
       not_70_out, not_71_out, not_72_out, not_73_out, not_74_out, not_75_out, not_76_out, not_77_out,
       not_78_out, not_79_out, not_80_out, not_81_out, not_82_out, not_83_out, not_84_out, not_85_out,
       not_86_out, not_87_out, not_88_out, not_89_out, not_90_out, not_91_out, not_92_out, not_93_out,
       not_94_out, not_95_out, not_96_out, not_97_out, not_98_out, not_99_out, not_100_out, not_101_out,
       not_102_out, not_103_out, not_104_out, not_105_out, not_106_out, not_107_out, not_108_out,
       not_109_out, not_110_out, not_111_out, not_112_out, not_113_out, not_114_out, not_115_out,
       not_116_out, not_117_out, not_118_out, not_119_out, not_120_out, not_121_out, not_122_out,
       not_123_out, not_124_out, not_125_out, not_126_out, not_127_out, not_128_out, not_129_out,
       not_130_out, not_131_out, not_132_out, not_133_out, not_134_out, not_135_out, not_136_out,
       not_137_out, not_138_out, not_139_out, not_140_out, not_141_out, not_142_out, not_143_out,
       not_144_out, not_145_out, not_146_out, not_147_out, not_148_out, not_149_out, not_150_out,
       not_151_out, not_152_out, not_153_out, not_154_out, not_155_out, not_156_out, not_157_out,
       not_158_out, not_159_out, not_160_out, not_161_out, not_162_out, not_163_out, not_164_out,
       not_165_out, not_166_out, not_167_out, not_168_out, not_169_out, not_170_out, not_171_out,
       not_172_out, not_173_out, not_174_out, not_175_out, not_176_out, not_177_out, not_178_out,
       not_179_out, not_180_out, not_181_out, not_182_out, or_1_out, or_2_out, or_3_out, or_4_out, or_5_out,
       or_6_out;

  not not_1 (not_1_out, funct[3]);
  not not_2 (not_2_out, funct[1]);
  not not_3 (not_3_out, funct[3]);
  not not_4 (not_4_out, funct[0]);
  not not_5 (not_5_out, funct[3]);
  not not_6 (not_6_out, funct[2]);
  not not_7 (not_7_out, funct[0]);
  not not_8 (not_8_out, funct[2]);
  not not_9 (not_9_out, funct[3]);
  not not_10 (not_10_out, funct[2]);
  not not_11 (not_11_out, funct[1]);
  not not_12 (not_12_out, funct[0]);
  not not_13 (not_13_out, funct[3]);
  not not_14 (not_14_out, funct[2]);
  not not_15 (not_15_out, funct[1]);
  not not_16 (not_16_out, funct[3]);
  not not_17 (not_17_out, funct[2]);
  not not_18 (not_18_out, funct[0]);
  not not_19 (not_19_out, funct[3]);
  not not_20 (not_20_out, funct[2]);
  not not_21 (not_21_out, funct[3]);
  not not_22 (not_22_out, funct[1]);
  not not_23 (not_23_out, funct[0]);
  not not_24 (not_24_out, funct[2]);
  not not_25 (not_25_out, funct[3]);
  not not_26 (not_26_out, funct[2]);
  not not_27 (not_27_out, funct[0]);
  not not_28 (not_28_out, funct[3]);
  not not_29 (not_29_out, funct[2]);
  not not_30 (not_30_out, funct[3]);
  not not_31 (not_31_out, funct[3]);
  not not_32 (not_32_out, funct[1]);
  not not_33 (not_33_out, funct[0]);
  not not_34 (not_34_out, funct[2]);
  not not_35 (not_35_out, funct[0]);
  not not_36 (not_36_out, funct[3]);
  not not_37 (not_37_out, funct[2]);
  not not_38 (not_38_out, funct[0]);
  not not_39 (not_39_out, funct[3]);
  not not_40 (not_40_out, funct[0]);
  not not_41 (not_41_out, funct[3]);
  not not_42 (not_42_out, funct[2]);
  not not_43 (not_43_out, funct[1]);
  not not_44 (not_44_out, funct[0]);
  not not_45 (not_45_out, funct[3]);
  not not_46 (not_46_out, funct[2]);
  not not_47 (not_47_out, funct[1]);
  not not_48 (not_48_out, funct[3]);
  not not_49 (not_49_out, funct[1]);
  not not_50 (not_50_out, funct[0]);
  not not_51 (not_51_out, funct[3]);
  not not_52 (not_52_out, funct[0]);
  not not_53 (not_53_out, funct[2]);
  not not_54 (not_54_out, funct[0]);
  not not_55 (not_55_out, funct[3]);
  not not_56 (not_56_out, funct[2]);
  not not_57 (not_57_out, funct[3]);
  and and_1 (and_1_out, not_1_out, funct[2], not_2_out, funct[0]);
  and and_2 (and_2_out, not_3_out, funct[2], funct[1], not_4_out);
  and and_3 (and_3_out, not_5_out, funct[2], funct[1], funct[0]);
  and and_4 (and_4_out, funct[3], not_6_out, funct[1], not_7_out);
  and and_5 (and_5_out, funct[3], not_8_out, funct[1], funct[0]);
  and and_6 (and_6_out, not_9_out, not_10_out, not_11_out, not_12_out);
  and and_7 (and_7_out, not_13_out, not_14_out, not_15_out, funct[0]);
  and and_8 (and_8_out, not_16_out, not_17_out, funct[1], not_18_out);
  and and_9 (and_9_out, not_19_out, not_20_out, funct[1], funct[0]);
  and and_10 (and_10_out, not_21_out, funct[2], not_22_out, not_23_out);
  and and_11 (and_11_out, funct[3], not_24_out, funct[1], funct[0]);
  and and_12 (and_12_out, not_25_out, not_26_out, funct[1], not_27_out);
  and and_13 (and_13_out, not_28_out, not_29_out, funct[1], funct[0]);
  and and_14 (and_14_out, not_30_out, funct[2], funct[1], funct[0]);
  and and_15 (and_15_out, not_31_out, funct[2], not_32_out, not_33_out);
  and and_16 (and_16_out, funct[3], not_34_out, funct[1], not_35_out);
  and and_17 (and_17_out, not_36_out, not_37_out, funct[1], not_38_out);
  and and_18 (and_18_out, not_39_out, funct[2], funct[1], not_40_out);
  and and_19 (and_19_out, not_41_out, not_42_out, not_43_out, not_44_out);
  and and_20 (and_20_out, not_45_out, not_46_out, not_47_out, funct[0]);
  and and_21 (and_21_out, not_48_out, funct[2], not_49_out, not_50_out);
  and and_22 (and_22_out, not_51_out, funct[2], funct[1], not_52_out);
  and and_23 (and_23_out, funct[3], not_53_out, funct[1], not_54_out);
  and and_24 (and_24_out, not_55_out, not_56_out, funct[1], funct[0]);
  and and_25 (and_25_out, not_57_out, funct[2], funct[1], funct[0]);
  not not_58 (not_58_out, op[5]);
  not not_59 (not_59_out, op[4]);
  not not_60 (not_60_out, op[3]);
  not not_61 (not_61_out, op[2]);
  not not_62 (not_62_out, op[1]);
  not not_63 (not_63_out, op[0]);
  not not_64 (not_64_out, funct[4]);
  or or_1 (or_1_out, and_1_out, and_2_out, and_3_out, and_4_out, and_5_out);
  not not_65 (not_65_out, op[5]);
  not not_66 (not_66_out, op[4]);
  not not_67 (not_67_out, op[1]);
  not not_68 (not_68_out, op[5]);
  not not_69 (not_69_out, op[4]);
  not not_70 (not_70_out, op[0]);
  not not_71 (not_71_out, op[5]);
  not not_72 (not_72_out, op[4]);
  not not_73 (not_73_out, op[2]);
  not not_74 (not_74_out, op[0]);
  not not_75 (not_75_out, op[5]);
  not not_76 (not_76_out, op[4]);
  not not_77 (not_77_out, op[2]);
  not not_78 (not_78_out, op[5]);
  not not_79 (not_79_out, op[4]);
  not not_80 (not_80_out, op[3]);
  not not_81 (not_81_out, op[0]);
  not not_82 (not_82_out, op[5]);
  not not_83 (not_83_out, op[4]);
  not not_84 (not_84_out, op[3]);
  not not_85 (not_85_out, op[2]);
  not not_86 (not_86_out, op[1]);
  not not_87 (not_87_out, op[0]);
  not not_88 (not_88_out, funct[4]);
  or or_2 (or_2_out, and_6_out, and_7_out, and_8_out, and_9_out, and_10_out, and_11_out);
  not not_89 (not_89_out, op[5]);
  not not_90 (not_90_out, op[4]);
  not not_91 (not_91_out, op[2]);
  not not_92 (not_92_out, op[1]);
  not not_93 (not_93_out, op[0]);
  not not_94 (not_94_out, op[5]);
  not not_95 (not_95_out, op[4]);
  not not_96 (not_96_out, op[2]);
  not not_97 (not_97_out, op[1]);
  not not_98 (not_98_out, op[5]);
  not not_99 (not_99_out, op[4]);
  not not_100 (not_100_out, op[1]);
  not not_101 (not_101_out, op[0]);
  not not_102 (not_102_out, op[5]);
  not not_103 (not_103_out, op[4]);
  not not_104 (not_104_out, op[2]);
  not not_105 (not_105_out, op[4]);
  not not_106 (not_106_out, op[3]);
  not not_107 (not_107_out, op[1]);
  not not_108 (not_108_out, op[0]);
  not not_109 (not_109_out, op[5]);
  not not_110 (not_110_out, op[4]);
  not not_111 (not_111_out, op[3]);
  not not_112 (not_112_out, op[2]);
  not not_113 (not_113_out, op[1]);
  not not_114 (not_114_out, op[0]);
  not not_115 (not_115_out, funct[4]);
  or or_3 (or_3_out, and_12_out, and_13_out, and_14_out, and_15_out, and_16_out);
  not not_116 (not_116_out, op[5]);
  not not_117 (not_117_out, op[4]);
  not not_118 (not_118_out, op[3]);
  not not_119 (not_119_out, op[2]);
  not not_120 (not_120_out, op[1]);
  not not_121 (not_121_out, op[0]);
  not not_122 (not_122_out, funct[5]);
  not not_123 (not_123_out, funct[4]);
  or or_4 (or_4_out, and_17_out, and_18_out);
  not not_124 (not_124_out, op[5]);
  not not_125 (not_125_out, op[4]);
  not not_126 (not_126_out, op[1]);
  not not_127 (not_127_out, op[0]);
  not not_128 (not_128_out, op[5]);
  not not_129 (not_129_out, op[4]);
  not not_130 (not_130_out, op[2]);
  not not_131 (not_131_out, op[0]);
  not not_132 (not_132_out, op[5]);
  not not_133 (not_133_out, op[4]);
  not not_134 (not_134_out, op[3]);
  not not_135 (not_135_out, op[0]);
  not not_136 (not_136_out, op[5]);
  not not_137 (not_137_out, op[4]);
  not not_138 (not_138_out, op[3]);
  not not_139 (not_139_out, op[2]);
  not not_140 (not_140_out, op[1]);
  not not_141 (not_141_out, op[0]);
  not not_142 (not_142_out, funct[4]);
  or or_5 (or_5_out, and_19_out, and_20_out, and_21_out, and_22_out, and_23_out);
  not not_143 (not_143_out, op[5]);
  not not_144 (not_144_out, op[4]);
  not not_145 (not_145_out, op[3]);
  not not_146 (not_146_out, op[2]);
  not not_147 (not_147_out, op[1]);
  not not_148 (not_148_out, op[0]);
  not not_149 (not_149_out, funct[5]);
  not not_150 (not_150_out, funct[4]);
  or or_6 (or_6_out, and_24_out, and_25_out);
  not not_151 (not_151_out, op[5]);
  not not_152 (not_152_out, op[4]);
  not not_153 (not_153_out, op[2]);
  not not_154 (not_154_out, op[1]);
  not not_155 (not_155_out, op[0]);
  not not_156 (not_156_out, op[5]);
  not not_157 (not_157_out, op[4]);
  not not_158 (not_158_out, op[2]);
  not not_159 (not_159_out, op[1]);
  not not_160 (not_160_out, op[5]);
  not not_161 (not_161_out, op[4]);
  not not_162 (not_162_out, op[1]);
  not not_163 (not_163_out, op[0]);
  not not_164 (not_164_out, op[5]);
  not not_165 (not_165_out, op[4]);
  not not_166 (not_166_out, op[0]);
  not not_167 (not_167_out, op[4]);
  not not_168 (not_168_out, op[2]);
  not not_169 (not_169_out, op[5]);
  not not_170 (not_170_out, op[4]);
  not not_171 (not_171_out, op[2]);
  not not_172 (not_172_out, op[0]);
  not not_173 (not_173_out, op[4]);
  not not_174 (not_174_out, op[3]);
  not not_175 (not_175_out, op[1]);
  not not_176 (not_176_out, op[0]);
  not not_177 (not_177_out, op[5]);
  not not_178 (not_178_out, op[4]);
  not not_179 (not_179_out, op[3]);
  not not_180 (not_180_out, op[0]);
  and and_26 (and_26_out, not_58_out, not_59_out, not_60_out, not_61_out, not_62_out, not_63_out, funct[5], not_64_out, or_1_out);
  and and_27 (and_27_out, not_65_out, not_66_out, op[3], op[2], not_67_out, op[0]);
  and and_28 (and_28_out, not_68_out, not_69_out, op[3], op[2], op[1], not_70_out);
  and and_29 (and_29_out, not_71_out, not_72_out, op[3], not_73_out, op[1], not_74_out);
  and and_30 (and_30_out, not_75_out, not_76_out, op[3], not_77_out, op[1], op[0]);
  and and_31 (and_31_out, not_78_out, not_79_out, not_80_out, op[2], op[1], not_81_out);
  not not_181 (not_181_out, op[4]);
  not not_182 (not_182_out, op[2]);
  and and_32 (and_32_out, not_109_out, not_110_out, not_111_out, not_112_out, not_113_out, not_114_out, funct[5], not_115_out, or_3_out);
  and and_33 (and_33_out, not_116_out, not_117_out, not_118_out, not_119_out, not_120_out, not_121_out, not_122_out, not_123_out, or_4_out);
  and and_34 (and_34_out, not_124_out, not_125_out, op[3], op[2], not_126_out, not_127_out);
  and and_35 (and_35_out, not_128_out, not_129_out, op[3], not_130_out, op[1], not_131_out);
  and and_36 (and_36_out, not_132_out, not_133_out, not_134_out, op[2], op[1], not_135_out);
  and and_37 (and_37_out, not_136_out, not_137_out, not_138_out, not_139_out, not_140_out, not_141_out, funct[5], not_142_out, or_5_out);
  and and_38 (and_38_out, not_143_out, not_144_out, not_145_out, not_146_out, not_147_out, not_148_out, not_149_out, not_150_out, or_6_out);
  and and_39 (and_39_out, not_151_out, not_152_out, op[3], not_153_out, not_154_out, not_155_out);
  and and_40 (and_40_out, not_156_out, not_157_out, op[3], not_158_out, not_159_out, op[0]);
  and and_41 (and_41_out, not_160_out, not_161_out, op[3], op[2], not_162_out, not_163_out);
  and and_42 (and_42_out, not_164_out, not_165_out, op[3], op[2], op[1], not_166_out);
  and and_43 (and_43_out, op[5], not_167_out, not_168_out, op[1], op[0]);
  and and_44 (and_44_out, not_169_out, not_170_out, op[3], not_171_out, op[1], not_172_out);
  and and_45 (and_45_out, op[5], not_173_out, not_174_out, op[2], not_175_out, not_176_out);
  and and_46 (and_46_out, not_177_out, not_178_out, not_179_out, op[2], op[1], not_180_out);
  and and_47 (and_47_out, not_82_out, not_83_out, not_84_out, not_85_out, not_86_out, not_87_out, funct[5], not_88_out, or_2_out);
  and and_48 (and_48_out, not_89_out, not_90_out, op[3], not_91_out, not_92_out, not_93_out);
  and and_49 (and_49_out, not_94_out, not_95_out, op[3], not_96_out, not_97_out, op[0]);
  and and_50 (and_50_out, not_98_out, not_99_out, op[3], op[2], not_100_out, not_101_out);
  and and_51 (and_51_out, op[5], not_181_out, not_182_out, op[1], op[0]);
  and and_52 (and_52_out, not_102_out, not_103_out, op[3], not_104_out, op[1], op[0]);
  and and_53 (and_53_out, op[5], not_105_out, not_106_out, op[2], not_107_out, not_108_out);
  or or_7 (out_3[1], and_32_out, and_33_out, and_34_out, and_35_out, and_36_out);
  or or_8 (out_3[3], and_26_out, and_27_out, and_28_out, and_29_out, and_30_out, and_31_out);
  or or_9 (out_3[2], and_47_out, and_48_out, and_49_out, and_50_out, and_51_out, and_52_out, and_53_out);
  or or_10 (out_3[0], and_37_out, and_38_out, and_39_out, and_40_out, and_41_out, and_42_out, and_43_out, and_44_out, and_45_out, and_46_out);

  // Other names for the same wires on the sheet: alu_op4 = out_3[0]; alu_op3 = out_3[1]; alu_op2 = out_3[2];
  //   alu_op1 = out_3[3]
endmodule

module r_slra (
  input  [4:0] op1,
  output r1
);

  wire not_1_out, not_2_out, not_3_out, not_4_out, not_5_out;

  not not_1 (not_1_out, op1[0]);
  not not_2 (not_2_out, op1[1]);
  not not_3 (not_3_out, op1[2]);
  not not_4 (not_4_out, op1[3]);
  not not_5 (not_5_out, op1[4]);
  and and_1 (r1, not_1_out, not_2_out, not_3_out, not_4_out, not_5_out);
endmodule

module R_TYPE (
  input  [5:0] op1,
  output IR_type
);

  wire not_1_out, not_2_out, not_3_out, not_4_out, not_5_out, not_6_out;

  not not_1 (not_1_out, op1[0]);
  not not_2 (not_2_out, op1[1]);
  not not_3 (not_3_out, op1[2]);
  not not_4 (not_4_out, op1[3]);
  not not_5 (not_5_out, op1[4]);
  not not_6 (not_6_out, op1[5]);
  and and_1 (IR_type, not_1_out, not_2_out, not_3_out, not_4_out, not_5_out, not_6_out);
endmodule

// R/ITYPE
module I_TYPE (
  input  [5:0] op1,
  output IR_type
);

  or or_1 (IR_type, op1[5], op1[4], op1[3], op1[2], op1[1], op1[0]);
endmodule

module LW (
  input  [5:0] op1,
  output LW
);

  wire and_1_out, and_2_out, not_1_out, not_2_out, not_3_out, not_4_out, not_5_out, not_6_out, not_7_out;

  not not_1 (not_1_out, op1[4]);
  not not_2 (not_2_out, op1[3]);
  not not_3 (not_3_out, op1[2]);
  not not_4 (not_4_out, op1[4]);
  not not_5 (not_5_out, op1[3]);
  not not_6 (not_6_out, op1[1]);
  not not_7 (not_7_out, op1[0]);
  and and_1 (and_1_out, op1[5], not_1_out, not_2_out, not_3_out, op1[1], op1[0]);
  and and_2 (and_2_out, op1[5], not_4_out, not_5_out, op1[2], not_6_out, not_7_out);
  or or_1 (LW, and_1_out, and_2_out);
endmodule

module SW (
  input  [5:0] op1,
  output SW
);

  wire not_1_out, not_2_out;

  not not_1 (not_1_out, op1[4]);
  not not_2 (not_2_out, op1[2]);
  and and_1 (SW, op1[5], not_1_out, op1[3], not_2_out, op1[1], op1[0]);
endmodule

module BEQ (
  input  [5:0] op1,
  output BEQ
);

  wire not_1_out, not_2_out, not_3_out, not_4_out, not_5_out;

  not not_1 (not_1_out, op1[5]);
  not not_2 (not_2_out, op1[4]);
  not not_3 (not_3_out, op1[3]);
  not not_4 (not_4_out, op1[1]);
  not not_5 (not_5_out, op1[0]);
  and and_1 (BEQ, not_1_out, not_2_out, not_3_out, op1[2], not_4_out, not_5_out);
endmodule

module BNE (
  input  [5:0] op1,
  output BEQ
);

  wire not_1_out, not_2_out, not_3_out, not_4_out;

  not not_1 (not_1_out, op1[5]);
  not not_2 (not_2_out, op1[4]);
  not not_3 (not_3_out, op1[3]);
  not not_4 (not_4_out, op1[1]);
  and and_1 (BEQ, not_1_out, not_2_out, not_3_out, op1[2], not_4_out, op1[0]);
endmodule

module R_SLRA (
  input  [5:0] op,
  input  [5:0] func,
  output r_slra
);

  wire and_1_out, and_2_out, and_3_out, not_1_out, not_2_out, not_3_out, not_4_out, not_5_out, not_6_out,
       not_7_out, not_8_out, not_9_out, not_10_out, not_11_out, not_12_out, not_13_out, or_1_out;

  not not_1 (not_1_out, func[1]);
  not not_2 (not_2_out, func[0]);
  not not_3 (not_3_out, func[0]);
  and and_1 (and_1_out, not_1_out, not_2_out);
  and and_2 (and_2_out, func[1], not_3_out);
  and and_3 (and_3_out, func[1], func[0]);
  not not_4 (not_4_out, op[5]);
  not not_5 (not_5_out, op[4]);
  not not_6 (not_6_out, op[3]);
  not not_7 (not_7_out, op[2]);
  not not_8 (not_8_out, op[1]);
  not not_9 (not_9_out, op[0]);
  not not_10 (not_10_out, func[5]);
  not not_11 (not_11_out, func[4]);
  not not_12 (not_12_out, func[3]);
  not not_13 (not_13_out, func[2]);
  or or_1 (or_1_out, and_1_out, and_2_out, and_3_out);
  and and_4 (r_slra, not_4_out, not_5_out, not_6_out, not_7_out, not_8_out, not_9_out, not_10_out, not_11_out, not_12_out, not_13_out, or_1_out);
endmodule

module JL (
  input  [5:0] op,
  output JL
);

  wire not_1_out, not_2_out, not_3_out, not_4_out, not_5_out;

  not not_1 (not_1_out, op[5]);
  not not_2 (not_2_out, op[4]);
  not not_3 (not_3_out, op[3]);
  not not_4 (not_4_out, op[2]);
  not not_5 (not_5_out, op[0]);
  and and_1 (JL, not_1_out, not_2_out, not_3_out, not_4_out, op[1], not_5_out);
endmodule

module WE (
  input  sw,
  input  beq,
  input  bne,
  input  jl,
  input  jr,
  input  blez,
  output we
);

  nor nor_1 (we, sw, beq, bne, jl, jr, blez);
endmodule

// SYS_B
module Syscall_b (
  input  [5:0] op,
  input  [5:0] funct,
  output syscall
);

  wire not_1_out, not_2_out, not_3_out, not_4_out, not_5_out, not_6_out, not_7_out, not_8_out, not_9_out,
       not_10_out;

  not not_1 (not_1_out, op[5]);
  not not_2 (not_2_out, op[4]);
  not not_3 (not_3_out, op[3]);
  not not_4 (not_4_out, op[2]);
  not not_5 (not_5_out, op[1]);
  not not_6 (not_6_out, op[0]);
  not not_7 (not_7_out, funct[5]);
  not not_8 (not_8_out, funct[4]);
  not not_9 (not_9_out, funct[1]);
  not not_10 (not_10_out, funct[0]);
  and and_1 (syscall, not_1_out, not_2_out, not_3_out, not_4_out, not_5_out, not_6_out, not_7_out, not_8_out, funct[3], funct[2], not_9_out, not_10_out);
endmodule

module JAL (
  input  [5:0] op,
  output JAL
);

  wire not_1_out, not_2_out, not_3_out, not_4_out;

  not not_1 (not_1_out, op[5]);
  not not_2 (not_2_out, op[4]);
  not not_3 (not_3_out, op[3]);
  not not_4 (not_4_out, op[2]);
  and and_1 (JAL, not_1_out, not_2_out, not_3_out, not_4_out, op[1], op[0]);
endmodule

module JR (
  input  [5:0] op,
  input  [5:0] func,
  output JR
);

  wire not_1_out, not_2_out, not_3_out, not_4_out, not_5_out, not_6_out, not_7_out, not_8_out, not_9_out,
       not_10_out, not_11_out;

  not not_1 (not_1_out, op[5]);
  not not_2 (not_2_out, op[4]);
  not not_3 (not_3_out, op[3]);
  not not_4 (not_4_out, op[2]);
  not not_5 (not_5_out, op[1]);
  not not_6 (not_6_out, op[0]);
  not not_7 (not_7_out, func[5]);
  not not_8 (not_8_out, func[4]);
  not not_9 (not_9_out, func[2]);
  not not_10 (not_10_out, func[1]);
  not not_11 (not_11_out, func[0]);
  and and_1 (JR, not_1_out, not_2_out, not_3_out, not_4_out, not_5_out, not_6_out, not_7_out, not_8_out, func[3], not_9_out, not_10_out, not_11_out);
endmodule

// zeroext
module zero_extend (
  input  [5:0] op1,
  output zero_ext
);

  wire and_1_out, and_2_out, and_3_out, and_4_out, and_5_out, not_1_out, not_2_out, not_3_out, not_4_out,
       not_5_out, not_6_out, not_7_out, not_8_out, not_9_out, or_1_out;

  not not_1 (not_1_out, op1[2]);
  not not_2 (not_2_out, op1[1]);
  not not_3 (not_3_out, op1[1]);
  not not_4 (not_4_out, op1[0]);
  not not_5 (not_5_out, op1[1]);
  not not_6 (not_6_out, op1[0]);
  not not_7 (not_7_out, op1[2]);
  and and_1 (and_1_out, not_1_out, not_2_out, op1[0]);
  and and_2 (and_2_out, op1[2], not_3_out, not_4_out);
  and and_3 (and_3_out, op1[2], not_5_out, op1[0]);
  and and_4 (and_4_out, op1[2], op1[1], not_6_out);
  and and_5 (and_5_out, not_7_out, op1[1], op1[0]);
  not not_8 (not_8_out, op1[5]);
  not not_9 (not_9_out, op1[4]);
  or or_1 (or_1_out, and_1_out, and_2_out, and_3_out, and_4_out, and_5_out);
  and and_6 (zero_ext, not_8_out, not_9_out, op1[3], or_1_out);
endmodule

module LUI (
  input  [5:0] op1,
  output LUI
);

  wire not_1_out, not_2_out;

  not not_1 (not_1_out, op1[5]);
  not not_2 (not_2_out, op1[4]);
  and and_1 (LUI, not_1_out, not_2_out, op1[3], op1[2], op1[1], op1[0]);
endmodule

module BLEZ (
  input  [5:0] op1,
  output BLEZ
);

  wire not_1_out, not_2_out, not_3_out, not_4_out;

  not not_1 (not_1_out, op1[5]);
  not not_2 (not_2_out, op1[4]);
  not not_3 (not_3_out, op1[3]);
  not not_4 (not_4_out, op1[0]);
  and and_1 (BLEZ, not_1_out, not_2_out, not_3_out, op1[2], op1[1], not_4_out);
endmodule

module LBU (
  input  [5:0] op1,
  output LUI
);

  wire not_1_out, not_2_out, not_3_out, not_4_out;

  not not_1 (not_1_out, op1[4]);
  not not_2 (not_2_out, op1[3]);
  not not_3 (not_3_out, op1[1]);
  not not_4 (not_4_out, op1[0]);
  and and_1 (LUI, op1[5], not_1_out, not_2_out, op1[2], not_3_out, not_4_out);
endmodule

module inresp (
  input  _1,
  input  _2,
  input  IE,
  input  _3,
  input  [2:0] code,
  input  clk,
  output [1:0] out_7,
  output out_8
);

  wire _1_t, _2_t, _3_t, and_1_out, and_2_out, and_3_out, d_ff_1_q, d_ff_3_q, d_ff_5_q, demultiplexer_1_out1,
       demultiplexer_1_out2, demultiplexer_1_out3, multiplexer_1_out, multiplexer_2_out, multiplexer_3_out,
       priority_encoder_1_gs, register_1_q, register_2_q, register_3_q, register_4_q, signal1, signal2,
       signal3;
  wire [1:0] num_choose;

  D_Flip_Flop d_ff_1 (.clk(_1), .D(1'b1), .Q(d_ff_1_q), .reset(signal1));  // open: Qn, preset, en
  Multiplexer #(.enable("false")) multiplexer_1 (.in0(d_ff_1_q), .in1(1'b0), .out(multiplexer_1_out), .sel(signal1));
  D_Flip_Flop d_ff_2 (.clk(clk), .D(multiplexer_1_out), .Q(_1_t));  // open: Qn, preset, en, reset
  D_Flip_Flop d_ff_3 (.clk(_2), .D(1'b1), .Q(d_ff_3_q), .reset(signal2));  // open: Qn, preset, en
  Multiplexer #(.enable("false")) multiplexer_2 (.in0(d_ff_3_q), .in1(1'b0), .out(multiplexer_2_out), .sel(signal2));
  D_Flip_Flop d_ff_4 (.clk(clk), .D(multiplexer_2_out), .Q(_2_t));  // open: Qn, preset, en, reset
  D_Flip_Flop d_ff_5 (.clk(_3), .D(1'b1), .Q(d_ff_5_q), .reset(signal3));  // open: Qn, preset, en
  Multiplexer #(.enable("false")) multiplexer_3 (.in0(d_ff_5_q), .in1(1'b0), .out(multiplexer_3_out), .sel(signal3));
  D_Flip_Flop d_ff_6 (.clk(clk), .D(multiplexer_3_out), .Q(_3_t));  // open: Qn, preset, en, reset
  Register #(.width(1)) register_1 (.D(code[0]), .Q(register_1_q), .clk(clk));  // open: en, clr
  Register #(.width(1)) register_2 (.D(code[1]), .Q(register_2_q), .clk(clk));  // open: en, clr
  Register #(.width(1)) register_3 (.D(code[2]), .Q(register_3_q), .clk(clk));  // open: en, clr
  and and_1 (and_1_out, _1_t, ~register_1_q);  // AND_Gate
  and and_2 (and_2_out, _2_t, ~register_2_q);  // AND_Gate
  and and_3 (and_3_out, _3_t, ~register_3_q);  // AND_Gate
  Priority_Encoder #(.select(2)) priority_encoder_1 (
    .in0(1'b0), .in1(and_1_out), .in2(and_2_out), .in3(and_3_out), .out(out_7), .gs(priority_encoder_1_gs),
    .en_in(1'b1));  // open: en_out
  Register #(.width(1)) register_4 (.D(IE), .Q(register_4_q), .clk(clk));  // open: en, clr
  Register #(.width(2)) register_5 (.D(out_7), .Q(num_choose), .clk(priority_encoder_1_gs));  // open: en, clr
  and and_4 (out_8, priority_encoder_1_gs, register_4_q);
  Demultiplexer #(.select(2), .enable("false")) demultiplexer_1 (
    .out1(demultiplexer_1_out1), .out2(demultiplexer_1_out2), .out3(demultiplexer_1_out3), .in(out_8),
    .sel(num_choose));  // open: out0
  and and_5 (signal1, demultiplexer_1_out1, _1_t);
  and and_6 (signal2, demultiplexer_1_out2, _2_t);
  and and_7 (signal3, demultiplexer_1_out3, _3_t);

  // Other names for the same wires on the sheet: num[1:0] = out_7
endmodule

// INTP
module INTRUPT (
  input  [5:0] op1,
  output INTRRUPT
);

  wire not_1_out, not_2_out, not_3_out, not_4_out, not_5_out;

  not not_1 (not_1_out, op1[5]);
  not not_2 (not_2_out, op1[3]);
  not not_3 (not_3_out, op1[2]);
  not not_4 (not_4_out, op1[1]);
  not not_5 (not_5_out, op1[0]);
  and and_1 (INTRRUPT, not_1_out, op1[4], not_2_out, not_3_out, not_4_out, not_5_out);
endmodule

// MFC0
module mfc0 (
  input  [5:0] op1,
  input  [4:0] mfc0in,
  output MFC0
);

  wire intrupt_1_intrrupt, not_1_out, not_2_out, not_3_out, not_4_out, not_5_out;

  INTRUPT intrupt_1 (.op1(op1), .INTRRUPT(intrupt_1_intrrupt));
  not not_1 (not_1_out, mfc0in[4]);
  not not_2 (not_2_out, mfc0in[3]);
  not not_3 (not_3_out, mfc0in[2]);
  not not_4 (not_4_out, mfc0in[1]);
  not not_5 (not_5_out, mfc0in[0]);
  and and_1 (MFC0, intrupt_1_intrrupt, not_1_out, not_2_out, not_3_out, not_4_out, not_5_out);
endmodule

// MTC0
module mtc0 (
  input  [5:0] op1,
  input  [4:0] mfc0in,
  output MFC0
);

  wire intrupt_1_intrrupt, not_1_out, not_2_out, not_3_out, not_4_out;

  INTRUPT intrupt_1 (.op1(op1), .INTRRUPT(intrupt_1_intrrupt));
  not not_1 (not_1_out, mfc0in[4]);
  not not_2 (not_2_out, mfc0in[3]);
  not not_3 (not_3_out, mfc0in[1]);
  not not_4 (not_4_out, mfc0in[0]);
  and and_1 (MFC0, intrupt_1_intrrupt, not_1_out, not_2_out, mfc0in[2], not_3_out, not_4_out);
endmodule

module CP0 (
  input  [31:0] PCin,
  input  [31:0] DTin,
  input  cp0we,
  input  [4:0] c1,
  input  clk,
  input  [4:0] c2,
  input  _1,
  input  _2,
  input  _3,
  output [31:0] EPCout,
  output [31:0] out,
  output out_12
);

  wire _1_t, _2_t, _3_t, and_1_out, and_2_out, and_3_out, d_ff_1_q, d_ff_3_q, d_ff_5_q,
       demultiplexer_1_out12, demultiplexer_1_out14, demultiplexer_2_out1, demultiplexer_2_out2,
       demultiplexer_2_out3, multiplexer_1_out, multiplexer_2_out, multiplexer_3_out, not_1_out, not_2_out,
       or_1_out, priority_encoder_1_gs, register_1_q, register_2_q, register_3_q, register_4_q, signal1,
       signal2, signal3;
  wire [1:0] CR, priority_encoder_1_out;
  wire [31:0] bit_extender_1_out, CAUSE_q, multiplexer_5_out, SR;

  D_Flip_Flop d_ff_1 (.clk(_1), .D(1'b1), .Q(d_ff_1_q), .reset(signal1));  // open: Qn, preset, en
  Multiplexer #(.enable("false")) multiplexer_1 (.in0(d_ff_1_q), .in1(1'b0), .out(multiplexer_1_out), .sel(signal1));
  D_Flip_Flop d_ff_2 (.clk(clk), .D(multiplexer_1_out), .Q(_1_t));  // open: Qn, preset, en, reset
  D_Flip_Flop d_ff_3 (.clk(_2), .D(1'b1), .Q(d_ff_3_q), .reset(signal2));  // open: Qn, preset, en
  Multiplexer #(.enable("false")) multiplexer_2 (.in0(d_ff_3_q), .in1(1'b0), .out(multiplexer_2_out), .sel(signal2));
  D_Flip_Flop d_ff_4 (.clk(clk), .D(multiplexer_2_out), .Q(_2_t));  // open: Qn, preset, en, reset
  D_Flip_Flop d_ff_5 (.clk(_3), .D(1'b1), .Q(d_ff_5_q), .reset(signal3));  // open: Qn, preset, en
  Multiplexer #(.enable("false")) multiplexer_3 (.in0(d_ff_5_q), .in1(1'b0), .out(multiplexer_3_out), .sel(signal3));
  D_Flip_Flop d_ff_6 (.clk(clk), .D(multiplexer_3_out), .Q(_3_t));  // open: Qn, preset, en, reset
  Register #(.width(1)) register_1 (.D(SR[1]), .Q(register_1_q), .clk(clk));  // open: en, clr
  Register #(.width(1)) register_2 (.D(SR[2]), .Q(register_2_q), .clk(clk));  // open: en, clr
  Register #(.width(1)) register_3 (.D(SR[3]), .Q(register_3_q), .clk(clk));  // open: en, clr
  and and_1 (and_1_out, _1_t, ~register_1_q);  // AND_Gate
  and and_2 (and_2_out, _2_t, ~register_2_q);  // AND_Gate
  and and_3 (and_3_out, _3_t, ~register_3_q);  // AND_Gate
  Multiplexer #(.width(2), .enable("false")) multiplexer_4 (
    .in0(2'b00), .in1(priority_encoder_1_out), .out(CR), .sel(out_12));
  Priority_Encoder #(.select(2)) priority_encoder_1 (
    .in0(1'b0), .in1(and_1_out), .in2(and_2_out), .in3(and_3_out), .out(priority_encoder_1_out),
    .gs(priority_encoder_1_gs), .en_in(1'b1));  // open: en_out
  not not_1 (not_1_out, SR[0]);
  Demultiplexer #(.select(5), .enable("false")) demultiplexer_1 (
    .out12(demultiplexer_1_out12), .out14(demultiplexer_1_out14), .in(cp0we), .sel(c1));  // open: out0, out1, out2, out3, out4, out5, out6, out7, out8, out9, out10, out11, out13, out15, out16, out17, out18, out19, out20, out21, out22, out23, out24, out25, out26, out27, out28, out29, out30, out31
  Register #(.width(1)) register_4 (.D(not_1_out), .Q(register_4_q), .clk(clk));  // open: en, clr
  not not_2 (not_2_out, out_12);
  assign bit_extender_1_out = {{30{1'b0}}, priority_encoder_1_out};  // Bit_Extender bit_extender_1
  and and_4 (out_12, priority_encoder_1_gs, register_4_q);
  Demultiplexer #(.select(2), .enable("false")) demultiplexer_2 (
    .out1(demultiplexer_2_out1), .out2(demultiplexer_2_out2), .out3(demultiplexer_2_out3), .in(out_12),
    .sel(CR));  // open: out0
  Multiplexer #(.width(32), .enable("false")) multiplexer_5 (
    .in0(PCin), .in1(DTin), .out(multiplexer_5_out), .sel(not_2_out));
  or or_1 (or_1_out, out_12, demultiplexer_1_out14);
  // Probe on DTin
  Register #(.width(32)) EPC (.D(multiplexer_5_out), .en(or_1_out), .Q(EPCout), .clk(clk));  // open: clr
  Register #(.width(32)) u_SR (.D(DTin), .en(demultiplexer_1_out12), .Q(SR), .clk(clk));  // open: clr
  Register #(.width(32)) CAUSE (.D(bit_extender_1_out), .Q(CAUSE_q), .clk(clk));  // open: en, clr
  and and_5 (signal1, demultiplexer_2_out1, _1_t);
  and and_6 (signal2, demultiplexer_2_out2, _2_t);
  and and_7 (signal3, demultiplexer_2_out3, _3_t);
  Multiplexer #(.select(5), .width(32), .enable("false")) multiplexer_6 (
    .in12(SR), .in13(CAUSE_q), .in14(EPCout), .out(out), .sel(c2));  // open: in0, in1, in2, in3, in4, in5, in6, in7, in8, in9, in10, in11, in15, in16, in17, in18, in19, in20, in21, in22, in23, in24, in25, in26, in27, in28, in29, in30, in31

  // Other names for the same wires on the sheet: IR = out_12
endmodule

// ERET
module eret (
  input  [5:0] op1,
  input  [5:0] eretin,
  output ERET
);

  wire intrupt_1_intrrupt, not_1_out, not_2_out, not_3_out, not_4_out;

  INTRUPT intrupt_1 (.op1(op1), .INTRRUPT(intrupt_1_intrrupt));
  not not_1 (not_1_out, eretin[5]);
  not not_2 (not_2_out, eretin[2]);
  not not_3 (not_3_out, eretin[1]);
  not not_4 (not_4_out, eretin[0]);
  and and_1 (ERET, intrupt_1_intrrupt, not_1_out, eretin[4], eretin[3], not_2_out, not_3_out, not_4_out);
endmodule

// CENTER_CONTROL
module CONTRAL (
  input  [5:0] _26_31,
  input  [5:0] _0_5,
  output ZERO_EXT,
  output I_TYPE,
  output LW,
  output SW,
  output BEQ,
  output BNE,
  output JL,
  output JR,
  output BLEZ,
  output WE,
  output JAL,
  output LUI,
  output LBU,
  output SYS_B,
  output [3:0] ALU_SOURCE,
  output SLRA
);

  R_SLRA r_slra_1 (.op(_26_31), .func(_0_5), .r_slra(SLRA));
  zero_extend zero_extend_1 (.op1(_26_31), .zero_ext(ZERO_EXT));
  I_TYPE i_type_1 (.op1(_26_31), .IR_type(I_TYPE));
  LW lw_1 (.op1(_26_31), .LW(LW));
  SW sw_1 (.op1(_26_31), .SW(SW));
  BEQ beq_1 (.op1(_26_31), .BEQ(BEQ));
  BNE bne_1 (.op1(_26_31), .BEQ(BNE));
  JL jl_1 (.op(_26_31), .JL(JL));
  JR jr_1 (.op(_26_31), .func(_0_5), .JR(JR));
  BLEZ blez_1 (.op1(_26_31), .BLEZ(BLEZ));
  JAL jal_1 (.op(_26_31), .JAL(JAL));
  LUI lui_1 (.op1(_26_31), .LUI(LUI));
  LBU lbu_1 (.op1(_26_31), .LUI(LBU));
  Syscall_b syscall_b_1 (.op(_26_31), .funct(_0_5), .syscall(SYS_B));
  ALU_T alu_t_1 (.op(_26_31), .out_3(ALU_SOURCE), .funct(_0_5));
  WE we_1 (.sw(SW), .beq(BEQ), .bne(BNE), .jl(JL), .jr(JR), .blez(BLEZ), .we(WE));
endmodule

module IF_ID (
  input  [31:0] PC_4,
  input  [31:0] INSTRUCTION,
  input  [31:0] PC_ID,
  input  CLK,
  input  CLEAR,
  input  STOP,
  output [4:0] RW_num,
  output I_TYPE,
  output LW,
  output SW,
  output BEQ,
  output BNE,
  output JL,
  output JR,
  output BLEZ,
  output WE,
  output JAL,
  output LUI,
  output LBU,
  output SYS_B,
  output [3:0] ALU_SOURCE,
  output SLRA,
  output [4:0] R1_num,
  output [4:0] R2_num,
  output MFC0,
  output MTC0,
  output [31:0] shamt,
  output [31:0] immediate,
  output [31:0] JUMP_ADDR,
  output ERET,
  output [4:0] RD,
  output [31:0] PC_id_out,
  output [31:0] NEW_PC2
);

  wire contral_1_i_type, contral_1_we, ZERO_EXT;
  wire [4:0] multiplexer_2_out;
  wire [25:0] shifter_1_out;
  wire [31:0] bit_extender_3_out, bit_extender_4_out, register_2_q;

  // Probe on INSTRUCTION
  Register #(.width(32)) register_1 (.D(PC_4), .en(STOP), .Q(NEW_PC2), .clk(CLK), .clr(CLEAR));
  Register #(.width(32)) register_2 (
    .D(INSTRUCTION), .en(STOP), .Q({register_2_q[31:26], R1_num, R2_num, RD, register_2_q[10:0]}), .clk(CLK),
    .clr(CLEAR));
  Register #(.width(32)) register_3 (.D(PC_ID), .Q(PC_id_out), .clk(CLK));  // open: en, clr
  Shifter #(.width(26)) shifter_1 (
    .in({R1_num, R2_num, RD, register_2_q[10:0]}), .\dist (5'b00010), .out(shifter_1_out));
  assign JUMP_ADDR = {{6{1'b0}}, shifter_1_out};  // Bit_Extender bit_extender_1
  CONTRAL contral_1 (
    ._26_31(register_2_q[31:26]), ._0_5(register_2_q[5:0]), .ZERO_EXT(ZERO_EXT), .I_TYPE(contral_1_i_type),
    .LW(LW), .SW(SW), .BEQ(BEQ), .BNE(BNE), .JL(JL), .JR(JR), .BLEZ(BLEZ), .WE(contral_1_we), .JAL(JAL),
    .LUI(LUI), .LBU(LBU), .SYS_B(SYS_B), .ALU_SOURCE(ALU_SOURCE), .SLRA(SLRA));
  mfc0 mfc0_1 (.op1(register_2_q[31:26]), .mfc0in(R1_num), .MFC0(MFC0));
  mtc0 mtc0_1 (.op1(register_2_q[31:26]), .mfc0in(R1_num), .MFC0(MTC0));
  eret eret_1 (.op1(register_2_q[31:26]), .eretin(register_2_q[5:0]), .ERET(ERET));
  assign shamt = {{27{1'b0}}, register_2_q[10:6]};  // Bit_Extender bit_extender_2
  assign bit_extender_3_out = {{16{RD[4]}}, {RD, register_2_q[10:0]}};  // Bit_Extender bit_extender_3
  assign bit_extender_4_out = {{16{1'b0}}, {RD, register_2_q[10:0]}};  // Bit_Extender bit_extender_4
  Multiplexer #(.width(32), .enable("false")) multiplexer_1 (
    .in0(bit_extender_3_out), .in1(bit_extender_4_out), .out(immediate), .sel(ZERO_EXT));
  and and_1 (I_TYPE, contral_1_i_type, ~MTC0);  // AND_Gate
  Multiplexer #(.width(5), .enable("false")) multiplexer_2 (
    .in0(RD), .in1(R2_num), .out(multiplexer_2_out), .sel(I_TYPE));
  // Probe on R1_num
  // Probe on R2_num
  Multiplexer #(.width(5), .enable("false")) multiplexer_3 (
    .in0(multiplexer_2_out), .in1({5{1'b1}}), .out(RW_num), .sel(JAL));
  and and_2 (WE, contral_1_we, ~MTC0);  // AND_Gate

  // Other names for the same wires on the sheet: INSTRUCTION1[31:0] = INSTRUCTION; NEW_PC1[31:0] = PC_4;
  //   SYSCALL = SYS_B
endmodule

module ID_EX (
  input  [4:0] RW_num,
  input  I_TYPE,
  input  LW,
  input  SW,
  input  BEQ,
  input  BNE,
  input  JL,
  input  JR,
  input  BLEZ,
  input  WE,
  input  JAL,
  input  LUI,
  input  LBU,
  input  SYS_B,
  input  [3:0] ALU_SOURCE,
  input  SLRA,
  input  [31:0] R1_num,
  input  [31:0] R2_num,
  input  [4:0] RSin,
  input  [4:0] RTin,
  input  [31:0] JUMP_ADDR,
  input  [31:0] PC,
  input  [31:0] shamt,
  input  [31:0] immediate,
  input  CLK,
  input  mtc0_exin,
  input  eret_exin,
  input  CLEAR,
  input  [4:0] rd_exin,
  input  mfc0_id,
  output [4:0] RW_num_2,
  output I_TYPE_2,
  output LW_2,
  output SW_2,
  output BEQ_2,
  output BNE_2,
  output JL_2,
  output JR_2,
  output BLEZ_2,
  output WE_2,
  output JAL_2,
  output LUI_2,
  output LBU_2,
  output SYS_B_2,
  output [3:0] ALU_SOURCE_2,
  output SLRA_2,
  output [31:0] R1_num_2,
  output [31:0] R2_num_2,
  output [4:0] RS_num,
  output [4:0] RT_num,
  output [31:0] shamt_2,
  output [31:0] immediate_2,
  output [31:0] JUMP_ADDR_2,
  output [31:0] PC_2,
  output mfc0_ex_in,
  output mtc0_exout,
  output eret_ex_out,
  output [4:0] rd_exout
);

  Register #(.width(32)) register_1 (.D(PC), .Q(PC_2), .clk(CLK), .clr(CLEAR));  // open: en
  Register #(.width(32)) register_2 (.D(R1_num), .Q(R1_num_2), .clk(CLK), .clr(CLEAR));  // open: en
  Register #(.width(32)) register_3 (.D(R2_num), .Q(R2_num_2), .clk(CLK), .clr(CLEAR));  // open: en
  Register #(.width(32)) register_4 (.D(shamt), .Q(shamt_2), .clk(CLK), .clr(CLEAR));  // open: en
  Register #(.width(32)) register_5 (.D(immediate), .Q(immediate_2), .clk(CLK), .clr(CLEAR));  // open: en
  Register #(.width(32)) register_6 (.D(JUMP_ADDR), .Q(JUMP_ADDR_2), .clk(CLK), .clr(CLEAR));  // open: en
  Register #(.width(1)) register_7 (.D(SLRA), .Q(SLRA_2), .clk(CLK), .clr(CLEAR));  // open: en
  Register #(.width(4)) register_8 (.D(ALU_SOURCE), .Q(ALU_SOURCE_2), .clk(CLK), .clr(CLEAR));  // open: en
  Register #(.width(1)) register_9 (.D(SYS_B), .Q(SYS_B_2), .clk(CLK), .clr(CLEAR));  // open: en
  Register #(.width(1)) register_10 (.D(LBU), .Q(LBU_2), .clk(CLK), .clr(CLEAR));  // open: en
  Register #(.width(1)) register_11 (.D(LUI), .Q(LUI_2), .clk(CLK), .clr(CLEAR));  // open: en
  Register #(.width(1)) register_12 (.D(JAL), .Q(JAL_2), .clk(CLK), .clr(CLEAR));  // open: en
  Register #(.width(1)) register_13 (.D(WE), .Q(WE_2), .clk(CLK), .clr(CLEAR));  // open: en
  Register #(.width(1)) register_14 (.D(BLEZ), .Q(BLEZ_2), .clk(CLK), .clr(CLEAR));  // open: en
  Register #(.width(1)) register_15 (.D(JR), .Q(JR_2), .clk(CLK), .clr(CLEAR));  // open: en
  Register #(.width(1)) register_16 (.D(JL), .Q(JL_2), .clk(CLK), .clr(CLEAR));  // open: en
  Register #(.width(1)) register_17 (.D(BNE), .Q(BNE_2), .clk(CLK), .clr(CLEAR));  // open: en
  Register #(.width(1)) register_18 (.D(SW), .Q(SW_2), .clk(CLK), .clr(CLEAR));  // open: en
  Register #(.width(1)) register_19 (.D(LW), .Q(LW_2), .clk(CLK), .clr(CLEAR));  // open: en
  Register #(.width(1)) register_20 (.D(mfc0_id), .Q(mfc0_ex_in), .clk(CLK), .clr(CLEAR));  // open: en
  Register #(.width(1)) register_21 (.D(I_TYPE), .Q(I_TYPE_2), .clk(CLK), .clr(CLEAR));  // open: en
  Register #(.width(5)) register_22 (.D(RW_num), .Q(RW_num_2), .clk(CLK), .clr(CLEAR));  // open: en
  Register #(.width(1)) register_23 (.D(BEQ), .Q(BEQ_2), .clk(CLK), .clr(CLEAR));  // open: en
  Register #(.width(5)) u_RSin (.D(RSin), .Q(RS_num), .clk(CLK), .clr(CLEAR));  // open: en
  Register #(.width(5)) register_24 (.D(RTin), .Q(RT_num), .clk(CLK), .clr(CLEAR));  // open: en
  Register #(.width(1)) register_25 (.D(mtc0_exin), .Q(mtc0_exout), .clk(CLK), .clr(CLEAR));  // open: en
  Register #(.width(1)) register_26 (.D(eret_exin), .Q(eret_ex_out), .clk(CLK), .clr(CLEAR));  // open: en
  Register #(.width(5)) register_27 (.D(rd_exin), .Q(rd_exout), .clk(CLK), .clr(CLEAR));  // open: en

  // Other names for the same wires on the sheet: ALU_SOURCE_t[3:0] = ALU_SOURCE_2; ALU_SOURCEin[3:0] = ALU_SOURCE;
  //   BEQ_t = BEQ_2; BEQin = BEQ; BLEZ_t = BLEZ_2; BLEZin = BLEZ; BNE_t = BNE_2; BNEin = BNE; I_TYPE_t = I_TYPE_2;
  //   I_TYPEin = I_TYPE; immediate_t[31:0] = immediate_2; immediatein[31:0] = immediate; JAL_t = JAL_2; JALin = JAL;
  //   JL_t = JL_2; JLin = JL; JR_t = JR_2; JRin = JR; JUMP_ADDR_t[31:0] = JUMP_ADDR_2; JUMP_ADDRin[31:0] = JUMP_ADDR;
  //   LBU_t = LBU_2; LBUin = LBU; LUI_t = LUI_2; LUIin = LUI; LW_t = LW_2; LWin = LW; PC_t[31:0] = PC_2;
  //   PCin[31:0] = PC; R1_in[31:0] = R1_num; R1_num_t[31:0] = R1_num_2; R2_in[31:0] = R2_num;
  //   R2_num_t[31:0] = R2_num_2; RW_in[4:0] = RW_num; RW_num_t[4:0] = RW_num_2; shamt_t[31:0] = shamt_2;
  //   shamtin[31:0] = shamt; SLRA_t = SLRA_2; SLRAin = SLRA; SW_t = SW_2; SWin = SW; SYSCALL = SYS_B_2;
  //   SYSCALLin = SYS_B; WE_t = WE_2; WEin = WE
endmodule

module EX_MEM (
  input  [31:0] PC1,
  input  [31:0] ALU_R1,
  input  [31:0] MDIN1,
  input  SYSCALL1,
  input  [4:0] RW1,
  input  LBU1,
  input  [31:0] IMMEDIATE1,
  input  LW1,
  input  SW1,
  input  JAL1,
  input  WE1,
  input  LUI1,
  input  eret_mem_in,
  input  CLK,
  input  [4:0] RSin,
  output [31:0] PC,
  output [31:0] ALU_R,
  output [31:0] MDIN,
  output SYSCALL,
  output [4:0] RW,
  output LBU,
  output eret_mem_out,
  output LW,
  output SW,
  output JAL,
  output [31:0] IMMEDIATE,
  output WE,
  output LUI,
  output [4:0] RSout
);

  Register #(.width(32)) register_1 (.D(PC1), .Q(PC), .clk(CLK));  // open: en, clr
  Register #(.width(32)) u_ALU_R (.D(ALU_R1), .Q(ALU_R), .clk(CLK));  // open: en, clr
  Register #(.width(32)) u_MDIN (.D(MDIN1), .Q(MDIN), .clk(CLK));  // open: en, clr
  Register #(.width(32)) u_IMMEDIATE (.D(IMMEDIATE1), .Q(IMMEDIATE), .clk(CLK));  // open: en, clr
  Register #(.width(1)) register_2 (.D(SYSCALL1), .Q(SYSCALL), .clk(CLK));  // open: en, clr
  Register #(.width(5)) u_RW (.D(RW1), .Q(RW), .clk(CLK));  // open: en, clr
  Register #(.width(1)) u_LBU (.D(LBU1), .Q(LBU), .clk(CLK));  // open: en, clr
  Register #(.width(1)) u_LUI (.D(LUI1), .Q(LUI), .clk(CLK));  // open: en, clr
  Register #(.width(1)) u_LW (.D(LW1), .Q(LW), .clk(CLK));  // open: en, clr
  Register #(.width(1)) u_SW (.D(SW1), .Q(SW), .clk(CLK));  // open: en, clr
  Register #(.width(1)) u_JAL (.D(JAL1), .Q(JAL), .clk(CLK));  // open: en, clr
  Register #(.width(1)) u_WE (.D(WE1), .Q(WE), .clk(CLK));  // open: en, clr
  Register #(.width(5)) u_RSin (.D(RSin), .Q(RSout), .clk(CLK));  // open: en, clr
  Register #(.width(1)) register_3 (.D(eret_mem_in), .Q(eret_mem_out), .clk(CLK));  // open: en, clr
endmodule

// MEM/Wb
module MEM_WB (
  input  [31:0] PC_41,
  input  [31:0] DATA1,
  input  SYSCALL1,
  input  [4:0] RW,
  input  JAL1,
  input  WE1,
  input  CLK,
  input  eret_wb_in,
  output [31:0] PC_4,
  output [31:0] DATA,
  output SYSCALL,
  output [4:0] RW_2,
  output JAL,
  output WE,
  output eret_wb_out
);

  Register #(.width(32)) register_1 (.D(PC_41), .Q(PC_4), .clk(CLK));  // open: en, clr
  Register #(.width(1)) register_2 (.D(SYSCALL1), .Q(SYSCALL), .clk(CLK));  // open: en, clr
  Register #(.width(1)) register_3 (.D(JAL1), .Q(JAL), .clk(CLK));  // open: en, clr
  Register #(.width(32)) register_4 (.D(DATA1), .Q(DATA), .clk(CLK));  // open: en, clr
  Register #(.width(5)) register_5 (.D(RW), .Q(RW_2), .clk(CLK));  // open: en, clr
  Register #(.width(1)) register_6 (.D(WE1), .Q(WE), .clk(CLK));  // open: en, clr
  Register #(.width(1)) register_7 (.D(eret_wb_in), .Q(eret_wb_out), .clk(CLK));  // open: en, clr

  // Other names for the same wires on the sheet: RW_t[4:0] = RW_2
endmodule

// BYPATH UNITY
module BYPATH (
  input  [4:0] RS_read1,
  input  [4:0] RS_read2,
  input  [4:0] WR1_MEM,
  input  [4:0] WR2_WB,
  input  WE1_MEM,
  input  WE2_WB,
  input  [4:0] RT_read3,
  input  [4:0] RT_read,
  input  [4:0] RT_read2,
  input  SLARin,
  output ForwardA1,
  output ForwardB1,
  output [1:0] ForwardA2,
  output [1:0] ForwardB2,
  output ForwardA3,
  output ForwardB3
);

  wire and_1_out, and_2_out, and_3_out, and_4_out, and_5_out, and_6_out, and_7_out, and_8_out,
       comparator_1_eq, comparator_2_eq, comparator_3_eq, comparator_4_eq, comparator_5_eq, comparator_6_eq,
       comparator_7_eq, comparator_8_eq, or_1_out, or_2_out, or_3_out, or_4_out, or_5_out;
  wire [1:0] multiplexer_5_out, multiplexer_6_out;
  wire [4:0] multiplexer_3_out, multiplexer_4_out;

  Comparator #(.width(5)) comparator_1 (.a(WR2_WB), .b(RS_read1), .eq(comparator_1_eq));  // open: gt, lt
  Comparator #(.width(5)) comparator_2 (.a(WR2_WB), .b(RT_read), .eq(comparator_2_eq));  // open: gt, lt
  or or_1 (or_1_out, WR2_WB[4], WR2_WB[3], WR2_WB[2], WR2_WB[1], WR2_WB[0]);
  Multiplexer #(.enable("false")) multiplexer_1 (.in0(1'b0), .in1(1'b1), .out(ForwardA1), .sel(and_1_out));
  and and_1 (and_1_out, WE2_WB, or_1_out, comparator_1_eq);
  Multiplexer #(.enable("false")) multiplexer_2 (.in0(1'b0), .in1(1'b1), .out(ForwardB1), .sel(and_2_out));
  and and_2 (and_2_out, WE2_WB, or_1_out, comparator_2_eq);
  Multiplexer #(.width(5), .enable("false")) multiplexer_3 (
    .in0(RS_read2), .in1(RT_read2), .out(multiplexer_3_out), .sel(SLARin));
  Multiplexer #(.width(5), .enable("false")) multiplexer_4 (
    .in0(RT_read2), .in1(RS_read2), .out(multiplexer_4_out), .sel(SLARin));
  Comparator #(.width(5)) comparator_3 (.a(WR1_MEM), .b(multiplexer_3_out), .eq(comparator_3_eq));  // open: gt, lt
  Comparator #(.width(5)) comparator_4 (.a(WR1_MEM), .b(multiplexer_4_out), .eq(comparator_4_eq));  // open: gt, lt
  Comparator #(.width(5)) comparator_5 (.a(multiplexer_4_out), .b(WR2_WB), .eq(comparator_5_eq));  // open: gt, lt
  Comparator #(.width(5)) comparator_6 (.a(multiplexer_3_out), .b(WR2_WB), .eq(comparator_6_eq));  // open: gt, lt
  or or_2 (or_2_out, WR1_MEM[4], WR1_MEM[3], WR1_MEM[2], WR1_MEM[1], WR1_MEM[0]);
  or or_3 (or_3_out, WR2_WB[4], WR2_WB[3], WR2_WB[2], WR2_WB[1], WR2_WB[0]);
  and and_3 (and_3_out, WE1_MEM, or_2_out, comparator_3_eq);
  and and_4 (and_4_out, WE1_MEM, or_2_out, comparator_4_eq);
  and and_5 (and_5_out, comparator_5_eq, or_3_out, WE2_WB);
  and and_6 (and_6_out, comparator_6_eq, or_3_out, WE2_WB);
  Multiplexer #(.width(2), .enable("false")) multiplexer_5 (
    .in0(2'b00), .in1(2'b01), .out(multiplexer_5_out), .sel(and_6_out));
  Multiplexer #(.width(2), .enable("false")) multiplexer_6 (
    .in0(2'b00), .in1(2'b01), .out(multiplexer_6_out), .sel(and_5_out));
  Multiplexer #(.width(2), .enable("false")) multiplexer_7 (
    .in0(multiplexer_6_out), .in1(2'b10), .out(ForwardB2), .sel(and_4_out));
  Multiplexer #(.width(2), .enable("false")) multiplexer_8 (
    .in0(multiplexer_5_out), .in1(2'b10), .out(ForwardA2), .sel(and_3_out));
  or or_4 (or_4_out, WR2_WB[4], WR2_WB[3], WR2_WB[2], WR2_WB[1], WR2_WB[0]);
  Comparator #(.width(5)) comparator_7 (.a(WR2_WB), .b(RT_read3), .eq(comparator_7_eq));  // open: gt, lt
  or or_5 (or_5_out, WR2_WB[4], WR2_WB[3], WR2_WB[2], WR2_WB[1], WR2_WB[0]);
  Comparator #(.width(5)) comparator_8 (.a(WR2_WB), .b(RT_read2), .eq(comparator_8_eq));  // open: gt, lt
  and and_7 (and_7_out, WE2_WB, or_4_out, comparator_7_eq);
  Multiplexer #(.enable("false")) multiplexer_9 (.in0(1'b0), .in1(1'b1), .out(ForwardA3), .sel(and_7_out));
  Multiplexer #(.enable("false")) multiplexer_10 (.in0(1'b0), .in1(1'b1), .out(ForwardB3), .sel(and_8_out));
  and and_8 (and_8_out, WE2_WB, or_5_out, comparator_8_eq);

  // Other names for the same wires on the sheet: RT_read1[4:0] = RT_read
endmodule

module HAZARD_UNITY (
  input  LWin,
  input  [4:0] IDEX_RT1,
  input  CLK,
  input  [4:0] IFID_RS1,
  input  [4:0] IFID_RT1,
  output STOP,
  output CLEAR
);

  wire and_1_out, comparator_1_eq, comparator_2_eq, d_ff_1_q, or_1_out;

  Comparator #(.width(5)) comparator_1 (.a(IDEX_RT1), .b(IFID_RS1), .eq(comparator_1_eq));  // open: gt, lt
  Comparator #(.width(5)) comparator_2 (.a(IDEX_RT1), .b(IFID_RT1), .eq(comparator_2_eq));  // open: gt, lt
  or or_1 (or_1_out, comparator_1_eq, comparator_2_eq);
  and and_1 (and_1_out, LWin, or_1_out);
  not not_1 (STOP, and_1_out);
  D_Flip_Flop #(.trigger("falling")) d_ff_1 (.clk(CLK), .D(and_1_out), .Q(d_ff_1_q));  // open: Qn, preset, en, reset
  and and_2 (CLEAR, CLK, d_ff_1_q);

  // Other names for the same wires on the sheet: IDEX_RT_1[4:0] = IDEX_RT1
endmodule
